// Logisim project processador4b_implementação_base_v1.0.circ as structural Verilog: 4 circuits, main circuit Processador
module Processador (
);

  wire C, CLK, EF, ER, OP, RST, SC, SI, SJ, unidade_funcional_1_cout;
  wire [1:0] bit_extender_1_out, SA, SB, SD;
  wire [3:0] banco_de_registos_1_a, banco_de_registos_1_b, banco_de_registos_1_r0, banco_de_registos_1_r1,
       banco_de_registos_1_r2, banco_de_registos_1_r3, bit_extender_2_out,
       \descodificador_de_instruções_1_imm4 , multiplexer_1_out, multiplexer_3_out, unidade_funcional_1_r;
  wire [5:0] adder_1_out, \descodificador_de_instruções_1_offset6 , multiplexer_2_out, PC_q;
  wire [9:0] rom_1_data;

  Button Reset (.out(RST));
  Clock MCLK (.out(CLK));
  Multiplexer #(.width(4), .enable("false")) multiplexer_1 (
    .in0(unidade_funcional_1_r), .in1(\descodificador_de_instruções_1_imm4 ), .out(multiplexer_1_out),
    .sel(SI));
  Multiplexer #(.width(6), .disabled(0), .enable("false")) multiplexer_2 (
    .in0(6'b000001), .in1(\descodificador_de_instruções_1_offset6 ), .out(multiplexer_2_out), .sel(SJ));
  // Probe on multiplexer_1_out
  // Probe on adder_1_out
  Adder #(.width(6)) adder_1 (.a(PC_q), .b(multiplexer_2_out), .out(adder_1_out), .cin(1'b1));  // open: cout
  Banco_de_Registos banco_de_registos_1 (
    .SD(SD), .ED(ER), .SB(SB), .CLK(CLK), .R0(banco_de_registos_1_r0), .R1(banco_de_registos_1_r1),
    .R2(banco_de_registos_1_r2), .R3(banco_de_registos_1_r3), .D(multiplexer_1_out),
    .A(banco_de_registos_1_a), .B(banco_de_registos_1_b), .SA(SA));
  // Probe on PC_q
  Register #(.width(6)) PC (.D(adder_1_out), .en(1'b1), .Q(PC_q), .clk(CLK), .clr(RST));
  // Probe on banco_de_registos_1_r0
  // Probe on banco_de_registos_1_r1
  // Probe on banco_de_registos_1_r2
  // Probe on banco_de_registos_1_r3
  Bit_Extender #(.in_width(4), .out_width(2)) bit_extender_1 (
    .in(\descodificador_de_instruções_1_imm4 ), .out(bit_extender_1_out));
  assign bit_extender_2_out = {{2{1'b0}}, bit_extender_1_out};  // Bit_Extender bit_extender_2
  // Probe on banco_de_registos_1_a
  // Probe on banco_de_registos_1_b
  // Probe on bit_extender_2_out
  // Probe on rom_1_data
  ROM #(.addrWidth(6), .dataWidth(10)) rom_1 (.addr(PC_q), .data(rom_1_data), .sel(1'b1));
  Multiplexer #(.width(4), .enable("false")) multiplexer_3 (
    .in0(banco_de_registos_1_b), .in1(bit_extender_2_out), .out(multiplexer_3_out), .sel(SC));
  \Descodificador_de_Instruções  \descodificador_de_instruções_1  (
    .Instruction(rom_1_data), .C(C), .SA(SA), .SB(SB), .SD(SD), .Imm4(\descodificador_de_instruções_1_imm4 ),
    .OP(OP), .ER(ER), .EF(EF), .SI(SI), .Offset6(\descodificador_de_instruções_1_offset6 ), .SJ(SJ), .SC(SC));
  // Probe on multiplexer_3_out
  Unidade_Funcional unidade_funcional_1 (
    .A(banco_de_registos_1_a), .B(multiplexer_3_out), .OP(OP), .R(unidade_funcional_1_r),
    .Cout(unidade_funcional_1_cout));
  // Probe on unidade_funcional_1_r
  Register #(.width(1)) PSW (.D(unidade_funcional_1_cout), .en(EF), .Q(C), .clk(CLK), .clr(1'b0));

  // Notes on the sheet:
  //   Imm4
  //   Memória de Programa
  //   contents of rom_1 (hex, n*v repeats v):
  //   96 7e 1 9 e3 25 40 8a 1e4 4
endmodule

module Banco_de_Registos (
  input  [3:0] D,
  input  ED,
  input  [1:0] SD,
  input  CLK,
  input  [1:0] SA,
  input  [1:0] SB,
  output [3:0] R0,
  output [3:0] R1,
  output [3:0] R2,
  output [3:0] R3,
  output [3:0] A,
  output [3:0] B
);

  wire decoder_1_out0, decoder_1_out1, decoder_1_out2, decoder_1_out3;

  Decoder #(.select(2), .disabled(0)) decoder_1 (
    .out0(decoder_1_out0), .out1(decoder_1_out1), .out2(decoder_1_out2), .out3(decoder_1_out3), .sel(SD),
    .en(ED));
  Register #(.width(4)) u_R0 (.D(D), .en(decoder_1_out0), .Q(R0), .clk(CLK), .clr(1'b0));
  Register #(.width(4)) u_R1 (.D(D), .en(decoder_1_out1), .Q(R1), .clk(CLK), .clr(1'b0));
  Register #(.width(4)) u_R2 (.D(D), .en(decoder_1_out2), .Q(R2), .clk(CLK), .clr(1'b0));
  Register #(.width(4)) u_R3 (.D(D), .en(decoder_1_out3), .Q(R3), .clk(CLK), .clr(1'b0));
  Multiplexer #(.select(2), .width(4)) multiplexer_1 (
    .in0(R0), .in1(R1), .in2(R2), .in3(R3), .out(A), .sel(SA), .en(1'b1));
  Multiplexer #(.select(2), .width(4)) multiplexer_2 (
    .in0(R0), .in1(R1), .in2(R2), .in3(R3), .out(B), .sel(SB), .en(1'b1));
endmodule

module Unidade_Funcional (
  input  [3:0] A,
  input  [3:0] B,
  input  OP,
  output [3:0] R,
  output Cout
);

  wire adder_1_cout;
  wire [3:0] bit_extender_1_out, xor_1_out;

  assign bit_extender_1_out = {{3{OP}}, OP};  // Bit_Extender bit_extender_1
  assign xor_1_out = B ^ bit_extender_1_out;  // XOR_Gate xor_1, 4 bits wide
  Adder #(.width(4)) adder_1 (.a(A), .b(xor_1_out), .out(R), .cin(OP), .cout(adder_1_cout));
  xor xor_2 (Cout, adder_1_cout, OP);
endmodule

module \Descodificador_de_Instruções  (
  input  [9:0] Instruction,
  input  C,
  output [1:0] SA,
  output [1:0] SB,
  output [1:0] SD,
  output [3:0] Imm4,
  output [5:0] Offset6,
  output OP,
  output SC,
  output ER,
  output SJ,
  output EF,
  output SI
);

  wire not_1_out;
  wire [3:2] rom_1_data;

  ROM #(.addrWidth(4), .dataWidth(7)) rom_1 (
    .addr(Instruction[3:0]), .data({OP, SC, ER, rom_1_data, EF, SI}), .sel(1'b1));
  not not_1 (not_1_out, C);
  Multiplexer #(.select(2), .disabled(0), .enable("false")) multiplexer_1 (
    .in0(1'b0), .in1(1'b1), .in2(not_1_out), .in3(C), .out(SJ), .sel(rom_1_data));

  assign Imm4 = Instruction[9:6];
  assign Offset6 = Instruction[9:4];
  assign SA = Instruction[9:8];
  assign SB = Instruction[7:6];
  assign SD = Instruction[5:4];

  // Notes on the sheet:
  //   contents of rom_1 (hex, n*v repeats v):
  //   10 50 30 42 30 0 11 10 8 c 4
endmodule
