// Logisim project G2 Paulo Rosa, Ricardo Pinto 21D.circ as structural Verilog: 4 circuits, main circuit CPU
module CPU (
  output [7:0] out_1
);

  wire EP, ER, MCLK_out, not_1_out, not_2_out, or_1_out, PSW_q, RD, Reset_out, SA, SC, SI, SO, WR, Z_out;
  wire [1:0] OP_ALU, SD;
  wire [2:0] AA, AB, AD;
  wire [7:0] adder_1_out, alu_1_r, Const3, controlled_buffer_1_out, multiplexer_1_out, multiplexer_2_out,
       multiplexer_3_out, multiplexer_4_out, multiplexer_5_out, Offset6, PC_q, register_file_1_a,
       register_file_1_r0, register_file_1_r1, register_file_1_r2, register_file_1_r3, register_file_1_r4,
       register_file_1_r5, register_file_1_r5_2, register_file_1_r6;
  wire [8:0] rom_1_data;

  Button Reset (.out(Reset_out));
  Clock MCLK (.out(MCLK_out));
  Multiplexer #(.width(8), .enable("false")) multiplexer_1 (
    .in0(8'h1), .in1(Offset6), .out(multiplexer_1_out), .sel(SO));
  // Probe on Offset6
  Adder adder_1 (.a(multiplexer_1_out), .b(PC_q), .out(adder_1_out), .cin(1'b0));  // open: cout
  Multiplexer #(.width(8), .disabled(0), .enable("false")) multiplexer_2 (
    .in0(adder_1_out), .in1(register_file_1_a), .out(multiplexer_2_out), .sel(SI));
  // Probe on multiplexer_2_out
  Register PC (.D(multiplexer_2_out), .en(1'b1), .Q(PC_q), .clk(MCLK_out), .clr(Reset_out));
  ROM #(.dataWidth(9)) rom_1 (.addr(PC_q), .data(rom_1_data));  // open: sel
  // Probe on register_file_1_a
  not not_1 (not_1_out, MCLK_out);
  // Probe on rom_1_data
  // Probe on SD
  Instruction_Decoder instruction_decoder_1 (
    .instructionCode(rom_1_data), .Const3(Const3), .Offset6(Offset6), .OP_ALU(OP_ALU), .Z(PSW_q), .RD(RD),
    .WR(WR), .EP(EP), .ER(ER), .SA(SA), .SC(SC), .SD(SD), .SO(SO), .SI(SI), .AA(AA), .AB(AB), .AD(AD));
  Multiplexer #(.select(2), .width(8), .disabled(0), .enable("false")) multiplexer_3 (
    .in0(Const3), .in1(controlled_buffer_1_out), .in2(alu_1_r), .out(multiplexer_3_out), .sel(SD));  // open: in3
  // Probe on multiplexer_3_out
  Register_File register_file_1 (
    .AD(AD), .ER(ER), .AA(AA), .AB(AB), .clk(not_1_out), .D(multiplexer_3_out), .A(register_file_1_a),
    .B(out_1), .R0(register_file_1_r0), .R1(register_file_1_r1), .R2(register_file_1_r2),
    .R3(register_file_1_r3), .R4(register_file_1_r4), .R5(register_file_1_r5), .R5_2(register_file_1_r5_2),
    .R6(register_file_1_r6));
  Multiplexer #(.width(8), .enable("false")) multiplexer_4 (
    .in0(Const3), .in1(out_1), .out(multiplexer_4_out), .sel(SC));
  ALU alu_1 (.Ci(1'b0), .A(register_file_1_a), .B(multiplexer_4_out), .R(alu_1_r), .OP_ALU(OP_ALU));  // open: Co
  // Probe on alu_1_r
  // Probe on register_file_1_r0
  // Probe on register_file_1_r1
  // Probe on register_file_1_r2
  // Probe on register_file_1_r3
  // Probe on register_file_1_r4
  // Probe on register_file_1_r5
  // Probe on register_file_1_r5_2
  // Probe on register_file_1_r6
  Multiplexer #(.width(8), .enable("false")) multiplexer_5 (
    .in0(alu_1_r), .in1(out_1), .out(multiplexer_5_out), .sel(SA));
  // Probe on multiplexer_5_out
  Register #(.width(1)) PSW (.D(Z_out), .en(EP), .Q(PSW_q), .clk(not_1_out), .clr(1'b0));
  nor Z (Z_out, alu_1_r[0], alu_1_r[1], alu_1_r[2], alu_1_r[3], alu_1_r[4], alu_1_r[5], alu_1_r[6], alu_1_r[7]);
  // Probe on controlled_buffer_1_out
  assign controlled_buffer_1_out = WR ? register_file_1_a : 8'bz;  // Controlled_Buffer controlled_buffer_1
  // Probe on PSW_q
  or or_1 (or_1_out, WR, RD);
  RAM ram_1 (
    .addr(multiplexer_5_out), .data(controlled_buffer_1_out), .sel(or_1_out), .clk(not_1_out),
    .ld(not_2_out), .clr(1'b0));
  not not_2 (not_2_out, WR);

  // Notes on the sheet:
  //   Code Memory
  //   contents of rom_1 (hex, n*v repeats v):
  //   c0 cd 49 91 2 189 13c e5 144 e6 a4 1e0
  //   Data Memory
endmodule

module Register_File (
  input  [7:0] D,
  input  ER,
  input  [2:0] AD,
  input  [2:0] AA,
  input  [2:0] AB,
  input  clk,
  output [7:0] R0,
  output [7:0] R1,
  output [7:0] R2,
  output [7:0] R3,
  output [7:0] R4,
  output [7:0] R5,
  output [7:0] R5_2,
  output [7:0] R6,
  output [7:0] A,
  output [7:0] B
);

  wire decoder_1_out0, decoder_1_out1, decoder_1_out2, decoder_1_out3, decoder_1_out4, decoder_1_out5,
       decoder_1_out6, decoder_1_out7;

  Decoder #(.select(3), .disabled(0)) decoder_1 (
    .out0(decoder_1_out0), .out1(decoder_1_out1), .out2(decoder_1_out2), .out3(decoder_1_out3),
    .out4(decoder_1_out4), .out5(decoder_1_out5), .out6(decoder_1_out6), .out7(decoder_1_out7), .sel(AD),
    .en(ER));
  Register u_R0 (.D(D), .en(decoder_1_out0), .Q(R0), .clk(clk), .clr(1'b0));
  Multiplexer #(.select(3), .width(8), .disabled(0), .enable("false")) multiplexer_1 (
    .in0(R0), .in1(R1), .in2(R2), .in3(R3), .in4(R4), .in5(R5), .in6(R5_2), .in7(R6), .out(A), .sel(AA));
  Register u_R1 (.D(D), .en(decoder_1_out1), .Q(R1), .clk(clk), .clr(1'b0));
  Register u_R2 (.D(D), .en(decoder_1_out2), .Q(R2), .clk(clk), .clr(1'b0));
  Register u_R3 (.D(D), .en(decoder_1_out3), .Q(R3), .clk(clk), .clr(1'b0));
  Multiplexer #(.select(3), .width(8), .disabled(0), .enable("false")) multiplexer_2 (
    .in0(R0), .in1(R1), .in2(R2), .in3(R3), .in4(R4), .in5(R5), .in6(R5_2), .in7(R6), .out(B), .sel(AB));
  Register u_R4 (.D(D), .en(decoder_1_out4), .Q(R4), .clk(clk), .clr(1'b0));
  Register u_R5 (.D(D), .en(decoder_1_out5), .Q(R5), .clk(clk), .clr(1'b0));
  Register u_R6 (.D(D), .en(decoder_1_out6), .Q(R5_2), .clk(clk), .clr(1'b0));
  Register R7 (.D(D), .en(decoder_1_out7), .Q(R6), .clk(clk), .clr(1'b0));
endmodule

module Instruction_Decoder (
  input  [8:0] instructionCode,
  input  Z,
  output [2:0] AB,
  output [2:0] AA,
  output [2:0] AD,
  output [7:0] Const3,
  output [7:0] Offset6,
  output [1:0] OP_ALU,
  output SI,
  output SO,
  output [1:0] SD,
  output SC,
  output SA,
  output ER,
  output EP,
  output WR,
  output RD
);

  ROM #(.addrWidth(4), .dataWidth(10)) rom_1 (
    .addr({instructionCode[8:6], Z}), .data({SI, SO, SD, SC, SA, ER, EP, WR, RD}), .sel(1'b1));
  assign Const3 = {{5{1'b0}}, instructionCode[2:0]};  // Bit_Extender bit_extender_1
  assign Offset6 = {{2{instructionCode[5]}}, instructionCode[5:0]};  // Bit_Extender bit_extender_2

  assign AA = instructionCode[5:3];
  assign AB = instructionCode[2:0];
  assign AD = instructionCode[5:3];
  assign OP_ALU = instructionCode[7:6];

  // Notes on the sheet:
  //   Opcode
  //   contents of rom_1 (hex, n*v repeats v):
  //   bd bd 9d 9d 79 79 39 39 131 31 32 32 bd bd 211 211
endmodule

module ALU (
  input  Ci,
  input  [7:0] A,
  input  [7:0] B,
  input  [1:0] OP_ALU,
  output Co,
  output [7:0] R
);

  wire adder_1_cout, or_1_out;
  wire [7:0] adder_1_out, and_1_out, bit_extender_1_out, xor_1_out;

  assign bit_extender_1_out = {{7{OP_ALU[0]}}, OP_ALU[0]};  // Bit_Extender bit_extender_1
  assign xor_1_out = B ^ bit_extender_1_out;  // XOR_Gate xor_1, 8 bits wide
  assign and_1_out = A & B;  // AND_Gate and_1, 8 bits wide
  or or_1 (or_1_out, Ci, OP_ALU[0]);
  Adder adder_1 (.a(A), .b(xor_1_out), .out(adder_1_out), .cin(or_1_out), .cout(adder_1_cout));
  xor xor_2 (Co, adder_1_cout, OP_ALU[0]);
  Multiplexer #(.width(8), .enable("false")) multiplexer_1 (
    .in0(adder_1_out), .in1(and_1_out), .out(R), .sel(OP_ALU[1]));
endmodule
