// Logisim project LIC.circ as structural Verilog: 28 circuits, main circuit decoder
module encoder (
  input  [7:0] in_1,
  output S0,
  output S1,
  output S2
);

  or or_1 (S0, in_1[1], in_1[3], in_1[5], in_1[7]);
  or or_2 (S1, in_1[1], in_1[2], in_1[6], in_1[7]);
  or or_3 (S2, in_1[3], in_1[4], in_1[6], in_1[7]);
endmodule

// DEC
module decoder (
  input  S0,
  input  S1,
  output D1,
  output D2,
  output D0
);

  wire not_1_out, not_2_out;

  not not_1 (not_1_out, S1);
  not not_2 (not_2_out, S0);
  // AND_Gate and_1 has open pins: in0=S0, in1=S1, out=open
  and and_2 (D1, S0, not_1_out);
  and and_3 (D2, not_2_out, S1);
  and and_4 (D0, not_2_out, not_1_out);
endmodule

module MUX4X1 (
  input  in_1,
  input  in_2,
  input  in_3,
  input  in_4,
  input  S1,
  input  S0,
  output out_7,
  output out_8,
  output out_9
);

  wire and_1_out, and_2_out, and_3_out, and_4_out;

  and and_1 (and_1_out, in_1, ~S1, ~S0);  // AND_Gate
  and and_2 (and_2_out, in_2, ~S1, S0);  // AND_Gate
  and and_3 (and_3_out, in_3, S1, ~S0);  // AND_Gate
  and and_4 (and_4_out, in_4, S1, S0);
  or or_1 (out_9, and_1_out, and_2_out, and_3_out, and_4_out);

  assign out_7 = S1;
  assign out_8 = S0;

  // Notes on the sheet:
  //   1
endmodule

module MUX2X1 (
  input  A0,
  input  A1,
  input  S0,
  output s0_2,
  output R0
);

  wire and_1_out, and_2_out;

  and and_1 (and_1_out, A0, ~S0);  // AND_Gate
  and and_2 (and_2_out, A1, S0);
  or or_1 (R0, and_1_out, and_2_out);

  assign s0_2 = S0;
endmodule

module Matrizpullyup__realista_i_guess (
  input  in_1,
  input  in_2,
  input  in_3,
  input  in_4,
  input  in_5,
  input  in_6,
  input  in_7,
  input  in_8,
  input  in_9,
  input  in_10,
  input  in_11,
  input  in_12,
  input  in_13,
  input  in_14,
  input  in_15,
  output out_16,
  output out_17,
  output out_18,
  output out_19
);

  wire and_1_out, and_2_out, and_3_out, and_4_out, and_5_out, and_6_out, and_7_out, and_8_out, and_9_out,
       and_10_out, and_11_out, and_12_out, and_13_out, and_14_out, and_15_out, and_16_out, and_17_out,
       and_18_out, and_19_out, and_20_out, and_21_out, and_22_out, and_23_out, and_24_out;

  and and_1 (and_1_out, in_1, 1'b1);
  and and_2 (and_2_out, in_1, 1'b1);
  and and_3 (and_3_out, in_1, 1'b1);
  and and_4 (and_4_out, in_1, 1'b1);
  and and_5 (and_5_out, and_1_out, ~in_4);  // AND_Gate
  and and_6 (and_6_out, and_2_out, in_7);
  and and_7 (and_7_out, and_3_out, in_10);
  and and_8 (and_8_out, and_4_out, in_13);
  and and_9 (and_9_out, in_2, 1'b1);
  and and_10 (and_10_out, in_2, 1'b1);
  and and_11 (and_11_out, in_2, 1'b1);
  and and_12 (and_12_out, in_2, 1'b1);
  and and_13 (and_13_out, and_9_out, ~in_5);  // AND_Gate
  and and_14 (and_14_out, and_10_out, in_8);
  and and_15 (and_15_out, and_11_out, in_11);
  and and_16 (and_16_out, and_12_out, in_14);
  and and_17 (and_17_out, in_3, 1'b1);
  and and_18 (and_18_out, in_3, 1'b1);
  and and_19 (and_19_out, in_3, 1'b1);
  and and_20 (and_20_out, in_3, 1'b1);
  and and_21 (and_21_out, and_17_out, ~in_6);  // AND_Gate
  or or_1 (out_16, and_21_out, and_13_out, and_5_out);
  and and_22 (and_22_out, and_18_out, in_9);
  or or_2 (out_17, and_22_out, and_14_out, and_6_out);
  and and_23 (and_23_out, and_19_out, in_12);
  or or_3 (out_18, and_23_out, and_15_out, and_7_out);
  and and_24 (and_24_out, and_20_out, in_15);
  or or_4 (out_19, and_24_out, and_16_out, and_8_out);
endmodule

module Matrizdedetecao_simplificada_so_para_aqui (
  input  in_1,
  input  in_2,
  input  in_3,
  input  in_4,
  input  in_5,
  input  in_6,
  input  in_7,
  input  in_8,
  input  in_9,
  input  in_10,
  input  in_11,
  input  in_12,
  input  in_13,
  input  in_14,
  input  in_15,
  output out_16,
  output out_17,
  output out_18,
  output out_19
);

  wire and_1_out, and_2_out, and_3_out, and_4_out, and_5_out, and_6_out, and_7_out, and_8_out, and_9_out,
       and_10_out, and_11_out, and_12_out;

  and and_1 (and_1_out, in_1, in_4);
  and and_2 (and_2_out, in_1, in_7);
  and and_3 (and_3_out, in_1, in_10);
  and and_4 (and_4_out, in_1, in_13);
  and and_5 (and_5_out, in_2, in_5);
  and and_6 (and_6_out, in_2, in_8);
  and and_7 (and_7_out, in_2, in_11);
  and and_8 (and_8_out, in_2, in_14);
  and and_9 (and_9_out, in_3, in_6);
  and and_10 (and_10_out, in_3, in_9);
  and and_11 (and_11_out, in_3, in_12);
  and and_12 (and_12_out, in_3, in_15);
  or or_1 (out_16, and_9_out, and_5_out, and_1_out);
  or or_2 (out_17, and_10_out, and_6_out, and_2_out);
  or or_3 (out_18, and_11_out, and_7_out, and_3_out);
  or or_4 (out_19, and_12_out, and_8_out, and_4_out);
endmodule

// Cont
module Contador (
  input  Enable,
  input  Clock,
  output Q0,
  output Q1,
  output Q2,
  output Q3
);

  wire comparator_1_eq;
  wire [3:0] adder_1_out, multiplexer_1_out;

  Adder #(.width(4)) adder_1 (.a({Q3, Q2, Q1, Q0}), .b({3'b000, Enable}), .out(adder_1_out));  // open: cin, cout
  Multiplexer #(.width(4), .enable("false")) multiplexer_1 (
    .in0(adder_1_out), .in1(4'b0000), .out(multiplexer_1_out), .sel(comparator_1_eq));
  Clock clock_1 ();  // open: out
  Register_part #(.width(4)) register_1 (.D(multiplexer_1_out), .Q({Q3, Q2, Q1, Q0}), .clk(Clock));  // open: en, clr
  Comparator #(.width(4), .mode("unsigned")) comparator_1 (
    .a({Q3, Q2, Q1, Q0}), .b(4'b1011), .eq(comparator_1_eq));  // open: gt, lt

  // Notes on the sheet:
  //   11, 0 a 11 carateres a percorrer
endmodule

// counter
module Contador2 (
  input  Clock,
  input  Clear,
  output [3:0] out_3
);

  wire [3:0] adder_1_out;

  Adder #(.width(4)) adder_1 (.a(out_3), .b(4'b0001), .out(adder_1_out));  // open: cin, cout
  Register_part #(.width(4)) register_1 (.D(adder_1_out), .Q(out_3), .clk(Clock), .clr(Clear));  // open: en
endmodule

module KeyScan_com_not (
  input  Kscan,
  input  Clock,
  input  [2:0] in_3,
  input  [2:0] in_4,
  input  [2:0] in_5,
  input  [2:0] in_6,
  output [3:0] K0__3,
  output Kpress
);

  wire decoder_1_d0, decoder_1_d1, decoder_1_d2, matrizpullyup_realista_i_guess_1_out_16,
       matrizpullyup_realista_i_guess_1_out_17, matrizpullyup_realista_i_guess_1_out_18,
       matrizpullyup_realista_i_guess_1_out_19, mux4x1_1_out_9, not_1_out, not_2_out, not_3_out;

  Clock clock_1 ();  // open: out
  decoder decoder_1 (.S0(K0__3[2]), .S1(K0__3[3]), .D1(decoder_1_d1), .D2(decoder_1_d2), .D0(decoder_1_d0));
  not not_1 (not_1_out, decoder_1_d0);
  not not_2 (not_2_out, decoder_1_d1);
  Contador contador_1 (.Enable(Kscan), .Q0(K0__3[0]), .Q1(K0__3[1]), .Q2(K0__3[2]), .Q3(K0__3[3]), .Clock(Clock));
  not not_3 (not_3_out, decoder_1_d2);
  Matrizpullyup__realista_i_guess matrizpullyup_realista_i_guess_1 (
    .out_16(matrizpullyup_realista_i_guess_1_out_16), .out_17(matrizpullyup_realista_i_guess_1_out_17),
    .out_18(matrizpullyup_realista_i_guess_1_out_18), .out_19(matrizpullyup_realista_i_guess_1_out_19),
    .in_1(not_1_out), .in_2(not_2_out), .in_3(not_3_out), .in_4(in_3[0]), .in_5(in_3[1]), .in_6(in_3[2]),
    .in_7(in_4[0]), .in_8(in_4[1]), .in_9(in_4[2]), .in_10(in_5[0]), .in_11(in_5[1]), .in_12(in_5[2]),
    .in_13(in_6[0]), .in_14(in_6[1]), .in_15(in_6[2]));
  MUX4X1 mux4x1_1 (
    .in_1(matrizpullyup_realista_i_guess_1_out_16), .in_2(matrizpullyup_realista_i_guess_1_out_17),
    .in_3(matrizpullyup_realista_i_guess_1_out_18), .in_4(matrizpullyup_realista_i_guess_1_out_19),
    .out_9(mux4x1_1_out_9), .S1(K0__3[1]), .S0(K0__3[0]));  // open: out_7, out_8
  not not_4 (Kpress, mux4x1_1_out_9);

  // Notes on the sheet:
  //   Enable
  //   Q3
  //   0           4           8
  //   1           5           9
  //   2           6           10
  //   3           7           11
  //   Q2
  //   Ordem pelo qual é feito o varrimento, valor no K0..3 
  //   Q0
  //   Q1
  //   S1
  //   S0
endmodule

// KeyScan
module KeyScan_simp (
  input  Kscan,
  input  Clock,
  input  [2:0] in_3,
  input  [2:0] in_4,
  input  [2:0] in_5,
  input  [2:0] in_6,
  output [3:0] K0__3,
  output Kpress
);

  wire decoder_1_d0, decoder_1_d1, decoder_1_d2, matrizdedetecao_simplificada_so_para_aqui_1_out_16,
       matrizdedetecao_simplificada_so_para_aqui_1_out_17,
       matrizdedetecao_simplificada_so_para_aqui_1_out_18, matrizdedetecao_simplificada_so_para_aqui_1_out_19;

  Clock clock_1 ();  // open: out
  decoder decoder_1 (.S0(K0__3[2]), .S1(K0__3[3]), .D1(decoder_1_d1), .D2(decoder_1_d2), .D0(decoder_1_d0));
  Contador contador_1 (.Enable(Kscan), .Q0(K0__3[0]), .Q1(K0__3[1]), .Q2(K0__3[2]), .Q3(K0__3[3]), .Clock(Clock));
  Matrizdedetecao_simplificada_so_para_aqui matrizdedetecao_simplificada_so_para_aqui_1 (
    .in_4(in_3[0]), .in_5(in_3[1]), .in_6(in_3[2]),
    .out_16(matrizdedetecao_simplificada_so_para_aqui_1_out_16), .in_1(decoder_1_d0), .in_2(decoder_1_d1),
    .in_3(decoder_1_d2), .out_17(matrizdedetecao_simplificada_so_para_aqui_1_out_17),
    .out_18(matrizdedetecao_simplificada_so_para_aqui_1_out_18),
    .out_19(matrizdedetecao_simplificada_so_para_aqui_1_out_19), .in_7(in_4[0]), .in_8(in_4[1]),
    .in_9(in_4[2]), .in_10(in_5[0]), .in_11(in_5[1]), .in_12(in_5[2]), .in_13(in_6[0]), .in_14(in_6[1]),
    .in_15(in_6[2]));
  MUX4X1 mux4x1_1 (
    .in_1(matrizdedetecao_simplificada_so_para_aqui_1_out_16),
    .in_2(matrizdedetecao_simplificada_so_para_aqui_1_out_17),
    .in_3(matrizdedetecao_simplificada_so_para_aqui_1_out_18),
    .in_4(matrizdedetecao_simplificada_so_para_aqui_1_out_19), .out_9(Kpress), .S1(K0__3[1]), .S0(K0__3[0]));  // open: out_7, out_8

  // Notes on the sheet:
  //   Enable
  //   Q3
  //   0           4           8
  //   1           5           9
  //   2           6           10
  //   3           7           11
  //   Q2
  //   Ordem pelo qual é feito o varrimento, valor no K0..3 
  //   Q0
  //   Q1
  //   S1
  //   S0
endmodule

module KeyControl (
  input  KeyPress,
  input  KAcknowledge,
  input  Clock,
  output Kscan,
  output Kvalue
);

  wire d_ff_1_q, d_ff_2_q, mux4x1_1_out_7, mux4x1_1_out_8, mux4x1_1_out_9, mux4x1_2_out_9, not_1_out,
       or_1_out;

  not not_1 (not_1_out, KAcknowledge);
  or or_1 (or_1_out, KeyPress, KAcknowledge);
  MUX4X1 mux4x1_1 (
    .in_1(KeyPress), .in_2(not_1_out), .in_3(1'b0), .out_9(mux4x1_1_out_9), .S1(d_ff_2_q), .S0(d_ff_1_q),
    .out_7(mux4x1_1_out_7), .out_8(mux4x1_1_out_8));  // open: in_4
  MUX4X1 mux4x1_2 (
    .in_1(1'b0), .in_2(KAcknowledge), .in_3(or_1_out), .out_9(mux4x1_2_out_9), .S1(mux4x1_1_out_7),
    .S0(mux4x1_1_out_8));  // open: in_4, out_7, out_8
  D_Flip_Flop d_ff_1 (.clk(Clock), .D(mux4x1_1_out_9), .Q(d_ff_1_q));  // open: Qn, preset, en, reset
  D_Flip_Flop d_ff_2 (.clk(Clock), .D(mux4x1_2_out_9), .Q(d_ff_2_q));  // open: Qn, preset, en, reset
  and and_1 (Kscan, ~d_ff_2_q, ~d_ff_1_q);  // AND_Gate
  and and_2 (Kvalue, d_ff_1_q, ~d_ff_2_q);  // AND_Gate

  // Notes on the sheet:
  //   S0
  //   S1
endmodule

// KeyDecode
module KeyDecode (
  input  Clock,
  input  KeyAck,
  input  [2:0] in_3,
  input  [2:0] in_4,
  input  [2:0] in_5,
  input  [2:0] in_6,
  output KeyVal,
  output [3:0] out_8
);

  wire clock_1_out, keycontrol_1_kscan, keyscan_simp_1_kpress;

  Clock clock_1 (.out(clock_1_out));
  KeyScan_simp keyscan_simp_1 (
    .Kscan(keycontrol_1_kscan), .in_6(in_6), .K0__3(out_8), .Kpress(keyscan_simp_1_kpress), .in_5(in_5),
    .in_4(in_4), .in_3(in_3), .Clock(clock_1_out));
  KeyControl keycontrol_1 (
    .KeyPress(keyscan_simp_1_kpress), .KAcknowledge(KeyAck), .Kscan(keycontrol_1_kscan), .Kvalue(KeyVal),
    .Clock(clock_1_out));

  // Notes on the sheet:
  //   K0..3
endmodule

module KeyBuffer (
  input  [3:0] in_1,
  input  Clock,
  input  DataAvaiable,
  input  KeyAck,
  output [3:0] out_5,
  output DataAccepted,
  output Dval
);

  wire keybuffercontrol_1_writetoregister;

  KeyBufferControl keybuffercontrol_1 (
    .DataAvailable(DataAvaiable), .KeyAck(KeyAck), .Dval(Dval), .DataAccepted(DataAccepted),
    .WritetoRegister(keybuffercontrol_1_writetoregister), .Clock(Clock));
  Register_part #(.width(4)) Output_Register (
    .D(in_1), .Q(out_5), .clk(keybuffercontrol_1_writetoregister));  // open: en, clr
endmodule

module KeyBufferControl (
  input  DataAvailable,
  input  KeyAck,
  input  Clock,
  output Dval,
  output DataAccepted,
  output WritetoRegister
);

  wire d_ff_1_q, d_ff_2_q, mux4x1_1_out_7, mux4x1_1_out_8, mux4x1_1_out_9, mux4x1_2_out_9;

  MUX4X1 mux4x1_1 (
    .in_1(DataAvailable), .in_2(1'b0), .in_3(KeyAck), .in_4(KeyAck), .out_9(mux4x1_1_out_9), .S1(d_ff_2_q),
    .S0(d_ff_1_q), .out_7(mux4x1_1_out_7), .out_8(mux4x1_1_out_8));
  MUX4X1 mux4x1_2 (
    .in_1(1'b0), .in_2(1'b1), .in_3(1'b1), .in_4(KeyAck), .out_9(mux4x1_2_out_9), .S1(mux4x1_1_out_7),
    .S0(mux4x1_1_out_8));  // open: out_7, out_8
  D_Flip_Flop d_ff_1 (.clk(Clock), .D(mux4x1_1_out_9), .Q(d_ff_1_q));  // open: Qn, preset, en, reset
  D_Flip_Flop d_ff_2 (.clk(Clock), .D(mux4x1_2_out_9), .Q(d_ff_2_q));  // open: Qn, preset, en, reset
  and and_1 (DataAccepted, d_ff_2_q, ~d_ff_1_q);  // AND_Gate
  and and_2 (WritetoRegister, d_ff_1_q, ~d_ff_2_q);  // AND_Gate

  assign Dval = DataAccepted;

  // Notes on the sheet:
  //   S0
  //   S1
endmodule

module KeyBoardReader (
  input  Clock,
  input  [2:0] in_2,
  input  [2:0] in_3,
  input  [2:0] in_4,
  input  [2:0] in_5,
  input  ACK,
  output [3:0] Q0_3,
  output Dval
);

  wire clock_1_out, keybuffer_1_dataaccepted, keydecode_1_keyval;
  wire [3:0] keydecode_1_out_8;

  Clock clock_1 (.out(clock_1_out));
  KeyDecode keydecode_1 (
    .Clock(clock_1_out), .KeyAck(keybuffer_1_dataaccepted), .in_3(in_2), .in_4(in_3), .in_5(in_4),
    .in_6(in_5), .KeyVal(keydecode_1_keyval), .out_8(keydecode_1_out_8));
  KeyBuffer keybuffer_1 (
    .in_1(keydecode_1_out_8), .Clock(clock_1_out), .DataAvaiable(keydecode_1_keyval), .KeyAck(ACK),
    .out_5(Q0_3), .DataAccepted(keybuffer_1_dataaccepted), .Dval(Dval));

  // Notes on the sheet:
  //   Kack
  //   DAV
  //   Kval
  //   D0:3
  //   K0:3
  //   ACK - >
  //   DACEP
  //   Control
endmodule

// Regi
module Register (
  input  SCLCK_clock,
  input  SDX_data,
  input  Sel_enable,
  input  Enable,
  output clock,
  output Qout,
  output data,
  output enable_2
);

  wire multiplexer_1_out;

  Multiplexer #(.enable("false")) multiplexer_1 (.in0(Qout), .in1(SDX_data), .out(multiplexer_1_out), .sel(Sel_enable));
  D_Flip_Flop d_ff_1 (.clk(SCLCK_clock), .D(multiplexer_1_out), .Q(Qout), .en(Enable));  // open: Qn, preset, reset

  assign clock = SCLCK_clock;
  assign data = SDX_data;
  assign enable_2 = Enable;
endmodule

// Data Storage
module DataStorage (
  input  SDX_data__em_pulsos,
  input  SCLCK_clock,
  input  Enable,
  input  [3:0] A0_3_adress,
  output [9:0] out_5
);

  wire decoder_1_out0, decoder_1_out1, decoder_1_out2, decoder_1_out3, decoder_1_out4, decoder_1_out5,
       decoder_1_out6, decoder_1_out7, decoder_1_out8, decoder_1_out9, register_1_clock, register_1_data,
       register_1_enable_2, register_2_clock, register_2_data, register_2_enable_2, register_3_clock,
       register_3_data, register_3_enable_2, register_4_clock, register_4_data, register_4_enable_2,
       register_5_clock, register_5_data, register_5_enable_2, register_6_clock, register_6_data,
       register_6_enable_2, register_7_clock, register_7_data, register_7_enable_2, register_8_clock,
       register_8_data, register_8_enable_2, register_9_clock, register_9_data, register_9_enable_2;

  Decoder #(.select(4), .enable("false")) decoder_1 (
    .out0(decoder_1_out0), .out1(decoder_1_out1), .out2(decoder_1_out2), .out3(decoder_1_out3),
    .out4(decoder_1_out4), .out5(decoder_1_out5), .out6(decoder_1_out6), .out7(decoder_1_out7),
    .out8(decoder_1_out8), .out9(decoder_1_out9), .sel(A0_3_adress));  // open: out10, out11, out12, out13, out14, out15
  Register register_1 (
    .SCLCK_clock(SCLCK_clock), .SDX_data(SDX_data__em_pulsos), .Sel_enable(decoder_1_out0),
    .clock(register_1_clock), .Qout(out_5[0]), .data(register_1_data), .Enable(Enable),
    .enable_2(register_1_enable_2));
  Register register_2 (
    .SCLCK_clock(register_1_clock), .SDX_data(register_1_data), .Sel_enable(decoder_1_out1),
    .clock(register_2_clock), .Qout(out_5[1]), .data(register_2_data), .Enable(register_1_enable_2),
    .enable_2(register_2_enable_2));
  Register register_3 (
    .SCLCK_clock(register_2_clock), .SDX_data(register_2_data), .Sel_enable(decoder_1_out2),
    .clock(register_3_clock), .Qout(out_5[2]), .data(register_3_data), .Enable(register_2_enable_2),
    .enable_2(register_3_enable_2));
  Register register_4 (
    .SCLCK_clock(register_3_clock), .SDX_data(register_3_data), .Sel_enable(decoder_1_out3),
    .clock(register_4_clock), .Qout(out_5[3]), .data(register_4_data), .Enable(register_3_enable_2),
    .enable_2(register_4_enable_2));
  Register register_5 (
    .SCLCK_clock(register_4_clock), .SDX_data(register_4_data), .Sel_enable(decoder_1_out4),
    .clock(register_5_clock), .Qout(out_5[4]), .data(register_5_data), .Enable(register_4_enable_2),
    .enable_2(register_5_enable_2));
  Register register_6 (
    .SCLCK_clock(register_5_clock), .SDX_data(register_5_data), .Sel_enable(decoder_1_out5),
    .clock(register_6_clock), .Qout(out_5[5]), .data(register_6_data), .Enable(register_5_enable_2),
    .enable_2(register_6_enable_2));
  Register register_7 (
    .SCLCK_clock(register_6_clock), .SDX_data(register_6_data), .Sel_enable(decoder_1_out6),
    .clock(register_7_clock), .Qout(out_5[6]), .data(register_7_data), .Enable(register_6_enable_2),
    .enable_2(register_7_enable_2));
  Register register_8 (
    .SCLCK_clock(register_7_clock), .SDX_data(register_7_data), .Sel_enable(decoder_1_out7),
    .clock(register_8_clock), .Qout(out_5[7]), .data(register_8_data), .Enable(register_7_enable_2),
    .enable_2(register_8_enable_2));
  Register register_9 (
    .SCLCK_clock(register_8_clock), .SDX_data(register_8_data), .Sel_enable(decoder_1_out8),
    .clock(register_9_clock), .Qout(out_5[8]), .data(register_9_data), .Enable(register_8_enable_2),
    .enable_2(register_9_enable_2));
  Register register_10 (
    .SCLCK_clock(register_9_clock), .SDX_data(register_9_data), .Sel_enable(decoder_1_out9), .Qout(out_5[9]),
    .Enable(register_9_enable_2));  // open: clock, data, enable_2
endmodule

// =5
module Equal5 (
  input  [3:0] in_1,
  output out_2
);

  Comparator #(.width(4), .mode("unsigned")) comparator_1 (.a(in_1), .b(4'b0101), .eq(out_2));  // open: gt, lt
endmodule

// =10
module Equal10 (
  input  [3:0] in_1,
  output out_2
);

  Comparator #(.width(4), .mode("unsigned")) comparator_1 (.a(in_1), .b(4'b1010), .eq(out_2));  // open: gt, lt
endmodule

// =6
module Equal6 (
  input  [3:0] in_1,
  output out_2
);

  Comparator #(.width(4), .mode("unsigned")) comparator_1 (.a(in_1), .b(4'b0110), .eq(out_2));  // open: gt, lt
endmodule

// =11
module Equal11 (
  input  [3:0] in_1,
  output out_2
);

  Comparator #(.width(4), .mode("unsigned")) comparator_1 (.a(in_1), .b(4'b1011), .eq(out_2));  // open: gt, lt
endmodule

module ParityChecker_maior (
  input  SDX_data__em_pulsos,
  input  SCLCK_clock,
  input  Init_Enable,
  output Error
);

  wire and_1_out, and_2_out, decoder_1_out0, decoder_1_out1, decoder_1_out2, decoder_1_out3, decoder_1_out4,
       decoder_1_out5, decoder_1_out6, decoder_1_out7, decoder_1_out8, decoder_1_out9, decoder_1_out10,
       or_1_out, register_1_clock, register_1_data, register_1_enable_2, register_1_qout, register_2_clock,
       register_2_data, register_2_enable_2, register_2_qout, register_3_clock, register_3_data,
       register_3_enable_2, register_3_qout, register_4_clock, register_4_data, register_4_enable_2,
       register_4_qout, register_5_clock, register_5_data, register_5_enable_2, register_5_qout,
       register_6_clock, register_6_data, register_6_enable_2, register_6_qout, register_7_clock,
       register_7_data, register_7_enable_2, register_7_qout, register_8_clock, register_8_data,
       register_8_enable_2, register_8_qout, register_9_clock, register_9_data, register_9_enable_2,
       register_9_qout, register_10_clock, register_10_data, register_10_enable_2, register_10_qout,
       register_11_qout, xor_1_out, xor_2_out;
  wire [3:0] contador2_1_out_3;

  Contador2 contador2_1 (.Clear(Init_Enable), .out_3(contador2_1_out_3), .Clock(SCLCK_clock));
  Decoder #(.select(4), .enable("false")) decoder_1 (
    .out0(decoder_1_out0), .out1(decoder_1_out1), .out2(decoder_1_out2), .out3(decoder_1_out3),
    .out4(decoder_1_out4), .out5(decoder_1_out5), .out6(decoder_1_out6), .out7(decoder_1_out7),
    .out8(decoder_1_out8), .out9(decoder_1_out9), .out10(decoder_1_out10), .sel(contador2_1_out_3));  // open: out11, out12, out13, out14, out15
  Register register_1 (
    .SCLCK_clock(SCLCK_clock), .SDX_data(SDX_data__em_pulsos), .Sel_enable(decoder_1_out0),
    .clock(register_1_clock), .Qout(register_1_qout), .data(register_1_data), .Enable(Init_Enable),
    .enable_2(register_1_enable_2));
  Register register_2 (
    .SCLCK_clock(register_1_clock), .SDX_data(register_1_data), .Sel_enable(decoder_1_out1),
    .clock(register_2_clock), .Qout(register_2_qout), .data(register_2_data), .Enable(register_1_enable_2),
    .enable_2(register_2_enable_2));
  Register register_3 (
    .SCLCK_clock(register_2_clock), .SDX_data(register_2_data), .Sel_enable(decoder_1_out2),
    .clock(register_3_clock), .Qout(register_3_qout), .data(register_3_data), .Enable(register_2_enable_2),
    .enable_2(register_3_enable_2));
  Register register_4 (
    .SCLCK_clock(register_3_clock), .SDX_data(register_3_data), .Sel_enable(decoder_1_out3),
    .clock(register_4_clock), .Qout(register_4_qout), .data(register_4_data), .Enable(register_3_enable_2),
    .enable_2(register_4_enable_2));
  Register register_5 (
    .SCLCK_clock(register_4_clock), .SDX_data(register_4_data), .Sel_enable(decoder_1_out4),
    .clock(register_5_clock), .Qout(register_5_qout), .data(register_5_data), .Enable(register_4_enable_2),
    .enable_2(register_5_enable_2));
  Register register_6 (
    .SCLCK_clock(register_5_clock), .SDX_data(register_5_data), .Sel_enable(decoder_1_out5),
    .clock(register_6_clock), .Qout(register_6_qout), .data(register_6_data), .Enable(register_5_enable_2),
    .enable_2(register_6_enable_2));
  Register register_7 (
    .SCLCK_clock(register_6_clock), .SDX_data(register_6_data), .Sel_enable(decoder_1_out6),
    .clock(register_7_clock), .Qout(register_7_qout), .data(register_7_data), .Enable(register_6_enable_2),
    .enable_2(register_7_enable_2));
  Register register_8 (
    .SCLCK_clock(register_7_clock), .SDX_data(register_7_data), .Sel_enable(decoder_1_out7),
    .clock(register_8_clock), .Qout(register_8_qout), .data(register_8_data), .Enable(register_7_enable_2),
    .enable_2(register_8_enable_2));
  Register register_9 (
    .SCLCK_clock(register_8_clock), .SDX_data(register_8_data), .Sel_enable(decoder_1_out8),
    .clock(register_9_clock), .Qout(register_9_qout), .data(register_9_data), .Enable(register_8_enable_2),
    .enable_2(register_9_enable_2));
  Register register_10 (
    .SCLCK_clock(register_9_clock), .SDX_data(register_9_data), .Sel_enable(decoder_1_out9),
    .clock(register_10_clock), .Qout(register_10_qout), .data(register_10_data),
    .Enable(register_9_enable_2), .enable_2(register_10_enable_2));
  Register register_11 (
    .SCLCK_clock(register_10_clock), .SDX_data(register_10_data), .Sel_enable(decoder_1_out10),
    .Qout(register_11_qout), .Enable(register_10_enable_2));  // open: clock, data, enable_2
  xor xor_1 (xor_1_out, register_1_qout, register_2_qout, register_3_qout, register_5_qout, register_6_qout, register_7_qout);
  xor xor_2 (xor_2_out, register_1_qout, register_2_qout, register_3_qout, register_4_qout, register_5_qout, register_6_qout, register_7_qout, register_8_qout, register_9_qout, register_10_qout, register_11_qout);
  and and_1 (and_1_out, ~register_1_qout, xor_1_out);  // AND_Gate
  and and_2 (and_2_out, register_1_qout, xor_2_out);
  or or_1 (or_1_out, and_1_out, and_2_out);
  and and_3 (Error, or_1_out, register_11_qout);

  // Notes on the sheet:
  //   bit 0
  //   Parity Bit
  //   se o bit 0 = 1, L -> LCD
  //   se o bit 0 = 0, D -> Dispenser
endmodule

// Parity Checker
module ParityCheckerSimples (
  input  SCLK,
  input  SDX_data,
  input  Clear,
  output \é_impar 
);

  wire t_ff_1_qn;

  T_Flip_Flop t_ff_1 (.clk(SCLK), .T(SDX_data), .Q(\é_impar ), .Qn(t_ff_1_qn), .reset(Clear));  // open: preset, en
endmodule

// Proto de com
module \Protocolo_de_comunicaçao  (
  input  SDX,
  input  SCLK,
  output Init,
  output Start
);

  wire and_1_out, d_ff_1_q, d_ff_2_q, mux4x1_1_out_7, mux4x1_1_out_8, mux4x1_1_out_9, mux4x1_2_out_9,
       not_1_out;

  and and_1 (and_1_out, ~SDX, ~SCLK);  // AND_Gate
  not not_1 (not_1_out, and_1_out);
  MUX4X1 mux4x1_1 (
    .in_1(SDX), .in_2(not_1_out), .in_3(1'b0), .in_4(1'b0), .out_9(mux4x1_1_out_9), .S1(d_ff_2_q),
    .S0(d_ff_1_q), .out_7(mux4x1_1_out_7), .out_8(mux4x1_1_out_8));
  MUX4X1 mux4x1_2 (
    .in_1(1'b0), .in_2(and_1_out), .in_3(1'b0), .in_4(1'b0), .out_9(mux4x1_2_out_9), .S1(mux4x1_1_out_7),
    .S0(mux4x1_1_out_8));  // open: out_7, out_8
  D_Flip_Flop d_ff_1 (.clk(SCLK), .D(mux4x1_1_out_9), .Q(d_ff_1_q));  // open: Qn, preset, en, reset
  D_Flip_Flop d_ff_2 (.clk(SCLK), .D(mux4x1_2_out_9), .Q(d_ff_2_q));  // open: Qn, preset, en, reset
  and and_2 (Init, d_ff_2_q, ~d_ff_1_q);  // AND_Gate

  assign Start = Init;

  // Other names for the same wires on the sheet: C = SCLK

  // Notes on the sheet:
  //   S0
  //   S1
endmodule

// Serial Control
module SerialControl (
  input  SDX,
  input  SCLK,
  input  Dflag,
  input  Pflag,
  input  RXerror,
  input  Accept,
  output init,
  output Init_2,
  output WR,
  output Busy,
  output Dxval
);

  wire and_1_out, and_2_out, and_3_out, and_4_out, d_ff_1_q, d_ff_2_q, d_ff_3_q, mux2x1_1_r0, mux4x1_1_out_7,
       mux4x1_1_out_8, mux4x1_1_out_9, mux4x1_2_out_9, not_1_out, or_1_out, or_2_out, or_3_out, or_4_out,
       or_5_out, or_6_out, \protocolo_de_comunicaçao_1_start , xor_1_out, xor_2_out;

  \Protocolo_de_comunicaçao  \protocolo_de_comunicaçao_1  (
    .SDX(SDX), .SCLK(SCLK), .Init(init), .Start(\protocolo_de_comunicaçao_1_start ));
  and and_1 (and_1_out, ~\protocolo_de_comunicaçao_1_start , ~Pflag);  // AND_Gate
  and and_2 (and_2_out, ~\protocolo_de_comunicaçao_1_start , Pflag, ~RXerror);  // AND_Gate
  or or_1 (or_1_out, and_1_out, \protocolo_de_comunicaçao_1_start , ~and_2_out);  // OR_Gate
  or or_2 (or_2_out, and_1_out, ~\protocolo_de_comunicaçao_1_start , and_2_out);  // OR_Gate
  or or_3 (or_3_out, \protocolo_de_comunicaçao_1_start , Accept);
  and and_3 (and_3_out, ~\protocolo_de_comunicaçao_1_start , Dflag);  // AND_Gate
  xor xor_1 (xor_1_out, or_2_out, and_2_out);
  or or_4 (or_4_out, \protocolo_de_comunicaçao_1_start , and_3_out);
  or or_5 (or_5_out, or_1_out, Accept);
  not not_1 (not_1_out, \protocolo_de_comunicaçao_1_start );
  MUX2X1 mux2x1_1 (.A0(and_2_out), .A1(Accept), .R0(mux2x1_1_r0), .S0(d_ff_3_q));  // open: s0_2
  or or_6 (or_6_out, 1'b0, Accept);
  MUX4X1 mux4x1_1 (
    .in_1(or_3_out), .in_2(or_6_out), .in_3(or_4_out), .in_4(or_5_out), .out_9(mux4x1_1_out_9),
    .S1(d_ff_2_q), .S0(d_ff_1_q), .out_7(mux4x1_1_out_7), .out_8(mux4x1_1_out_8));
  xor xor_2 (xor_2_out, 1'b1, and_4_out);
  MUX4X1 mux4x1_2 (
    .in_1(1'b0), .in_2(xor_2_out), .in_3(not_1_out), .in_4(xor_1_out), .out_9(mux4x1_2_out_9),
    .S1(mux4x1_1_out_7), .S0(mux4x1_1_out_8));  // open: out_7, out_8
  D_Flip_Flop d_ff_1 (.clk(SCLK), .D(mux4x1_1_out_9), .Q(d_ff_1_q));  // open: Qn, preset, en, reset
  D_Flip_Flop d_ff_2 (.clk(SCLK), .D(mux4x1_2_out_9), .Q(d_ff_2_q));  // open: Qn, preset, en, reset
  D_Flip_Flop d_ff_3 (.clk(SCLK), .D(mux2x1_1_r0), .Q(d_ff_3_q));  // open: Qn, preset, en, reset
  and and_4 (and_4_out, d_ff_1_q, ~d_ff_2_q, d_ff_3_q);  // AND_Gate
  and and_5 (Init_2, d_ff_1_q, ~d_ff_2_q);  // AND_Gate
  and and_6 (WR, ~d_ff_1_q, d_ff_2_q);  // AND_Gate
  and and_7 (Busy, ~d_ff_1_q, ~d_ff_2_q, d_ff_3_q);  // AND_Gate

  assign Dxval = Busy;

  // Other names for the same wires on the sheet: C = SCLK

  // Notes on the sheet:
  //   Start
  //   S0
  //   S1
endmodule

module SerialReceiver (
  input  SDX,
  input  SCLK,
  input  Accept_Enable,
  output [9:0] out_4,
  output DXval,
  output busy
);

  wire equal5_1_out_2, equal6_1_out_2, equal10_1_out_2, equal11_1_out_2, mux2x1_1_r0, mux2x1_2_r0,
       mux2x1_2_s0_2, \paritycheckersimples_1_é_impar , serialcontrol_1_init, serialcontrol_1_init_2;
  wire [3:0] contador2_1_out_3;

  SerialControl serialcontrol_1 (
    .SDX(SDX), .SCLK(SCLK), .Dflag(mux2x1_1_r0), .Pflag(mux2x1_2_r0),
    .RXerror(\paritycheckersimples_1_é_impar ), .Accept(Accept_Enable), .init(serialcontrol_1_init),
    .Init_2(serialcontrol_1_init_2), .WR(DXval), .Dxval(busy));  // open: Busy
  Contador2 contador2_1 (.Clear(serialcontrol_1_init), .out_3(contador2_1_out_3), .Clock(SCLK));
  ParityCheckerSimples paritycheckersimples_1 (
    .SCLK(SCLK), .SDX_data(SDX), .Clear(serialcontrol_1_init), .\é_impar (\paritycheckersimples_1_é_impar ));
  Equal5 equal5_1 (.in_1(contador2_1_out_3), .out_2(equal5_1_out_2));
  MUX2X1 mux2x1_1 (.A0(equal10_1_out_2), .A1(equal5_1_out_2), .R0(mux2x1_1_r0), .S0(mux2x1_2_s0_2));  // open: s0_2
  DataStorage datastorage_1 (
    .SCLCK_clock(SCLK), .SDX_data__em_pulsos(SDX), .A0_3_adress(contador2_1_out_3), .out_5(out_4),
    .Enable(serialcontrol_1_init_2));
  Equal10 equal10_1 (.in_1(contador2_1_out_3), .out_2(equal10_1_out_2));
  Equal6 equal6_1 (.in_1(contador2_1_out_3), .out_2(equal6_1_out_2));
  MUX2X1 mux2x1_2 (.A0(equal11_1_out_2), .A1(equal6_1_out_2), .R0(mux2x1_2_r0), .s0_2(mux2x1_2_s0_2), .S0(out_4[0]));
  Equal11 equal11_1 (.in_1(contador2_1_out_3), .out_2(equal11_1_out_2));

  // Notes on the sheet:
  //   dFlag
  //   0
  //   1
  //   pFlag
  //   0
  //   1
  //   LnD
endmodule

module Dispatcher (
  input  Dval,
  input  [9:0] in_2,
  input  CLK,
  input  Finish,
  output WrD,
  output [8:0] out_6,
  output WrL,
  output Done
);

  wire and_1_out, and_2_out, d_ff_1_q, d_ff_2_q, mux4x1_1_out_7, mux4x1_1_out_8, mux4x1_1_out_9,
       mux4x1_2_out_9, or_1_out, xor_1_out;

  and and_1 (and_1_out, Dval, in_2[0]);
  and and_2 (and_2_out, ~in_2[0], Dval);  // AND_Gate
  or or_1 (or_1_out, and_1_out, and_2_out);
  xor xor_1 (xor_1_out, or_1_out, and_2_out);
  MUX4X1 mux4x1_1 (
    .in_1(xor_1_out), .in_2(1'b1), .in_3(Finish), .in_4(1'b0), .out_9(mux4x1_1_out_9), .S1(d_ff_2_q),
    .S0(d_ff_1_q), .out_7(mux4x1_1_out_7), .out_8(mux4x1_1_out_8));
  MUX4X1 mux4x1_2 (
    .in_1(and_2_out), .in_2(Finish), .in_3(1'b1), .in_4(1'b0), .out_9(mux4x1_2_out_9), .S1(mux4x1_1_out_7),
    .S0(mux4x1_1_out_8));  // open: out_7, out_8
  D_Flip_Flop d_ff_1 (.clk(CLK), .D(mux4x1_1_out_9), .Q(d_ff_1_q));  // open: Qn, preset, en, reset
  D_Flip_Flop d_ff_2 (.clk(CLK), .D(mux4x1_2_out_9), .Q(d_ff_2_q));  // open: Qn, preset, en, reset
  and and_3 (WrD, d_ff_2_q, ~d_ff_1_q);  // AND_Gate
  and and_4 (WrL, ~d_ff_2_q, d_ff_1_q);  // AND_Gate
  and and_5 (Done, d_ff_1_q, d_ff_1_q);

  assign out_6 = in_2[9:1];

  // Notes on the sheet:
  //   LnD
  //   S0
  //   S1
endmodule

module Integrated_Output_System (
  input  Fni,
  input  SDX,
  input  SCLK
);

  wire dispatcher_1_done, dispatcher_1_wrd, dispatcher_1_wrl, serialreceiver_1_busy, serialreceiver_1_dxval;
  wire [8:0] dispatcher_1_out_6;
  wire [9:0] serialreceiver_1_out_4;

  SerialReceiver serialreceiver_1 (
    .SDX(SDX), .SCLK(SCLK), .Accept_Enable(dispatcher_1_done), .out_4(serialreceiver_1_out_4),
    .DXval(serialreceiver_1_dxval), .busy(serialreceiver_1_busy));
  Dispatcher dispatcher_1 (
    .Dval(serialreceiver_1_dxval), .CLK(SCLK), .Finish(Fni), .WrD(dispatcher_1_wrd), .WrL(dispatcher_1_wrl),
    .Done(dispatcher_1_done), .in_2(serialreceiver_1_out_4), .out_6(dispatcher_1_out_6));

  // Notes on the sheet:
  //   busy
  //   Control
  //   Serial Receiver
  //   Dispatcher
  //   Ej
  //   PI d0:3
  //   RS
  //   D0:7
  //   E
  //   Dispenser
  //   LCD
endmodule
