// Logisim project ALU_empty_1920_v0.circ as structural Verilog: 14 circuits, main circuit main
module main (
  input  in_1,
  input  in_2,
  input  in_3,
  input  in_4,
  input  in_5,
  input  in_6,
  input  in_7,
  input  in_8,
  input  in_9,
  input  in_10,
  input  in_11,
  input  in_12,
  output out_13,
  output out_14,
  output out_15,
  output out_16,
  output out_17,
  output out_18,
  output out_19
);

  ALU alu_1 (
    .A0(in_4), .A1(in_3), .A2(in_2), .A3(in_1), .B0(in_8), .B1(in_7), .B2(in_6), .B3(in_5), .S0(in_10),
    .R0(out_17), .R1(out_16), .R2(out_15), .R3(out_14), .S1(in_11), .S2(in_12), .CyBwi(in_9), .Ov(out_19),
    .CyBwo(out_18), .L(out_13));
endmodule

module ALU (
  input  CyBwi,
  input  A0,
  input  A1,
  input  A2,
  input  A3,
  input  B0,
  input  B1,
  input  B2,
  input  B3,
  input  S0,
  input  S1,
  input  S2,
  output L,
  output R0,
  output R1,
  output R2,
  output R3,
  output CyBwo,
  output Ov
);

  wire aritmethic_1_cybwa, aritmethic_1_ra0, aritmethic_1_ra1, aritmethic_1_ra2, aritmethic_1_ra3,
       logic_shift_1_cys, logic_shift_1_rls0, logic_shift_1_rls1, logic_shift_1_rls2, logic_shift_1_rls3,
       logic_shift_1_s0_2, logic_shift_1_s1_2, mux_2x1_1_out_4;

  Aritmethic aritmethic_1 (
    .CyBwi(CyBwi), .A0(A0), .A1(A1), .A2(A2), .A3(A3), .B0(B0), .B1(B1), .B2(B2), .S0(logic_shift_1_s0_2),
    .S1(logic_shift_1_s1_2), .RA0(aritmethic_1_ra0), .RA1(aritmethic_1_ra1), .RA2(aritmethic_1_ra2),
    .RA3(aritmethic_1_ra3), .OvA(Ov), .B3(B3), .G(L), .CyBwA(aritmethic_1_cybwa));
  Logic_Shift logic_shift_1 (
    .CyBwi(CyBwi), .A0(A0), .A1(A1), .A2(A2), .A3(A3), .B0(B0), .B1(B1), .B2(B2), .B3(B3), .S0(S0), .S1(S1),
    .RLS0(logic_shift_1_rls0), .RLS1(logic_shift_1_rls1), .RLS2(logic_shift_1_rls2),
    .RLS3(logic_shift_1_rls3), .CyS(logic_shift_1_cys), .S0_2(logic_shift_1_s0_2), .S1_2(logic_shift_1_s1_2));
  MUX_2x4 mux_2x4_1 (
    .A0(aritmethic_1_ra0), .A1(aritmethic_1_ra1), .A2(aritmethic_1_ra2), .A3(aritmethic_1_ra3),
    .B0(logic_shift_1_rls0), .B1(logic_shift_1_rls1), .B2(logic_shift_1_rls2), .B3(logic_shift_1_rls3),
    .Y0(R0), .Y1(R1), .Y3(R3), .in_9(mux_2x1_1_out_4), .Y2(R2));  // open: out_10
  MUX_2x1 mux_2x1_1 (
    .in_1(aritmethic_1_cybwa), .in_2(logic_shift_1_cys), .out_5(CyBwo), .in_3(S2), .out_4(mux_2x1_1_out_4));

  // Notes on the sheet:
  //   RLS0
  //   RLS1
  //   RLS2
  //   RLS3
  //   CyS
  //   OvA
  //   RA0
  //   RA1
  //   RA2
  //   RA3
  //   CyBwA
endmodule

module Aritmethic (
  input  CyBwi,
  input  A0,
  input  A1,
  input  A2,
  input  A3,
  input  B0,
  input  B1,
  input  B2,
  input  B3,
  input  S0,
  input  S1,
  output RA0,
  output RA1,
  output RA2,
  output RA3,
  output G,
  output OvA,
  output CyBwA
);

  wire adder_input_adapter_1_a0_2, adder_input_adapter_1_a1_2, adder_input_adapter_1_a2_2,
       adder_input_adapter_1_a3_2, adder_input_adapter_1_bt0, adder_input_adapter_1_bt1,
       adder_input_adapter_1_bt2, adder_input_adapter_1_bt3, adder_input_adapter_1_c0, n4bit_full_adder_1_c3,
       n4bit_full_adder_1_c4;

  ADDER_Input_Adapter adder_input_adapter_1 (
    .B0(B0), .B1(B1), .B2(B2), .B3(B3), .BT0(adder_input_adapter_1_bt0), .BT1(adder_input_adapter_1_bt1),
    .BT2(adder_input_adapter_1_bt2), .BT3(adder_input_adapter_1_bt3), .S1(S1), .S0(S0), .A0(A0),
    .A0_2(adder_input_adapter_1_a0_2), .A1(A1), .A1_2(adder_input_adapter_1_a1_2), .A2(A2),
    .A2_2(adder_input_adapter_1_a2_2), .A3(A3), .A3_2(adder_input_adapter_1_a3_2), .CyBwi(CyBwi),
    .C0(adder_input_adapter_1_c0));
  _4bit_full_ADDER u_4bit_full_adder_1 (
    .A0(adder_input_adapter_1_a0_2), .A1(adder_input_adapter_1_a1_2), .A2(adder_input_adapter_1_a2_2),
    .B0(adder_input_adapter_1_bt0), .B1(adder_input_adapter_1_bt1), .B2(adder_input_adapter_1_bt2), .S0(RA0),
    .S1(RA1), .S2(RA2), .C0(adder_input_adapter_1_c0), .C4(n4bit_full_adder_1_c4),
    .C3(n4bit_full_adder_1_c3), .A3(adder_input_adapter_1_a3_2), .S3(RA3), .B3(adder_input_adapter_1_bt3));
  Flags flags_1 (
    .C3(n4bit_full_adder_1_c3), .C4(n4bit_full_adder_1_c4), .S0(S0), .Ov(OvA), .G(G), .CwBwo(CyBwA),
    .RA3(RA3), .RA2(RA2), .RA1(RA1), .RA0(RA0));

  // Notes on the sheet:
  //   C0
  //   BT0
  //   BT1
  //   BT2
  //   BT3
  //   Caux
  //   Cout
endmodule

module ADDER_Input_Adapter (
  input  CyBwi,
  input  A0,
  input  A1,
  input  A2,
  input  A3,
  input  B0,
  input  B1,
  input  B2,
  input  B3,
  input  S1,
  input  S0,
  output C0,
  output A0_2,
  output A1_2,
  output A2_2,
  output A3_2,
  output BT0,
  output BT1,
  output BT2,
  output BT3
);

  CyBwi_Adapter cybwi_adapter_1 (
    .S0(S0), .S1(S1), .C0(C0), .CyBwi(CyBwi), .CyBwi_2(S1), .S0_2(S1), .S1_2(S1));  // open: C0_2
  xor xor_1 (BT0, B0, S0);
  xor xor_2 (BT1, B1, S0);
  xor xor_3 (BT2, B2, S0);
  xor xor_4 (BT3, B3, S0);

  assign A0_2 = A0;
  assign A1_2 = A1;
  assign A2_2 = A2;
  assign A3_2 = A3;
endmodule

module CyBwi_Adapter (
  input  CyBwi,
  input  S0,
  input  S1,
  input  CyBwi_2,
  input  S0_2,
  input  S1_2,
  output C0,
  output C0_2
);

  wire and_1_out, and_2_out, and_3_out, and_4_out;

  and and_1 (and_1_out, ~CyBwi, S0);  // AND_Gate
  and and_2 (and_2_out, CyBwi, S1);
  and and_3 (and_3_out, ~CyBwi_2, S0_2);  // AND_Gate
  and and_4 (and_4_out, CyBwi_2, S1_2);
  xor xor_1 (C0, and_1_out, and_2_out);
  or or_1 (C0_2, and_3_out, and_4_out);
endmodule

module _4bit_full_ADDER (
  input  C0,
  input  A0,
  input  B0,
  input  A1,
  input  B1,
  input  A2,
  input  B2,
  input  A3,
  input  B3,
  output S0,
  output S1,
  output S2,
  output S3,
  output C4,
  output C3
);

  wire singlebit_full_adder_1_out_5, singlebit_full_adder_2_out_5;

  SingleBit_full_ADDER singlebit_full_adder_1 (
    .A0(A0), .B0(B0), .out_4(S0), .C0(C0), .out_5(singlebit_full_adder_1_out_5));
  SingleBit_full_ADDER singlebit_full_adder_2 (
    .A0(A1), .B0(B1), .out_4(S1), .C0(singlebit_full_adder_1_out_5), .out_5(singlebit_full_adder_2_out_5));
  SingleBit_full_ADDER singlebit_full_adder_3 (
    .A0(A2), .B0(B2), .out_4(S2), .C0(singlebit_full_adder_2_out_5), .out_5(C3));
  SingleBit_full_ADDER singlebit_full_adder_4 (.A0(A3), .B0(B3), .out_4(S3), .C0(C3), .out_5(C4));
endmodule

module SingleBit_full_ADDER (
  input  C0,
  input  A0,
  input  B0,
  output out_4,
  output out_5
);

  wire and_1_out, and_2_out, and_3_out, xor_1_out;

  xor xor_1 (xor_1_out, A0, B0);
  and and_1 (and_1_out, A0, C0);
  and and_2 (and_2_out, A0, B0);
  and and_3 (and_3_out, C0, B0);
  xor xor_2 (out_4, C0, xor_1_out);
  or or_1 (out_5, and_1_out, and_2_out, and_3_out);
endmodule

module Logic_Shift (
  input  B0,
  input  B1,
  input  B2,
  input  B3,
  input  A0,
  input  A1,
  input  A2,
  input  A3,
  input  CyBwi,
  input  S0,
  input  S1,
  output RLS0,
  output RLS1,
  output RLS2,
  output RLS3,
  output CyS,
  output S0_2,
  output S1_2
);

  wire or_1_out, or_2_out, or_3_out, or_4_out, shifter_1_rs0, shifter_1_rs1, shifter_1_rs2, shifter_1_rs3;

  Shifter shifter_1 (
    .B0(B0), .B1(B1), .A3(A3), .RS3(shifter_1_rs3), .RS2(shifter_1_rs2), .RS1(shifter_1_rs1),
    .RS0(shifter_1_rs0), .CyS(CyS), .A2(A2), .A1(A1), .A0(A0), .CyBwi(CyBwi));
  or or_1 (or_1_out, B0, A0);
  or or_2 (or_2_out, B1, A1);
  or or_3 (or_3_out, B2, A2);
  or or_4 (or_4_out, B3, A3);
  MUX_2x4 mux_2x4_1 (
    .A0(or_1_out), .A1(or_2_out), .A2(or_3_out), .A3(or_4_out), .B0(shifter_1_rs0), .B1(shifter_1_rs1),
    .B2(shifter_1_rs2), .B3(shifter_1_rs3), .Y0(RLS0), .Y1(RLS1), .Y3(RLS3), .in_9(S0), .Y2(RLS2));  // open: out_10

  assign S0_2 = S0;
  assign S1_2 = S1;

  // Notes on the sheet:
  //   F_or0
  //   F_or1
  //   F_or2
  //   F_or3
  //   RS0
  //   RS1
  //   RS2
  //   RS3
endmodule

module Shifter (
  input  A3,
  input  A2,
  input  A1,
  input  A0,
  input  CyBwi,
  input  B1,
  input  B0,
  output RS3,
  output RS2,
  output RS1,
  output RS0,
  output CyS
);

  wire mux_4x1_1_out_7, mux_4x1_1_out_8, mux_4x1_2_out_7, mux_4x1_2_out_8, mux_4x1_3_out_7, mux_4x1_3_out_8;

  MUX_4x1 mux_4x1_1 (
    .in_1(A2), .in_2(A3), .in_3(A3), .in_4(A3), .out_9(RS2), .out_7(mux_4x1_1_out_7),
    .out_8(mux_4x1_1_out_8), .in_5(B1), .in_6(B0));
  MUX_4x1 mux_4x1_2 (
    .in_1(A1), .in_2(A2), .in_3(A3), .in_4(A3), .out_9(RS1), .out_7(mux_4x1_2_out_7),
    .out_8(mux_4x1_2_out_8), .in_5(mux_4x1_1_out_7), .in_6(mux_4x1_1_out_8));
  MUX_4x1 mux_4x1_3 (
    .in_1(A0), .in_2(A1), .in_3(A2), .in_4(A3), .out_9(RS0), .out_7(mux_4x1_3_out_7),
    .out_8(mux_4x1_3_out_8), .in_5(mux_4x1_2_out_7), .in_6(mux_4x1_2_out_8));
  MUX_4x1 mux_4x1_4 (
    .in_1(CyBwi), .in_2(A0), .in_3(A1), .in_4(A2), .out_9(CyS), .in_5(mux_4x1_3_out_7), .in_6(mux_4x1_3_out_8));  // open: out_7, out_8

  assign RS3 = A3;
endmodule

module MUX_2x1 (
  input  in_1,
  input  in_2,
  input  in_3,
  output out_4,
  output out_5
);

  wire and_1_out, and_2_out;

  and and_1 (and_1_out, in_1, ~in_3);  // AND_Gate
  and and_2 (and_2_out, in_2, in_3);
  or or_1 (out_5, and_1_out, and_2_out);

  assign out_4 = in_3;
endmodule

module MUX_4x1 (
  input  in_1,
  input  in_2,
  input  in_3,
  input  in_4,
  input  in_5,
  input  in_6,
  output out_7,
  output out_8,
  output out_9
);

  wire and_1_out, and_2_out, and_3_out, and_4_out;

  and and_1 (and_1_out, in_1, ~in_6, ~in_5);  // AND_Gate
  and and_2 (and_2_out, in_2, in_6, ~in_5);  // AND_Gate
  and and_3 (and_3_out, in_3, ~in_6, in_5);  // AND_Gate
  and and_4 (and_4_out, in_4, in_6, in_5);
  or or_1 (out_9, and_1_out, and_2_out, and_3_out, and_4_out);

  assign out_7 = in_5;
  assign out_8 = in_6;
endmodule

module MUX_2x4 (
  input  A0,
  input  B0,
  input  A1,
  input  B1,
  input  A2,
  input  B2,
  input  A3,
  input  B3,
  input  in_9,
  output out_10,
  output Y0,
  output Y1,
  output Y2,
  output Y3
);

  wire mux_2x1_2_out_4, mux_2x1_3_out_4, mux_2x1_4_out_4;

  MUX_2x1 mux_2x1_1 (.in_1(A0), .in_2(B0), .out_5(Y0), .in_3(mux_2x1_2_out_4), .out_4(out_10));
  MUX_2x1 mux_2x1_2 (.in_1(A1), .in_2(B1), .out_5(Y1), .in_3(mux_2x1_3_out_4), .out_4(mux_2x1_2_out_4));
  MUX_2x1 mux_2x1_3 (.in_1(A2), .in_2(B2), .out_5(Y2), .in_3(mux_2x1_4_out_4), .out_4(mux_2x1_3_out_4));
  MUX_2x1 mux_2x1_4 (.in_1(A3), .in_2(B3), .out_5(Y3), .in_3(in_9), .out_4(mux_2x1_4_out_4));
endmodule

module MUX_4x4 (
  input  A0,
  input  B0,
  input  C0,
  input  D0,
  input  A1,
  input  B1,
  input  C1,
  input  D1,
  input  A2,
  input  B2,
  input  C2,
  input  D2,
  input  A3,
  input  B3,
  input  C3,
  input  D3,
  input  in_17,
  input  in_18,
  output out_19,
  output out_20,
  output Y0,
  output Y1,
  output Y2,
  output Y3
);

  wire mux_4x1_2_out_7, mux_4x1_2_out_8, mux_4x1_3_out_7, mux_4x1_3_out_8, mux_4x1_4_out_7, mux_4x1_4_out_8;

  MUX_4x1 mux_4x1_1 (
    .in_1(A0), .in_2(B0), .in_3(C0), .in_4(D0), .out_9(Y0), .out_7(out_19), .out_8(out_20),
    .in_5(mux_4x1_2_out_7), .in_6(mux_4x1_2_out_8));
  MUX_4x1 mux_4x1_2 (
    .in_1(A1), .in_2(B1), .in_3(C1), .in_4(D1), .out_9(Y1), .out_7(mux_4x1_2_out_7), .out_8(mux_4x1_2_out_8),
    .in_5(mux_4x1_3_out_7), .in_6(mux_4x1_3_out_8));
  MUX_4x1 mux_4x1_3 (
    .in_1(A2), .in_2(B2), .in_3(C2), .in_4(D2), .out_9(Y2), .out_7(mux_4x1_3_out_7), .out_8(mux_4x1_3_out_8),
    .in_5(mux_4x1_4_out_7), .in_6(mux_4x1_4_out_8));
  MUX_4x1 mux_4x1_4 (
    .in_1(A3), .in_2(B3), .in_3(C3), .in_4(D3), .out_9(Y3), .out_7(mux_4x1_4_out_7), .out_8(mux_4x1_4_out_8),
    .in_5(in_17), .in_6(in_18));
endmodule

module Flags (
  input  RA0,
  input  RA1,
  input  RA2,
  input  RA3,
  input  C3,
  input  C4,
  input  S0,
  output G,
  output Ov,
  output CwBwo
);

  wire or_1_out, xnor_1_out;

  xor xor_1 (Ov, C3, C4);
  or or_1 (or_1_out, RA0, RA1, RA2, RA3);
  xnor xnor_1 (xnor_1_out, RA3, Ov);
  xor xor_2 (CwBwo, C4, S0);
  and and_1 (G, or_1_out, xnor_1_out);
endmodule
