// Logisim project A_PORTA_DA_GARAGEM_v2.circ as structural Verilog: 4 circuits, main circuit main
module main (
  input  Aberto,
  input  Fechado,
  input  Pessoa,
  output Motor_On,
  output SF
);

  wire and_1_out, and_2_out, clock_1_out, d_ff_2_q, multiplexer_1_out, multiplexer_2__0_3,
       multiplexer_2__1_3, multiplexer_2_out, not_1_out, not_2_out, or_1_out;

  and and_1 (and_1_out, Pessoa, ~Fechado);  // AND_Gate
  and and_2 (and_2_out, ~Fechado, ~Pessoa);  // AND_Gate
  not not_1 (not_1_out, Aberto);
  not not_2 (not_2_out, Pessoa);
  or or_1 (or_1_out, and_1_out, and_2_out);
  MultiPlexer multiplexer_1 (
    ._3(or_1_out), ._2(not_2_out), ._1_2(not_1_out), ._0_2(Pessoa), .Out(multiplexer_1_out),
    ._0(multiplexer_2__0_3), ._1(multiplexer_2__1_3));  // open: _0_3, _1_3
  MultiPlexer multiplexer_2 (
    ._3(and_2_out), ._2(1'b1), ._1_2(Aberto), ._0_2(1'b0), .Out(multiplexer_2_out), ._0(Motor_On),
    ._1(d_ff_2_q), ._0_3(multiplexer_2__0_3), ._1_3(multiplexer_2__1_3));
  Clock clock_1 (.out(clock_1_out));
  D_Flip_Flop d_ff_1 (.clk(clock_1_out), .D(multiplexer_1_out), .Q(Motor_On));  // open: Qn, preset, en, reset
  D_Flip_Flop d_ff_2 (.clk(clock_1_out), .D(multiplexer_2_out), .Q(d_ff_2_q));  // open: Qn, preset, en, reset
  and and_3 (SF, Motor_On, d_ff_2_q);

  // Notes on the sheet:
  //   3
  //   1
  //   2
  //   X0
  //   X1
  //   S0
  //   3
  //   2
  //   S1
  //   11
  //   12
  //   5
  //   9
endmodule

module MultiPlexer (
  input  _0,
  input  _1,
  input  _3,
  input  _2,
  input  _1_2,
  input  _0_2,
  output Out,
  output _0_3,
  output _1_3
);

  wire and_1_out, and_2_out, and_3_out, and_4_out;

  and and_1 (and_1_out, _0, _3, _1);
  and and_2 (and_2_out, ~_0, _2, _1);  // AND_Gate
  and and_3 (and_3_out, _0, _1_2, ~_1);  // AND_Gate
  and and_4 (and_4_out, ~_1, _0_2, ~_0);  // AND_Gate
  or or_1 (Out, and_1_out, and_2_out, and_3_out, and_4_out);

  assign _0_3 = _0;
  assign _1_3 = _1;
endmodule

module register (
  input  CLK,
  input  D0,
  input  D1,
  input  reset,
  output Q0,
  output Q1
);

  D_Flip_Flop d_ff_1 (.clk(CLK), .D(D0), .Q(Q0), .reset(reset));  // open: Qn, preset, en
  D_Flip_Flop d_ff_2 (.clk(CLK), .D(D1), .Q(Q1), .reset(reset));  // open: Qn, preset, en
endmodule

module REGISTER (
  input  D0,
  input  D1,
  input  in_3,
  output Q0,
  output Q1
);

  wire clock_1_out;

  Clock clock_1 (.out(clock_1_out));
  register register_1 (.CLK(clock_1_out), .D0(D0), .reset(in_3), .Q0(Q0), .Q1(Q1), .D1(D1));
endmodule
