// Logisim project Aula Prática 1 de Circuitos Sequenciais 44873 46046.circ as structural Verilog: 14 circuits, main circuit main
module main (
  input  Aberto,
  input  Fechado,
  input  Pessoa,
  output T10,
  output Motor_On_a_abrir,
  output SF
);

  wire and_1_out, and_2_out, and_3_out, clock_1_out, counter_tipo_t_1_q0, counter_tipo_t_1_q1,
       counter_tipo_t_1_q2, counter_tipo_t_1_q3, d_ff_2_q, multiplexer_1_out, multiplexer_2__0_3,
       multiplexer_2__1_3, multiplexer_2_out, not_1_out, or_1_out, or_2_out;

  not not_1 (not_1_out, Aberto);
  and and_1 (and_1_out, ~Pessoa, T10);  // AND_Gate
  and and_2 (and_2_out, Pessoa, ~Fechado);  // AND_Gate
  and and_3 (and_3_out, ~Fechado, ~Pessoa);  // AND_Gate
  or or_1 (or_1_out, and_2_out, and_3_out);
  MultiPlexer multiplexer_1 (
    ._3(or_1_out), ._2(and_1_out), ._1_2(not_1_out), ._0_2(Pessoa), .Out(multiplexer_1_out),
    ._0(multiplexer_2__0_3), ._1(multiplexer_2__1_3));  // open: _0_3, _1_3
  MultiPlexer multiplexer_2 (
    ._3(and_3_out), ._2(1'b1), ._1_2(Aberto), ._0_2(1'b0), .Out(multiplexer_2_out), ._0(Motor_On_a_abrir),
    ._1(d_ff_2_q), ._0_3(multiplexer_2__0_3), ._1_3(multiplexer_2__1_3));
  Clock clock_1 (.out(clock_1_out));
  D_Flip_Flop d_ff_1 (.clk(clock_1_out), .D(multiplexer_1_out), .Q(Motor_On_a_abrir));  // open: Qn, preset, en, reset
  D_Flip_Flop d_ff_2 (.clk(clock_1_out), .D(multiplexer_2_out), .Q(d_ff_2_q));  // open: Qn, preset, en, reset
  COUNTER_tipo_T counter_tipo_t_1 (
    .RESET(or_2_out), .Q0(counter_tipo_t_1_q0), .Q1(counter_tipo_t_1_q1), .Q2(counter_tipo_t_1_q2),
    .Q3(counter_tipo_t_1_q3), .CLOCK(clock_1_out));
  or or_2 (or_2_out, Pessoa, Motor_On_a_abrir);
  and and_4 (SF, Motor_On_a_abrir, d_ff_2_q);
  and and_5 (T10, ~counter_tipo_t_1_q0, counter_tipo_t_1_q1, ~counter_tipo_t_1_q2, counter_tipo_t_1_q3);  // AND_Gate

  // Other names for the same wires on the sheet: T = T10

  // Notes on the sheet:
  //   3
  //   1
  //   2
  //   X0
  //   X1
  //   S0
  //   3
  //   2
  //   S1
  //   11
  //   12
  //   5
  //   9
endmodule

module MultiPlexer (
  input  _0,
  input  _1,
  input  _3,
  input  _2,
  input  _1_2,
  input  _0_2,
  output Out,
  output _0_3,
  output _1_3
);

  wire and_1_out, and_2_out, and_3_out, and_4_out;

  and and_1 (and_1_out, _0, _3, _1);
  and and_2 (and_2_out, ~_0, _2, _1);  // AND_Gate
  and and_3 (and_3_out, _0, _1_2, ~_1);  // AND_Gate
  and and_4 (and_4_out, ~_1, _0_2, ~_0);  // AND_Gate
  or or_1 (Out, and_1_out, and_2_out, and_3_out, and_4_out);

  assign _0_3 = _0;
  assign _1_3 = _1;
endmodule

module register (
  input  CLOCK,
  input  D0,
  input  D1,
  input  RESET,
  output Q0,
  output Q1
);

  D_edge_trigger d_edge_trigger_1 (.CLK(CLOCK), .D(D0), .AR(RESET), .out_5(Q0));  // open: AS
  D_edge_trigger d_edge_trigger_2 (.CLK(CLOCK), .D(D1), .AR(RESET), .out_5(Q1));  // open: AS
endmodule

module REGISTER (
  input  D0,
  input  D1,
  input  in_3,
  output Q0,
  output Q1
);

  wire clock_1_out;

  Clock clock_1 (.out(clock_1_out));
  register register_1 (.D1(D1), .RESET(in_3), .CLOCK(clock_1_out), .D0(D0), .Q0(Q0), .Q1(Q1));
endmodule

module D_edge_trigger (
  input  CLK,
  input  D,
  input  AS,
  input  AR,
  output out_5
);

  D_Flip_Flop d_ff_1 (.clk(CLK), .D(D), .Q(out_5), .preset(AS), .en(1'b1), .reset(AR));  // open: Qn
endmodule

module D_edge_trigger_para_count_PL (
  input  CLK,
  input  D,
  input  AS,
  input  AR,
  output out_5
);

  D_Flip_Flop d_ff_1 (.clk(CLK), .D(D), .Q(out_5), .preset(AS), .en(1'b1), .reset(AR));  // open: Qn
endmodule

module T_edge_trigger (
  input  CLK,
  input  D,
  input  AS,
  input  AR,
  output out_5
);

  T_Flip_Flop t_ff_1 (.clk(CLK), .T(D), .Q(out_5), .preset(AS), .reset(AR), .en(1'b1));  // open: Qn
endmodule

module T__Q (
  input  CLK,
  input  D,
  input  AS,
  input  AR,
  output out_5
);

  T_Flip_Flop t_ff_1 (.clk(CLK), .T(D), .Qn(out_5), .preset(AS), .reset(AR), .en(1'b1));  // open: Q
endmodule

module COUNTER_tipo_D (
  input  Clock,
  input  RESET,
  output Q3,
  output Q2,
  output Q1,
  output Q0
);

  wire and_1_out, and_2_out, and_3_out, xor_1_out, xor_2_out, xor_3_out, xor_4_out;

  xor xor_1 (xor_1_out, Q0, 1'b1);
  D_edge_trigger d_edge_trigger_1 (.CLK(Clock), .D(xor_1_out), .AR(RESET), .out_5(Q0));  // open: AS
  and and_1 (and_1_out, 1'b1, Q0);
  xor xor_2 (xor_2_out, Q1, and_1_out);
  D_edge_trigger d_edge_trigger_2 (.CLK(Clock), .D(xor_2_out), .AR(RESET), .out_5(Q1));  // open: AS
  and and_2 (and_2_out, and_1_out, Q1);
  xor xor_3 (xor_3_out, Q2, and_2_out);
  D_edge_trigger d_edge_trigger_3 (.CLK(Clock), .D(xor_3_out), .AR(RESET), .out_5(Q2));  // open: AS
  and and_3 (and_3_out, and_2_out, Q2);
  xor xor_4 (xor_4_out, Q3, and_3_out);
  D_edge_trigger d_edge_trigger_4 (.CLK(Clock), .D(xor_4_out), .AR(RESET), .out_5(Q3));  // open: AS

  // Notes on the sheet:
  //   CE
  //   Q0
  //   Q1
  //   Q2
  //   Q3
endmodule

module COUNTER_tipo_T (
  input  CLOCK,
  input  RESET,
  output Q0,
  output Q1,
  output Q2,
  output Q3
);

  wire and_1_out, and_2_out, and_3_out, not_1_out;

  not not_1 (not_1_out, RESET);
  T_edge_trigger t_edge_trigger_1 (.CLK(CLOCK), .D(not_1_out), .AR(RESET), .out_5(Q0));  // open: AS
  T_edge_trigger t_edge_trigger_2 (.CLK(CLOCK), .D(and_1_out), .AR(RESET), .out_5(Q1));  // open: AS
  and and_1 (and_1_out, Q0, not_1_out);
  T_edge_trigger t_edge_trigger_3 (.CLK(CLOCK), .D(and_2_out), .AR(RESET), .out_5(Q2));  // open: AS
  and and_2 (and_2_out, Q1, and_1_out);
  T_edge_trigger t_edge_trigger_4 (.CLK(CLOCK), .D(and_3_out), .AR(RESET), .out_5(Q3));  // open: AS
  and and_3 (and_3_out, Q2, and_2_out);
endmodule

module counter_tipo_T_2_down (
  input  CLOCK,
  input  RESET,
  output Q0,
  output Q1,
  output Q2,
  output Q3
);

  T_edge_trigger t_edge_trigger_1 (.CLK(CLOCK), .D(1'b1), .AR(RESET), .out_5(Q0));  // open: AS
  T_edge_trigger t_edge_trigger_2 (.CLK(Q0), .D(1'b1), .out_5(Q1));  // open: AS, AR
  T_edge_trigger t_edge_trigger_3 (.CLK(Q1), .D(1'b1), .AR(RESET), .out_5(Q2));  // open: AS
  T_edge_trigger t_edge_trigger_4 (.CLK(Q2), .D(1'b1), .AR(RESET), .out_5(Q3));  // open: AS
endmodule

module counter_tipo_T_3_up (
  input  CLOCK,
  input  RESET,
  output Q0,
  output Q1,
  output Q2,
  output Q3
);

  wire t_edge_trigger_1_out_5, t_edge_trigger_2_out_5, t_edge_trigger_3_out_5, t_edge_trigger_4_out_5;

  T_edge_trigger t_edge_trigger_1 (.CLK(CLOCK), .D(1'b1), .AR(RESET), .out_5(t_edge_trigger_1_out_5));  // open: AS
  not not_1 (Q0, t_edge_trigger_1_out_5);
  T_edge_trigger t_edge_trigger_2 (
    .CLK(t_edge_trigger_1_out_5), .D(1'b1), .AR(RESET), .out_5(t_edge_trigger_2_out_5));  // open: AS
  not not_2 (Q1, t_edge_trigger_2_out_5);
  T_edge_trigger t_edge_trigger_3 (
    .CLK(t_edge_trigger_2_out_5), .D(1'b1), .AR(RESET), .out_5(t_edge_trigger_3_out_5));  // open: AS
  not not_3 (Q2, t_edge_trigger_3_out_5);
  T_edge_trigger t_edge_trigger_4 (
    .CLK(t_edge_trigger_3_out_5), .D(1'b1), .AR(RESET), .out_5(t_edge_trigger_4_out_5));  // open: AS
  not not_4 (Q3, t_edge_trigger_4_out_5);
endmodule

module multiplicador_meu (
  input  [3:0] in_1,
  input  Calculate_enable,
  input  [3:0] in_3,
  output [3:0] out_4
);

  wire and_1_out, and_2_out, and_3_out, and_4_out, clock_1_out, counter_down_com_pl_parallel_load_1_q0,
       counter_down_com_pl_parallel_load_1_q1, counter_down_com_pl_parallel_load_1_q2,
       counter_down_com_pl_parallel_load_1_q3, or_1_out, Set_out;
  wire [3:0] adder_1_out;

  Clock clock_1 (.out(clock_1_out));
  and and_1 (and_1_out, Calculate_enable, clock_1_out);
  Button Set (.out(Set_out));
  counter_down_com_PL_parallel_load counter_down_com_pl_parallel_load_1 (
    .PL(Set_out), .MCLK(and_1_out), .Clear(and_4_out), .Q0(counter_down_com_pl_parallel_load_1_q0),
    .Q1(counter_down_com_pl_parallel_load_1_q1), .Q2(counter_down_com_pl_parallel_load_1_q2),
    .Q3(counter_down_com_pl_parallel_load_1_q3), .in_1(in_3));
  Adder #(.width(4)) adder_1 (.a(out_4), .b(in_1), .out(adder_1_out));  // open: cin, cout
  or or_1 (or_1_out, counter_down_com_pl_parallel_load_1_q3, counter_down_com_pl_parallel_load_1_q2, counter_down_com_pl_parallel_load_1_q1, counter_down_com_pl_parallel_load_1_q0);
  Register #(.width(4)) register_1 (.D(adder_1_out), .Q(out_4), .clk(and_2_out), .clr(Set_out));  // open: en
  and and_2 (and_2_out, and_1_out, or_1_out);
  and and_3 (and_3_out, ~counter_down_com_pl_parallel_load_1_q0, ~counter_down_com_pl_parallel_load_1_q1, ~counter_down_com_pl_parallel_load_1_q2, ~counter_down_com_pl_parallel_load_1_q3);  // AND_Gate
  and and_4 (and_4_out, and_3_out, ~Set_out);  // AND_Gate
endmodule

module counter_down_com_PL_parallel_load (
  input  [3:0] in_1,
  input  PL,
  input  MCLK,
  input  Clear,
  output Q0,
  output Q1,
  output Q2,
  output Q3
);

  wire and_1_out, and_2_out, and_3_out, and_4_out, and_5_out, and_6_out, and_7_out, xor_1_out, xor_2_out,
       xor_3_out, xor_4_out;

  and and_1 (and_1_out, PL, in_1[0]);
  xor xor_1 (xor_1_out, Q0, 1'b1);
  D_edge_trigger_para_count_PL d_edge_trigger_para_count_pl_1 (
    .CLK(MCLK), .D(xor_1_out), .AS(and_1_out), .AR(Clear), .out_5(Q0));
  and and_2 (and_2_out, 1'b1, ~Q0);  // AND_Gate
  and and_3 (and_3_out, PL, in_1[1]);
  xor xor_2 (xor_2_out, Q1, and_2_out);
  D_edge_trigger_para_count_PL d_edge_trigger_para_count_pl_2 (
    .CLK(MCLK), .D(xor_2_out), .AS(and_3_out), .AR(Clear), .out_5(Q1));
  and and_4 (and_4_out, and_2_out, ~Q1);  // AND_Gate
  xor xor_3 (xor_3_out, Q2, and_4_out);
  and and_5 (and_5_out, PL, in_1[2]);
  D_edge_trigger_para_count_PL d_edge_trigger_para_count_pl_3 (
    .CLK(MCLK), .D(xor_3_out), .AS(and_5_out), .AR(Clear), .out_5(Q2));
  and and_6 (and_6_out, and_4_out, ~Q2);  // AND_Gate
  xor xor_4 (xor_4_out, Q3, and_6_out);
  and and_7 (and_7_out, PL, in_1[3]);
  D_edge_trigger_para_count_PL d_edge_trigger_para_count_pl_4 (
    .CLK(MCLK), .D(xor_4_out), .AS(and_7_out), .AR(Clear), .out_5(Q3));
endmodule
