// Logisim project Carro Ignocao ou alarme Grupo 8 LI11D Paulo, Goncalo, Diogo 1718V.circ as structural Verilog: 1 circuit, main circuit main
// 1 ou 2 =
module main (
  input  BS_start,
  input  Cinto_do_Condutor,
  input  Cinto_de_Passageiro,
  input  K,
  input  \Presença_de_passageiro ,
  output Ignicao,
  output Alerta
);

  wire and_1_out, and_2_out, not_1_out, not_2_out, not_3_out, or_1_out;

  not not_1 (not_1_out, \Presença_de_passageiro );
  or or_1 (or_1_out, Cinto_de_Passageiro, not_1_out);
  and and_1 (and_1_out, Cinto_do_Condutor, or_1_out);
  not not_2 (not_2_out, and_1_out);
  and and_2 (and_2_out, BS_start, K);
  and and_3 (Alerta, not_2_out, K);
  and and_4 (Ignicao, and_2_out, not_3_out);
  not not_3 (not_3_out, Alerta);

  // Notes on the sheet:
  //   se nao houver passageiro, nao
  //   precisamos de nos preocupar com o seu cinto
  //   se houver presença de passageiro, vamos querer o cinto de passageiro a 1
  //   verificaçao cintos
  //   é preciso a chave inserida e o start a 1 para fazer ignicao
  //   se nao passou na verificaçao
  //   e carro for inserida a chave, dá alarme
endmodule
