// Logisim project Cofre_TP3.circ as structural Verilog: 12 circuits, main circuit main
module main (
  input  K,
  input  P,
  input  I,
  input  PA,
  input  PB,
  input  CA0,
  input  CA1,
  input  CB0,
  input  CB1,
  output Abrir,
  output Alarme,
  output Lampada
);

  wire validador_1_v;

  Validador validador_1 (
    .K(K), .PA(PA), .PB(PB), .I(I), .CA0(CA0), .CA1(CA1), .CB0(CB0), .CB1(CB1), .L(Lampada), .V(validador_1_v));
  Alarme___Controlo alarme_controlo_1 (.K(K), .V(validador_1_v), .P(P), .I(I), .A(Alarme));
  and and_1 (Abrir, K, ~Alarme);  // AND_Gate
endmodule

module Alarme___Controlo (
  input  K,
  input  V,
  input  P,
  input  I,
  output A
);

  wire and_1_out, or_1_out;

  and and_1 (and_1_out, ~P, ~I);  // AND_Gate
  or or_1 (or_1_out, ~V, and_1_out);  // OR_Gate
  and and_2 (A, K, or_1_out);
endmodule

module Validador___Controlo (
  input  K,
  input  CLK,
  input  TOpen,
  input  TCode,
  input  Err,
  input  Start,
  output InitTime,
  output SetCode,
  output L,
  output V,
  output ClrCode
);

  wire and_1_out, and_2_out, and_3_out, and_4_out, mux8x1_1_out, mux8x1_2_out, mux8x1_2_s0_2, mux8x1_2_s1_2,
       mux8x1_2_s2_2, mux8x1_3_out, mux8x1_3_s0_2, mux8x1_3_s1_2, mux8x1_3_s2_2, not_1_out, not_2_out,
       or_1_out, X0_q, X1_q, X2_q;

  and and_1 (and_1_out, ~TOpen, ~Err);  // AND_Gate
  not not_1 (not_1_out, TOpen);
  or or_1 (or_1_out, Err, ~K);  // OR_Gate
  not not_2 (not_2_out, TOpen);
  MUX8x1 mux8x1_1 (
    ._0(1'b0), ._1(1'b0), ._2(1'b0), ._3(and_1_out), ._7(1'b0), .OUT(mux8x1_1_out), .S2(mux8x1_2_s2_2),
    .S1(mux8x1_2_s1_2), .S0(mux8x1_2_s0_2));  // open: _4, _5, _6, S2_2, S1_2, S0_2
  MUX8x1 mux8x1_2 (
    ._0(Start), ._1(1'b0), ._2(1'b1), ._3(not_1_out), ._7(or_1_out), .OUT(mux8x1_2_out),
    .S2_2(mux8x1_2_s2_2), .S1_2(mux8x1_2_s1_2), .S0_2(mux8x1_2_s0_2), .S2(mux8x1_3_s2_2), .S1(mux8x1_3_s1_2),
    .S0(mux8x1_3_s0_2));  // open: _4, _5, _6
  MUX8x1 mux8x1_3 (
    ._0(1'b0), ._1(K), ._2(TCode), ._3(not_2_out), ._7(1'b1), .OUT(mux8x1_3_out), .S2_2(mux8x1_3_s2_2),
    .S1_2(mux8x1_3_s1_2), .S0_2(mux8x1_3_s0_2), .S2(X2_q), .S1(X1_q), .S0(X0_q));  // open: _4, _5, _6
  D_Flip_Flop X2 (.clk(CLK), .D(mux8x1_1_out), .Q(X2_q));  // open: Qn, preset, en, reset
  D_Flip_Flop X1 (.clk(CLK), .D(mux8x1_2_out), .Q(X1_q));  // open: Qn, preset, en, reset
  D_Flip_Flop X0 (.clk(CLK), .D(mux8x1_3_out), .Q(X0_q));  // open: Qn, preset, en, reset
  and and_2 (and_2_out, ~X2_q, X1_q, X0_q);  // AND_Gate
  and and_3 (and_3_out, V, ~K);  // AND_Gate
  and and_4 (and_4_out, and_2_out, TOpen);
  and and_5 (InitTime, ~X2_q, ~X1_q, ~X0_q);  // AND_Gate
  and and_6 (SetCode, X2_q, X1_q, X0_q);
  and and_7 (L, ~X2_q, X1_q, ~X0_q);  // AND_Gate
  and and_8 (V, ~X2_q, ~X1_q, X0_q);  // AND_Gate
  or or_2 (ClrCode, and_3_out, and_4_out);
endmodule

module MUX8x1 (
  input  _0,
  input  _1,
  input  _2,
  input  _3,
  input  _4,
  input  _5,
  input  _6,
  input  _7,
  input  S2,
  input  S1,
  input  S0,
  output S2_2,
  output S1_2,
  output S0_2,
  output OUT
);

  wire and_1_out, and_2_out, and_3_out, and_4_out, and_5_out, and_6_out, and_7_out, and_8_out, and_9_out,
       and_10_out, and_11_out, and_12_out, and_13_out, and_14_out, and_15_out, and_16_out;

  and and_1 (and_1_out, ~S0, ~S1, ~S2);  // AND_Gate
  and and_2 (and_2_out, S0, ~S1, ~S2);  // AND_Gate
  and and_3 (and_3_out, ~S0, S1, ~S2);  // AND_Gate
  and and_4 (and_4_out, S0, S1, ~S2);  // AND_Gate
  and and_5 (and_5_out, ~S0, ~S1, S2);  // AND_Gate
  and and_6 (and_6_out, S0, ~S1, S2);  // AND_Gate
  and and_7 (and_7_out, ~S0, S1, S2);  // AND_Gate
  and and_8 (and_8_out, S0, S1, S2);
  and and_9 (and_9_out, and_1_out, _0);
  and and_10 (and_10_out, and_2_out, _1);
  and and_11 (and_11_out, and_3_out, _2);
  and and_12 (and_12_out, and_4_out, _3);
  and and_13 (and_13_out, and_5_out, _4);
  and and_14 (and_14_out, and_6_out, _5);
  and and_15 (and_15_out, and_7_out, _6);
  and and_16 (and_16_out, and_8_out, _7);
  or or_1 (OUT, and_9_out, and_10_out, and_11_out, and_12_out, and_13_out, and_14_out, and_15_out, and_16_out);

  assign S0_2 = S0;
  assign S1_2 = S1;
  assign S2_2 = S2;
endmodule

module MUX2x1 (
  input  _0,
  input  _1,
  input  S0,
  output S0_2,
  output Out
);

  wire and_1_out, and_2_out;

  and and_1 (and_1_out, ~S0, _0);  // AND_Gate
  and and_2 (and_2_out, S0, _1);
  or or_1 (Out, and_1_out, and_2_out);

  assign S0_2 = S0;
endmodule

module MUX2x2 (
  input  A0,
  input  B0,
  input  A1,
  input  B1,
  input  S0,
  output S0_2,
  output Out0,
  output Out1
);

  wire mux2x1_2_s0_2;

  MUX2x1 mux2x1_1 (._0(A0), ._1(B0), .Out(Out0), .S0_2(S0_2), .S0(mux2x1_2_s0_2));
  MUX2x1 mux2x1_2 (._0(A1), ._1(B1), .Out(Out1), .S0_2(mux2x1_2_s0_2), .S0(S0));
endmodule

module Validador (
  input  K,
  input  PA,
  input  PB,
  input  I,
  input  CA0,
  input  CA1,
  input  CB0,
  input  CB1,
  output L,
  output V
);

  wire _1Hz_out, codigo_digito_1_q0, codigo_digito_1_q1, codigo_digito_2_cl_2, codigo_digito_2_q0,
       codigo_digito_2_q1, comparador_1_x____z, MCLK_out, mux2x2_1_out0, mux2x2_1_out1, mux2x2_2_out0,
       mux2x2_2_out1, mux2x2_2_s0_2, or_1_out, t5_t12_1_t5, t5_t12_1_t12, validador_controlo_1_clrcode,
       validador_controlo_1_inittime, validador_controlo_1_setcode, xor_1_out;

  Codigo___Digito codigo_digito_1 (
    .Cup(PA), .Q0(codigo_digito_1_q0), .Q1(codigo_digito_1_q1), .CL(codigo_digito_2_cl_2));  // open: CL_2
  Codigo___Digito codigo_digito_2 (
    .Cup(PB), .Q0(codigo_digito_2_q0), .Q1(codigo_digito_2_q1), .CL_2(codigo_digito_2_cl_2),
    .CL(validador_controlo_1_clrcode));
  MUX2x2 mux2x2_1 (
    .A0(codigo_digito_1_q0), .B0(codigo_digito_2_q0), .A1(codigo_digito_1_q1), .B1(codigo_digito_2_q1),
    .Out0(mux2x2_1_out0), .Out1(mux2x2_1_out1), .S0(xor_1_out));  // open: S0_2
  xor xor_1 (xor_1_out, I, mux2x2_2_s0_2);
  MUX2x2 mux2x2_2 (
    .A0(CA0), .B0(CB0), .A1(CA1), .B1(CB1), .Out0(mux2x2_2_out0), .Out1(mux2x2_2_out1), .S0_2(mux2x2_2_s0_2),
    .S0(validador_controlo_1_setcode));
  or or_1 (or_1_out, PA, PB);
  Comparador comparador_1 (
    .X0(mux2x2_1_out0), .Z0(mux2x2_2_out0), .X1(mux2x2_1_out1), .Z1(mux2x2_2_out1),
    .X____Z(comparador_1_x____z));
  Clock #(.highDuration(1000), .lowDuration(1000)) _1Hz (.out(_1Hz_out));
  Clock MCLK (.out(MCLK_out));
  T5_T12 t5_t12_1 (.Cup(_1Hz_out), .CL(validador_controlo_1_inittime), .T5(t5_t12_1_t5), .T12(t5_t12_1_t12));
  Validador___Controlo validador_controlo_1 (
    .K(K), .CLK(MCLK_out), .TOpen(t5_t12_1_t5), .TCode(t5_t12_1_t12), .Err(comparador_1_x____z),
    .Start(or_1_out), .InitTime(validador_controlo_1_inittime), .SetCode(validador_controlo_1_setcode),
    .L(L), .V(V), .ClrCode(validador_controlo_1_clrcode));
endmodule

module Comparador (
  input  X0,
  input  Z0,
  input  X1,
  input  Z1,
  output X____Z
);

  wire xor_1_out, xor_2_out;

  xor xor_1 (xor_1_out, X0, Z0);
  xor xor_2 (xor_2_out, X1, Z1);
  or or_1 (X____Z, xor_1_out, xor_2_out);
endmodule

module Contador_2_bits (
  input  CLK,
  input  CE,
  input  PS,
  input  CL,
  output Q0,
  output Q1
);

  wire and_1_out;

  T_Flip_Flop t_ff_1 (.clk(CLK), .T(CE), .Q(Q0), .preset(PS), .reset(CL));  // open: Qn, en
  and and_1 (and_1_out, Q0, CE);
  T_Flip_Flop t_ff_2 (.clk(CLK), .T(and_1_out), .Q(Q1), .preset(PS), .reset(CL));  // open: Qn, en
endmodule

module Codigo___Digito (
  input  Cup,
  input  CL,
  output Q0,
  output Q1,
  output CL_2
);

  Contador_2_bits contador_2_bits_1 (.CLK(Cup), .CE(1'b1), .CL(CL), .Q0(Q0), .Q1(Q1));  // open: PS

  assign CL_2 = CL;
endmodule

module Contador_4_bits (
  input  PS,
  input  CE,
  input  CL,
  input  CL_2,
  output Q2,
  output Q3,
  output Q0,
  output Q1
);

  wire and_1_out;

  Contador_2_bits contador_2_bits_1 (.CLK(CL), .CE(CE), .PS(PS), .CL(CL_2), .Q0(Q0), .Q1(Q1));
  and and_1 (and_1_out, Q0, Q1);
  Contador_2_bits contador_2_bits_2 (.CLK(CL), .CE(and_1_out), .PS(PS), .CL(CL_2), .Q0(Q2), .Q1(Q3));
endmodule

module T5_T12 (
  input  Cup,
  input  CL,
  output T5,
  output T12
);

  wire and_3_out, contador_4_bits_1_q0, contador_4_bits_1_q1, contador_4_bits_1_q2, contador_4_bits_1_q3,
       or_1_out;

  Contador_4_bits contador_4_bits_1 (
    .CE(1'b1), .CL(Cup), .CL_2(or_1_out), .Q0(contador_4_bits_1_q0), .Q2(contador_4_bits_1_q2),
    .Q3(contador_4_bits_1_q3), .Q1(contador_4_bits_1_q1));  // open: PS
  or or_1 (or_1_out, CL, and_3_out);
  and and_1 (T5, ~Cup, ~contador_4_bits_1_q3, contador_4_bits_1_q2, ~contador_4_bits_1_q1, contador_4_bits_1_q0);  // AND_Gate
  and and_2 (T12, ~Cup, contador_4_bits_1_q3, contador_4_bits_1_q2, ~contador_4_bits_1_q1, ~contador_4_bits_1_q0);  // AND_Gate
  and and_3 (and_3_out, ~Cup, contador_4_bits_1_q3, contador_4_bits_1_q2, ~contador_4_bits_1_q1, contador_4_bits_1_q0);  // AND_Gate

  // Notes on the sheet:
  //   T13
endmodule
