// Logisim project D_EDGETRIGGER.circ as structural Verilog: 1 circuit, main circuit D edgetrigger
module D_edgetrigger (
  input  CLK,
  input  D,
  input  AS,
  input  AR,
  output out_5
);

  wire not_1_out, not_2_out;

  not not_1 (not_1_out, AS);
  not not_2 (not_2_out, AR);
  D_Flip_Flop d_ff_1 (.clk(CLK), .D(D), .Q(out_5), .preset(not_1_out), .en(1'b1), .reset(not_2_out));  // open: Qn
endmodule
