// Logisim project Eletronics transistors.circ as structural Verilog: 1 circuit, main circuit main
module main (
  input  in_1,
  input  in_2,
  input  in_3,
  output out_4
);

  wire transistor_3_out, transistor_4_out;

  Transistor transistor_1 (.in(1'b1), .out(out_4), .gate(in_3));
  Transistor #(.\type ("n")) transistor_2 (.in(1'b0), .out(out_4), .gate(in_3));
  Transistor #(.\type ("n")) transistor_3 (.in(1'b0), .out(transistor_3_out), .gate(in_2));
  Transistor transistor_4 (.in(1'b1), .out(transistor_4_out), .gate(in_1));
  // also tied to GND on the sheet: transistor_4_out
  // also tied to VCC on the sheet: transistor_3_out
endmodule
