// Logisim project Flip flops implementation.circ as structural Verilog: 6 circuits, main circuit main
module main (
  input  e,
  input  Enable,
  output out_3,
  output out_4
);

  wire and_1_out, and_2_out, not_1_out;

  not not_1 (not_1_out, e);
  and and_1 (and_1_out, not_1_out, Enable);
  and and_2 (and_2_out, Enable, e);
  nor nor_1 (out_3, and_1_out, out_4);
  nor nor_2 (out_4, out_3, and_2_out);
endmodule

module D_latch (
  input  D,
  input  Enable,
  output out_3,
  output out_4
);

  wire and_1_out, and_2_out, not_1_out;

  not not_1 (not_1_out, D);
  and and_1 (and_1_out, not_1_out, Enable);
  and and_2 (and_2_out, Enable, D);
  nor nor_1 (out_3, and_1_out, out_4);
  nor nor_2 (out_4, out_3, and_2_out);
endmodule

module flip_flop_D_delay (
  input  in_1,
  input  Clock,
  output out_3,
  output out_4
);

  wire d_latch_1_out_3, not_1_out;

  not not_1 (not_1_out, Clock);
  D_latch d_latch_1 (.D(in_1), .Enable(not_1_out), .out_3(d_latch_1_out_3));  // open: out_4
  D_latch d_latch_2 (.D(d_latch_1_out_3), .Enable(Clock), .out_3(out_3), .out_4(out_4));
endmodule

module Set_Reset_latch (
  input  Reset,
  input  Set,
  output out_3,
  output out_4
);

  nor nor_1 (out_3, Reset, out_4);
  nor nor_2 (out_4, out_3, Set);
endmodule

module SR_latch_with_enable (
  input  Reset,
  input  Enable,
  input  Set,
  output out_4,
  output out_5
);

  wire and_1_out, and_2_out;

  and and_1 (and_1_out, Reset, Enable);
  and and_2 (and_2_out, Enable, Set);
  nor nor_1 (out_4, and_1_out, out_5);
  nor nor_2 (out_5, out_4, and_2_out);
endmodule

module Timer_ou_counter (
  input  in_1,
  input  \Count__se_load_é_um_faz_count_down ,
  input  [3:0] in_3,
  input  clock,
  input  Reset
);

  wire counter_1_carry;
  wire [3:0] counter_1_q;

  Counter #(.width(4), .max('hf)) counter_1 (
    .load(in_1), .D(in_3), .count(\Count__se_load_é_um_faz_count_down ), .Q(counter_1_q),
    .carry(counter_1_carry), .clk(clock), .clr(Reset));
endmodule
