// Logisim project MUITAS COISAS.circ as structural Verilog: 24 circuits, main circuit Full Adder
module Full_Adder (
  input  Cn,
  input  An,
  input  Bn,
  output Sn,
  output Cn_1
);

  wire and_1_out, and_2_out, and_3_out, xor_1_out;

  xor xor_1 (xor_1_out, An, Bn);
  and and_1 (and_1_out, Bn, An);
  and and_2 (and_2_out, Bn, Cn);
  and and_3 (and_3_out, Cn, An);
  or or_1 (Cn_1, and_1_out, and_2_out, and_3_out);
  xor xor_2 (Sn, Cn, xor_1_out);
endmodule

module _4bit_Full_Adder (
  input  C0,
  input  A0,
  input  A1,
  input  A2,
  input  A3,
  input  B0,
  input  B1,
  input  B2,
  input  B3,
  output S0,
  output S1,
  output S2,
  output S3,
  output C4
);

  wire full_adder_1_cn_1, full_adder_2_cn_1, full_adder_3_cn_1;

  Full_Adder full_adder_1 (.An(A0), .Bn(B0), .Cn(C0), .Sn(S0), .Cn_1(full_adder_1_cn_1));
  Full_Adder full_adder_2 (.An(A1), .Bn(B1), .Cn(full_adder_1_cn_1), .Sn(S1), .Cn_1(full_adder_2_cn_1));
  Full_Adder full_adder_3 (.An(A2), .Bn(B2), .Cn(full_adder_2_cn_1), .Sn(S2), .Cn_1(full_adder_3_cn_1));
  Full_Adder full_adder_4 (.An(A3), .Bn(B3), .Cn(full_adder_3_cn_1), .Sn(S3), .Cn_1(C4));
endmodule

module Full_Subtractor (
  input  BWn_1,
  input  An,
  input  Bn,
  output Sn,
  output BWn
);

  wire and_1_out, and_2_out, and_3_out, xor_1_out;

  xor xor_1 (xor_1_out, An, Bn);
  and and_1 (and_1_out, Bn, ~An);  // AND_Gate
  and and_2 (and_2_out, Bn, BWn_1);
  and and_3 (and_3_out, BWn_1, ~An);  // AND_Gate
  or or_1 (BWn, and_1_out, and_2_out, and_3_out);
  xor xor_2 (Sn, BWn_1, xor_1_out);
endmodule

module MUX_2x1 (
  input  I0,
  input  I1,
  input  S,
  output out_4,
  output Y
);

  wire and_1_out, and_2_out;

  and and_1 (and_1_out, I0, ~S);  // AND_Gate
  and and_2 (and_2_out, I1, S);
  or or_1 (Y, and_1_out, and_2_out);

  assign out_4 = S;
endmodule

module MUX_4x1 (
  input  I0,
  input  I1,
  input  I2,
  input  I3,
  input  S0,
  input  S1,
  output out_7,
  output out_8,
  output Y
);

  wire and_1_out, and_2_out, and_3_out, and_4_out;

  and and_1 (and_1_out, I0, ~S0, ~S1);  // AND_Gate
  and and_2 (and_2_out, I1, S0, ~S1);  // AND_Gate
  and and_3 (and_3_out, I2, ~S0, S1);  // AND_Gate
  and and_4 (and_4_out, I3, S0, S1);
  or or_1 (Y, and_1_out, and_2_out, and_3_out, and_4_out);

  assign out_7 = S0;
  assign out_8 = S1;
endmodule

module MUX_8x1 (
  input  I0,
  input  I1,
  input  I2,
  input  I3,
  input  I4,
  input  I5,
  input  I6,
  input  I7,
  input  S0,
  input  S1,
  input  S2,
  output out_12,
  output out_13,
  output out_14,
  output Y
);

  wire and_1_out, and_2_out, and_3_out, and_4_out, and_5_out, and_6_out, and_7_out, and_8_out;

  and and_1 (and_1_out, I0, ~S0, ~S1, ~S2);  // AND_Gate
  and and_2 (and_2_out, I1, S0, ~S1, ~S2);  // AND_Gate
  and and_3 (and_3_out, I2, ~S0, S1, ~S2);  // AND_Gate
  and and_4 (and_4_out, I3, S0, S1, ~S2);  // AND_Gate
  and and_5 (and_5_out, I4, ~S0, ~S1, S2);  // AND_Gate
  and and_6 (and_6_out, I5, S0, ~S1, S2);  // AND_Gate
  and and_7 (and_7_out, I6, ~S0, S1, S2);  // AND_Gate
  and and_8 (and_8_out, I7, S0, S1, S2);
  or or_1 (Y, and_1_out, and_2_out, and_3_out, and_4_out, and_5_out, and_6_out, and_7_out, and_8_out);

  assign out_12 = S0;
  assign out_13 = S1;
  assign out_14 = S2;
endmodule

module MUX_16x4 (
  input  I00,
  input  I01,
  input  I02,
  input  I03,
  input  I10,
  input  I11,
  input  I12,
  input  I13,
  input  I20,
  input  I21,
  input  I22,
  input  I23,
  input  I30,
  input  I31,
  input  I32,
  input  I33,
  input  S0,
  input  S1,
  output out_19,
  output out_20,
  output out_21,
  output out_22,
  output out_23,
  output out_24
);

  wire mux_4x1_2_out_7, mux_4x1_2_out_8, mux_4x1_3_out_7, mux_4x1_3_out_8, mux_4x1_4_out_7, mux_4x1_4_out_8;

  MUX_4x1 mux_4x1_1 (
    .I0(I00), .I1(I01), .I2(I02), .I3(I03), .S0(mux_4x1_2_out_7), .S1(mux_4x1_2_out_8), .Y(out_21),
    .out_7(out_19), .out_8(out_20));
  MUX_4x1 mux_4x1_2 (
    .I0(I10), .I1(I11), .I2(I12), .I3(I13), .S0(mux_4x1_3_out_7), .S1(mux_4x1_3_out_8), .Y(out_22),
    .out_7(mux_4x1_2_out_7), .out_8(mux_4x1_2_out_8));
  MUX_4x1 mux_4x1_3 (
    .I0(I20), .I1(I21), .I2(I22), .I3(I23), .S0(mux_4x1_4_out_7), .S1(mux_4x1_4_out_8), .Y(out_23),
    .out_7(mux_4x1_3_out_7), .out_8(mux_4x1_3_out_8));
  MUX_4x1 mux_4x1_4 (
    .I0(I30), .I1(I31), .I2(I32), .I3(I33), .S0(S0), .S1(S1), .Y(out_24), .out_7(mux_4x1_4_out_7),
    .out_8(mux_4x1_4_out_8));
endmodule

// DEC
module DEC_2x4__DECODER (
  input  S0,
  input  S1,
  output D0,
  output D1,
  output D2,
  output D3
);

  and and_1 (D0, ~S0, ~S1);  // AND_Gate
  and and_2 (D1, S0, ~S1);  // AND_Gate
  and and_3 (D2, ~S0, S1);  // AND_Gate
  and and_4 (D3, S0, S1);
endmodule

// DECODER
module DEC_3x8 (
  input  S0,
  input  S1,
  input  S2,
  output D0,
  output D1,
  output D2,
  output D3,
  output D4,
  output D5,
  output D6,
  output D7
);

  and and_1 (D0, ~S0, ~S2, ~S1);  // AND_Gate
  and and_2 (D1, S0, ~S1, ~S2);  // AND_Gate
  and and_3 (D2, ~S0, S1, ~S2);  // AND_Gate
  and and_4 (D3, S0, S1, ~S2);  // AND_Gate
  and and_5 (D4, ~S0, ~S1, S2);  // AND_Gate
  and and_6 (D5, S0, ~S1, S2);  // AND_Gate
  and and_7 (D6, ~S0, S1, S2);  // AND_Gate
  and and_8 (D7, S0, S1, S2);
endmodule

module Flip_Flop_SR (
  input  S,
  input  R,
  output Q,
  output nQ
);

  wire not_1_out, not_2_out;

  not not_1 (not_1_out, S);
  not not_2 (not_2_out, R);
  nand nand_1 (Q, not_1_out, nQ);
  nand nand_2 (nQ, Q, not_2_out);

  // Notes on the sheet:
  //   Flip-Flop SR
endmodule

module Flip_Flop_D_Latch__Preset_e_Clear (
  input  SET,
  input  D,
  input  E,
  input  CLEAR,
  output Q,
  output nQ
);

  wire and_1_out, and_2_out, and_3_out, and_4_out, and_5_out, not_1_out, or_1_out, or_2_out;

  not not_1 (not_1_out, D);
  and and_1 (and_1_out, D, E);
  and and_2 (and_2_out, E, not_1_out);
  and and_3 (and_3_out, SET, ~CLEAR);  // AND_Gate
  and and_4 (and_4_out, and_1_out, ~CLEAR);  // AND_Gate
  and and_5 (and_5_out, ~SET, and_2_out);  // AND_Gate
  or or_1 (or_1_out, and_3_out, and_4_out);
  or or_2 (or_2_out, and_5_out, CLEAR);
  Flip_Flop_SR ff_sr_1 (.S(or_1_out), .R(or_2_out), .Q(Q), .nQ(nQ));

  // Notes on the sheet:
  //   Flip-Flop D Latch, Preset e Clear
endmodule

module Flip_Flop_D_Edge_Trigger__Preset_e_Clear (
  input  SET,
  input  D,
  input  CLK,
  input  CLR,
  output Q,
  output Q_2
);

  wire ff_d_latch_preset_e_clear_1_q, not_1_out;

  not not_1 (not_1_out, CLK);
  Flip_Flop_D_Latch__Preset_e_Clear ff_d_latch_preset_e_clear_1 (
    .SET(SET), .D(D), .E(not_1_out), .CLEAR(CLR), .Q(ff_d_latch_preset_e_clear_1_q));  // open: nQ
  Flip_Flop_D_Latch__Preset_e_Clear ff_d_latch_preset_e_clear_2 (
    .SET(SET), .D(ff_d_latch_preset_e_clear_1_q), .E(CLK), .CLEAR(CLR), .Q(Q), .nQ(Q_2));

  // Notes on the sheet:
  //   Flip-Flop D Edge Trigger com Preset e Clear
endmodule

module Flip_Flop_T_Edge_Trigger__Preset_e_Clear (
  input  SET,
  input  T,
  input  CLK,
  input  CLR,
  output Q,
  output Q_2
);

  wire xor_1_out;

  xor xor_1 (xor_1_out, Q, T);
  Flip_Flop_D_Edge_Trigger__Preset_e_Clear ff_d_edge_trigger_preset_e_clear_1 (
    .SET(SET), .D(xor_1_out), .CLK(CLK), .CLR(CLR), .Q(Q), .Q_2(Q_2));

  // Notes on the sheet:
  //   Flip-Flop T Edge Trigger com Preset e Clear
endmodule

module Counter_Up_3_bits__D (
  input  CE,
  input  Clear,
  output TC,
  output Q0,
  output Q1,
  output Q2
);

  wire and_1_out, and_2_out, button_1_out, xor_1_out, xor_2_out, xor_3_out;

  Button button_1 (.out(button_1_out));
  xor xor_1 (xor_1_out, Q0, CE);
  Flip_Flop_D_Edge_Trigger__Preset_e_Clear ff_d_edge_trigger_preset_e_clear_1 (
    .SET(1'b0), .D(xor_1_out), .CLK(button_1_out), .CLR(Clear), .Q(Q0));  // open: Q_2
  and and_1 (and_1_out, CE, Q0);
  xor xor_2 (xor_2_out, Q1, and_1_out);
  Flip_Flop_D_Edge_Trigger__Preset_e_Clear ff_d_edge_trigger_preset_e_clear_2 (
    .SET(1'b0), .D(xor_2_out), .CLK(button_1_out), .CLR(Clear), .Q(Q1));  // open: Q_2
  and and_2 (and_2_out, and_1_out, Q1);
  xor xor_3 (xor_3_out, Q2, and_2_out);
  Flip_Flop_D_Edge_Trigger__Preset_e_Clear ff_d_edge_trigger_preset_e_clear_3 (
    .SET(1'b0), .D(xor_3_out), .CLK(button_1_out), .CLR(Clear), .Q(Q2));  // open: Q_2
  and and_3 (TC, Q2, Q1, Q0);

  // Notes on the sheet:
  //   Contador Up 3 bits
endmodule

module Counter_Down_3_bits__D (
  input  CE,
  input  MCLK,
  input  Clear,
  output TC,
  output Q1,
  output Q2,
  output Q0
);

  wire and_1_out, and_2_out, ff_d_edge_trigger_preset_e_clear_1_q_2, ff_d_edge_trigger_preset_e_clear_2_q_2,
       xor_1_out, xor_2_out, xor_3_out;

  xor xor_1 (xor_1_out, Q0, CE);
  Flip_Flop_D_Edge_Trigger__Preset_e_Clear ff_d_edge_trigger_preset_e_clear_1 (
    .SET(1'b0), .D(xor_1_out), .CLK(MCLK), .CLR(Clear), .Q(Q0), .Q_2(ff_d_edge_trigger_preset_e_clear_1_q_2));
  and and_1 (and_1_out, CE, ff_d_edge_trigger_preset_e_clear_1_q_2);
  xor xor_2 (xor_2_out, Q1, and_1_out);
  Flip_Flop_D_Edge_Trigger__Preset_e_Clear ff_d_edge_trigger_preset_e_clear_2 (
    .SET(1'b0), .D(xor_2_out), .CLK(MCLK), .CLR(Clear), .Q(Q1), .Q_2(ff_d_edge_trigger_preset_e_clear_2_q_2));
  and and_2 (and_2_out, and_1_out, ff_d_edge_trigger_preset_e_clear_2_q_2);
  xor xor_3 (xor_3_out, Q2, and_2_out);
  Flip_Flop_D_Edge_Trigger__Preset_e_Clear ff_d_edge_trigger_preset_e_clear_3 (
    .SET(1'b0), .D(xor_3_out), .CLK(MCLK), .CLR(Clear), .Q(Q2));  // open: Q_2
  and and_3 (TC, Q2, Q1, Q0);

  // Notes on the sheet:
  //   Contador Down 3 bits
endmodule

module Counter_Up_Down_3_bits__D (
  input  CE,
  input  MCLK,
  input  Clear,
  input  DnU,
  output MIN,
  output MAX,
  output Q0,
  output Q1,
  output Q2
);

  wire and_1_out, and_2_out, ff_d_edge_trigger_preset_e_clear_1_q_2, ff_d_edge_trigger_preset_e_clear_2_q_2,
       mux_2x1_1_y, mux_2x1_2_y, xor_1_out, xor_2_out, xor_3_out;

  xor xor_1 (xor_1_out, Q0, CE);
  Flip_Flop_D_Edge_Trigger__Preset_e_Clear ff_d_edge_trigger_preset_e_clear_1 (
    .SET(1'b0), .D(xor_1_out), .CLK(MCLK), .CLR(Clear), .Q(Q0), .Q_2(ff_d_edge_trigger_preset_e_clear_1_q_2));
  MUX_2x1 mux_2x1_1 (.I0(Q0), .I1(ff_d_edge_trigger_preset_e_clear_1_q_2), .S(DnU), .Y(mux_2x1_1_y));  // open: out_4
  and and_1 (and_1_out, CE, mux_2x1_1_y);
  xor xor_2 (xor_2_out, Q1, and_1_out);
  Flip_Flop_D_Edge_Trigger__Preset_e_Clear ff_d_edge_trigger_preset_e_clear_2 (
    .SET(1'b0), .D(xor_2_out), .CLK(MCLK), .CLR(Clear), .Q(Q1), .Q_2(ff_d_edge_trigger_preset_e_clear_2_q_2));
  MUX_2x1 mux_2x1_2 (.I0(Q1), .I1(ff_d_edge_trigger_preset_e_clear_2_q_2), .S(DnU), .Y(mux_2x1_2_y));  // open: out_4
  and and_2 (and_2_out, and_1_out, mux_2x1_2_y);
  xor xor_3 (xor_3_out, Q2, and_2_out);
  Flip_Flop_D_Edge_Trigger__Preset_e_Clear ff_d_edge_trigger_preset_e_clear_3 (
    .SET(1'b0), .D(xor_3_out), .CLK(MCLK), .CLR(Clear), .Q(Q2));  // open: Q_2
  and and_3 (MIN, ~Q2, ~Q1, ~Q0, DnU);  // AND_Gate
  and and_4 (MAX, Q2, Q1, Q0, ~DnU);  // AND_Gate

  // Notes on the sheet:
  //   Contador Up/Down 3 bits
endmodule

module Counter_Up_3_bits_com_PL_Async (
  input  P0,
  input  P1,
  input  P2,
  input  PL,
  input  CE,
  input  MCLK,
  input  Clear,
  output TC,
  output Q0,
  output Q1,
  output Q2
);

  wire and_1_out, and_2_out, and_3_out, and_4_out, and_5_out, and_6_out, and_7_out, and_8_out, or_1_out,
       or_2_out, or_3_out, xor_1_out, xor_2_out, xor_3_out;

  and and_1 (and_1_out, PL, ~P0);  // AND_Gate
  and and_2 (and_2_out, PL, P0);
  xor xor_1 (xor_1_out, Q0, CE);
  or or_1 (or_1_out, and_1_out, Clear);
  Flip_Flop_D_Edge_Trigger__Preset_e_Clear ff_d_edge_trigger_preset_e_clear_1 (
    .SET(and_2_out), .D(xor_1_out), .CLK(MCLK), .CLR(or_1_out), .Q(Q0));  // open: Q_2
  and and_3 (and_3_out, CE, Q0);
  and and_4 (and_4_out, PL, ~P1);  // AND_Gate
  and and_5 (and_5_out, PL, P1);
  xor xor_2 (xor_2_out, Q1, and_3_out);
  or or_2 (or_2_out, and_4_out, Clear);
  Flip_Flop_D_Edge_Trigger__Preset_e_Clear ff_d_edge_trigger_preset_e_clear_2 (
    .SET(and_5_out), .D(xor_2_out), .CLK(MCLK), .CLR(or_2_out), .Q(Q1));  // open: Q_2
  and and_6 (and_6_out, and_3_out, Q1);
  and and_7 (and_7_out, PL, ~P2);  // AND_Gate
  and and_8 (and_8_out, PL, P2);
  xor xor_3 (xor_3_out, Q2, and_6_out);
  or or_3 (or_3_out, and_7_out, Clear);
  Flip_Flop_D_Edge_Trigger__Preset_e_Clear ff_d_edge_trigger_preset_e_clear_3 (
    .SET(and_8_out), .D(xor_3_out), .CLK(MCLK), .CLR(or_3_out), .Q(Q2));  // open: Q_2
  and and_9 (TC, Q2, Q1, Q0);

  // Notes on the sheet:
  //   Contador Up 3 bits com PL(Async)
endmodule

module Counter_Up_3_bits_com_PL_Sync (
  input  P0,
  input  P1,
  input  P2,
  input  CE,
  input  MCLK,
  input  Clear,
  input  PL,
  output TC,
  output Q0,
  output Q1,
  output Q2
);

  wire and_1_out, and_2_out, mux_2x1_1_y, mux_2x1_2_y, mux_2x1_3_y, xor_1_out, xor_2_out, xor_3_out;

  MUX_2x1 mux_2x1_1 (.I0(xor_1_out), .I1(P0), .S(PL), .Y(mux_2x1_1_y));  // open: out_4
  xor xor_1 (xor_1_out, Q0, CE);
  Flip_Flop_D_Edge_Trigger__Preset_e_Clear ff_d_edge_trigger_preset_e_clear_1 (
    .SET(1'b0), .D(mux_2x1_1_y), .CLK(MCLK), .CLR(Clear), .Q(Q0));  // open: Q_2
  and and_1 (and_1_out, CE, Q0);
  xor xor_2 (xor_2_out, Q1, and_1_out);
  MUX_2x1 mux_2x1_2 (.I0(xor_2_out), .I1(P1), .S(PL), .Y(mux_2x1_2_y));  // open: out_4
  Flip_Flop_D_Edge_Trigger__Preset_e_Clear ff_d_edge_trigger_preset_e_clear_2 (
    .SET(1'b0), .D(mux_2x1_2_y), .CLK(MCLK), .CLR(Clear), .Q(Q1));  // open: Q_2
  and and_2 (and_2_out, and_1_out, Q1);
  MUX_2x1 mux_2x1_3 (.I0(xor_3_out), .I1(P2), .S(PL), .Y(mux_2x1_3_y));  // open: out_4
  xor xor_3 (xor_3_out, Q2, and_2_out);
  Flip_Flop_D_Edge_Trigger__Preset_e_Clear ff_d_edge_trigger_preset_e_clear_3 (
    .SET(1'b0), .D(mux_2x1_3_y), .CLK(MCLK), .CLR(Clear), .Q(Q2));  // open: Q_2
  and and_3 (TC, Q2, Q1, Q0);

  // Notes on the sheet:
  //   Contador Up 3 bits com PL(Sync)
endmodule

module Counter_Up_4_bits__T (
  input  CE,
  input  MCLK,
  input  Clear,
  output TC,
  output Q0,
  output Q1,
  output Q2,
  output Q3
);

  wire and_1_out, and_2_out, and_3_out;

  Flip_Flop_T_Edge_Trigger__Preset_e_Clear ff_t_edge_trigger_preset_e_clear_1 (
    .SET(1'b0), .T(CE), .CLK(MCLK), .CLR(Clear), .Q(Q0));  // open: Q_2
  and and_1 (and_1_out, CE, Q0);
  Flip_Flop_T_Edge_Trigger__Preset_e_Clear ff_t_edge_trigger_preset_e_clear_2 (
    .SET(1'b0), .T(and_1_out), .CLK(MCLK), .CLR(Clear), .Q(Q1));  // open: Q_2
  and and_2 (and_2_out, and_1_out, Q1);
  Flip_Flop_T_Edge_Trigger__Preset_e_Clear ff_t_edge_trigger_preset_e_clear_3 (
    .SET(1'b0), .T(and_2_out), .CLK(MCLK), .CLR(Clear), .Q(Q2));  // open: Q_2
  and and_3 (and_3_out, and_2_out, Q2);
  Flip_Flop_T_Edge_Trigger__Preset_e_Clear ff_t_edge_trigger_preset_e_clear_4 (
    .SET(1'b0), .T(and_3_out), .CLK(MCLK), .CLR(Clear), .Q(Q3));  // open: Q_2
  and and_4 (TC, Q3, Q2, Q1, Q0);

  // Notes on the sheet:
  //   Contador Up 4 bits
endmodule

module Counter_Up_Down_3_bits__Sync (
  input  P0,
  input  P1,
  input  P2,
  input  CE,
  input  MCLK,
  input  Clear,
  input  PL,
  input  DnU,
  output TC,
  output Q0,
  output Q1,
  output Q2
);

  wire and_1_out, and_2_out, ff_d_edge_trigger_preset_e_clear_1_q_2, ff_d_edge_trigger_preset_e_clear_2_q_2,
       mux_2x1_1_y, mux_2x1_2_y, mux_2x1_3_y, mux_2x1_4_y, mux_2x1_5_y, xor_1_out, xor_2_out, xor_3_out;

  xor xor_1 (xor_1_out, Q0, CE);
  MUX_2x1 mux_2x1_1 (.I0(xor_1_out), .I1(P0), .S(PL), .Y(mux_2x1_1_y));  // open: out_4
  Flip_Flop_D_Edge_Trigger__Preset_e_Clear ff_d_edge_trigger_preset_e_clear_1 (
    .SET(1'b0), .D(mux_2x1_1_y), .CLK(MCLK), .CLR(Clear), .Q(Q0), .Q_2(ff_d_edge_trigger_preset_e_clear_1_q_2));
  and and_1 (and_1_out, CE, mux_2x1_2_y);
  MUX_2x1 mux_2x1_2 (.I0(Q0), .I1(ff_d_edge_trigger_preset_e_clear_1_q_2), .S(DnU), .Y(mux_2x1_2_y));  // open: out_4
  xor xor_2 (xor_2_out, Q1, and_1_out);
  MUX_2x1 mux_2x1_3 (.I0(xor_2_out), .I1(P1), .S(PL), .Y(mux_2x1_3_y));  // open: out_4
  Flip_Flop_D_Edge_Trigger__Preset_e_Clear ff_d_edge_trigger_preset_e_clear_2 (
    .SET(1'b0), .D(mux_2x1_3_y), .CLK(MCLK), .CLR(Clear), .Q(Q1), .Q_2(ff_d_edge_trigger_preset_e_clear_2_q_2));
  and and_2 (and_2_out, and_1_out, mux_2x1_4_y);
  MUX_2x1 mux_2x1_4 (.I0(Q1), .I1(ff_d_edge_trigger_preset_e_clear_2_q_2), .S(DnU), .Y(mux_2x1_4_y));  // open: out_4
  xor xor_3 (xor_3_out, Q2, and_2_out);
  MUX_2x1 mux_2x1_5 (.I0(xor_3_out), .I1(P2), .S(PL), .Y(mux_2x1_5_y));  // open: out_4
  Flip_Flop_D_Edge_Trigger__Preset_e_Clear ff_d_edge_trigger_preset_e_clear_3 (
    .SET(1'b0), .D(mux_2x1_5_y), .CLK(MCLK), .CLR(Clear), .Q(Q2));  // open: Q_2
  and and_3 (TC, Q2, Q1, Q0);

  // Notes on the sheet:
  //   Contador Up/Down 3 bits com PL(Sync)
endmodule

module Shift_Register (
  input  in_1,
  input  in_2,
  input  in_3,
  input  in_4,
  input  SIN,
  input  LDnSH,
  input  CLK,
  input  CLR,
  output SOUT,
  output out_10,
  output out_11,
  output out_12,
  output out_13
);

  wire mux_2x1_1_y, mux_2x1_2_y, mux_2x1_3_y, mux_2x1_4_y;

  MUX_2x1 mux_2x1_1 (.I0(SIN), .I1(in_1), .S(LDnSH), .Y(mux_2x1_1_y));  // open: out_4
  Flip_Flop_D_Edge_Trigger__Preset_e_Clear ff_d_edge_trigger_preset_e_clear_1 (
    .SET(1'b0), .D(mux_2x1_1_y), .CLK(CLK), .CLR(CLR), .Q(out_10));  // open: Q_2
  MUX_2x1 mux_2x1_2 (.I0(out_10), .I1(in_2), .S(LDnSH), .Y(mux_2x1_2_y));  // open: out_4
  Flip_Flop_D_Edge_Trigger__Preset_e_Clear ff_d_edge_trigger_preset_e_clear_2 (
    .SET(1'b0), .D(mux_2x1_2_y), .CLK(CLK), .CLR(CLR), .Q(out_11));  // open: Q_2
  MUX_2x1 mux_2x1_3 (.I0(out_11), .I1(in_3), .S(LDnSH), .Y(mux_2x1_3_y));  // open: out_4
  Flip_Flop_D_Edge_Trigger__Preset_e_Clear ff_d_edge_trigger_preset_e_clear_3 (
    .SET(1'b0), .D(mux_2x1_3_y), .CLK(CLK), .CLR(CLR), .Q(out_12));  // open: Q_2
  MUX_2x1 mux_2x1_4 (.I0(out_12), .I1(in_4), .S(LDnSH), .Y(mux_2x1_4_y));  // open: out_4
  Flip_Flop_D_Edge_Trigger__Preset_e_Clear ff_d_edge_trigger_preset_e_clear_4 (
    .SET(1'b0), .D(mux_2x1_4_y), .CLK(CLK), .CLR(CLR), .Q(out_13));  // open: Q_2

  assign SOUT = out_13;
endmodule

module Greater_or_equal (
  input  A,
  input  B,
  output A_B,
  output A_B_2,
  output A_B_3
);

  wire xor_1_out;

  and and_1 (A_B, A, ~B);  // AND_Gate
  xor xor_1 (xor_1_out, A, B);
  and and_2 (A_B_3, ~A, B);  // AND_Gate
  not not_1 (A_B_2, xor_1_out);
endmodule

module GE_2 (
  input  A,
  input  B,
  output A_B
);

  and and_1 (A_B, A, ~B);  // AND_Gate
endmodule

module GE_3 (
  input  a,
  input  b,
  input  a_2,
  input  b_2,
  input  a_3,
  input  b_3
);

  wire ge_2_1_a_b, ge_2_2_a_b, ge_2_3_a_b;

  GE_2 ge_2_1 (.A(a), .B(b), .A_B(ge_2_1_a_b));
  GE_2 ge_2_2 (.A(a_2), .B(b_2), .A_B(ge_2_2_a_b));
  GE_2 ge_2_3 (.A(a_3), .B(b_3), .A_B(ge_2_3_a_b));
endmodule
