// Logisim project SOMADOR 44873.circ as structural Verilog: 9 circuits, main circuit SomadorSubtrator
module main (
  input  CyIn,
  input  A0,
  input  A1,
  input  A2,
  input  A3,
  input  B0,
  input  B1,
  input  B2,
  input  B3,
  input  SnA,
  output S0,
  output S1,
  output S2,
  output S3,
  output CyBw_overflow_dos_naturais,
  output overflow__com_sinal
);

  // SomadorSubtrator somadorsubtrator_1: pin names not known; wires that end beside it: A0, A1, A2, A3, B0, B1, B2, B3, SnA, CyIn, S0, S1, S2, S3, CyBw_overflow_dos_naturais, overflow__com_sinal
endmodule

module SomadorSubtrator (
  input  CyIn,
  input  A0,
  input  A1,
  input  A2,
  input  A3,
  input  B0,
  input  B1,
  input  B2,
  input  B3,
  input  SnA,
  output S0,
  output S1,
  output S2,
  output S3,
  output Overflow,
  output CyBw_overflow_dos_naturais
);

  wire b_trs_1_b0_trs, b_trs_1_b1_trs, b_trs_1_b2_trs, b_trs_1_b3_trs, cybw_trs_1_c0, somador_1_c3,
       somador_1_cyout;

  CyBw__TRS cybw_trs_1 (.CyIn(CyIn), .C0(cybw_trs_1_c0), .S(SnA));
  B__TRS b_trs_1 (
    .B0(B0), .B1(B1), .B2(B2), .B3(B3), .B0_TRS(b_trs_1_b0_trs), .B1_TRS(b_trs_1_b1_trs),
    .B2_TRS(b_trs_1_b2_trs), .B3_TRS(b_trs_1_b3_trs), .in_5(SnA));
  Somador somador_1 (
    .Cyn(cybw_trs_1_c0), .A0(A0), .B0(b_trs_1_b0_trs), .A0_2(A1), .in_5(b_trs_1_b1_trs), .in_6(A2),
    .in_7(b_trs_1_b2_trs), .S0(S0), .S1(S1), .S2(S2), .CyOut(somador_1_cyout), .in_8(A3),
    .in_9(b_trs_1_b3_trs), .S3(S3), .C3(somador_1_c3));
  xor xor_1 (Overflow, somador_1_c3, somador_1_cyout);
  CyBwOut__TRS cybwout_trs_1 (.SnA(somador_1_cyout), .C4(SnA), .CyBw_overflow_dos_naturais(CyBw_overflow_dos_naturais));

  // Notes on the sheet:
  //   Naturais: 0 a 15
  //   Com sinal: -8 a +7
endmodule

module Soma (
  input  A,
  input  B,
  input  CyIn,
  output Soma,
  output CyOut
);

  wire and_1_out, and_2_out, and_3_out;

  xor xor_1 (Soma, A, B, CyIn);
  and and_1 (and_1_out, A, B);
  or or_1 (CyOut, and_1_out, and_2_out, and_3_out);
  and and_2 (and_2_out, A, CyIn);
  and and_3 (and_3_out, B, CyIn);
endmodule

// +
module Somador (
  input  Cyn,
  input  A0,
  input  B0,
  input  A0_2,
  input  in_5,
  input  in_6,
  input  in_7,
  input  in_8,
  input  in_9,
  output S0,
  output S1,
  output S2,
  output C3,
  output S3,
  output CyOut
);

  wire soma_1_cyout, soma_2_cyout;

  Soma soma_1 (.A(A0), .B(B0), .CyIn(Cyn), .Soma(S0), .CyOut(soma_1_cyout));
  Soma soma_2 (.A(A0_2), .B(in_5), .CyIn(soma_1_cyout), .Soma(S1), .CyOut(soma_2_cyout));
  Soma soma_3 (.A(in_6), .B(in_7), .CyIn(soma_2_cyout), .Soma(S2), .CyOut(C3));
  Soma soma_4 (.A(in_8), .B(in_9), .CyIn(C3), .Soma(S3), .CyOut(CyOut));
endmodule

module B__TRS (
  input  B0,
  input  B1,
  input  B2,
  input  B3,
  input  in_5,
  output B0_TRS,
  output B1_TRS,
  output B2_TRS,
  output B3_TRS
);

  xor xor_1 (B0_TRS, B0, in_5);
  xor xor_2 (B1_TRS, B1, in_5);
  xor xor_3 (B2_TRS, B2, in_5);
  xor xor_4 (B3_TRS, B3, in_5);
endmodule

module MUX2X1 (
  input  In0,
  input  In1,
  input  S0,
  output Out
);

  wire and_1_out, and_2_out;

  and and_1 (and_1_out, In0, ~S0);  // AND_Gate
  and and_2 (and_2_out, In1, S0);
  or or_1 (Out, and_1_out, and_2_out);
endmodule

module CyBw__TRS (
  input  CyIn,
  input  S,
  output C0
);

  wire not_1_out;

  not not_1 (not_1_out, CyIn);
  MUX2X1 mux2x1_1 (.In0(CyIn), .In1(not_1_out), .Out(C0), .S0(S));
endmodule

module CyBwOut__TRS (
  input  SnA,
  input  C4,
  output CyBw_overflow_dos_naturais
);

  xor xor_1 (CyBw_overflow_dos_naturais, SnA, C4);
endmodule

module Overflow_alternativo (
  input  A3,
  input  B3,
  input  S3,
  output Overflow
);

  wire and_1_out, and_2_out;

  and and_1 (and_1_out, A3, B3, ~S3);  // AND_Gate
  and and_2 (and_2_out, ~B3, ~A3, S3);  // AND_Gate
  or or_1 (Overflow, and_1_out, and_2_out);
endmodule
