// Logisim project Somador-Subtrator_2.circ as structural Verilog: 8 circuits, main circuit main
module main (
  input  in_1,
  input  in_2,
  input  in_3,
  input  in_4,
  input  in_5,
  input  in_6,
  input  in_7,
  input  in_8,
  input  in_9,
  input  in_10,
  output out_11,
  output out_12,
  output out_13,
  output out_14,
  output out_15,
  output out_16
);

  // Somador_Subtrator_ALU somador_subtrator_alu_1: pin names not known; wires that end beside it: in_1, in_2, in_3, in_4, in_5, in_6, in_7, in_8, in_9, in_10, out_11, out_12, out_13, out_14, out_15, out_16
endmodule

module Half_Adder (
  input  a,
  input  b,
  output Soma,
  output Carry
);

  xor xor_1 (Soma, a, b);
  and and_1 (Carry, b, a);
endmodule

module Full_Adder (
  input  a,
  input  b,
  input  Carry_in,
  output Soma,
  output Carry_Out
);

  wire half_adder_1_carry, half_adder_1_soma, half_adder_2_carry;

  Half_Adder half_adder_1 (.a(a), .b(b), .Soma(half_adder_1_soma), .Carry(half_adder_1_carry));
  Half_Adder half_adder_2 (.a(half_adder_1_soma), .b(Carry_in), .Soma(Soma), .Carry(half_adder_2_carry));
  or or_1 (Carry_Out, half_adder_2_carry, half_adder_1_carry);
endmodule

module Somador (
  input  C0,
  input  A0,
  input  B0,
  input  A1,
  input  B1,
  input  A2,
  input  B2,
  input  A3,
  input  B3,
  output S0,
  output S1,
  output S2,
  output S3,
  output C4
);

  wire full_adder_1_carry_out, full_adder_2_carry_out, full_adder_3_carry_out;

  Full_Adder full_adder_1 (.a(A0), .b(B0), .Carry_in(C0), .Soma(S0), .Carry_Out(full_adder_1_carry_out));
  Full_Adder full_adder_2 (
    .a(A1), .b(B1), .Carry_in(full_adder_1_carry_out), .Soma(S1), .Carry_Out(full_adder_2_carry_out));
  Full_Adder full_adder_3 (
    .a(A2), .b(B2), .Carry_in(full_adder_2_carry_out), .Soma(S2), .Carry_Out(full_adder_3_carry_out));
  Full_Adder full_adder_4 (.a(A3), .b(B3), .Carry_in(full_adder_3_carry_out), .Soma(S3), .Carry_Out(C4));
endmodule

module Somador_Subtrator_ALU (
  input  CyBwIn,
  input  A0,
  input  A1,
  input  A2,
  input  A3,
  input  B0,
  input  B1,
  input  B2,
  input  B3,
  input  S1,
  input  S0,
  output S0_2,
  output S1_2,
  output S2,
  output S3,
  output CyBwout,
  output Overflow
);

  wire selecionador_de_funcao_1_c0, somador_1_c4, xor_1_out, xor_2_out, xor_3_out, xor_4_out;

  Selecionador_de_Funcao selecionador_de_funcao_1 (.CyBwIn(CyBwIn), .C0(selecionador_de_funcao_1_c0), .S1(S1), .S0(S0));
  xor xor_1 (xor_1_out, B0, S0);
  xor xor_2 (xor_2_out, B1, S0);
  xor xor_3 (xor_3_out, B2, S0);
  xor xor_4 (xor_4_out, B3, S0);
  Somador somador_1 (
    .A0(A0), .B0(xor_1_out), .A1(A1), .B1(xor_2_out), .A2(A2), .B2(xor_3_out), .A3(A3), .B3(xor_4_out),
    .S0(S0_2), .S1(S1_2), .S2(S2), .S3(S3), .C0(selecionador_de_funcao_1_c0), .C4(somador_1_c4));
  xor xor_5 (CyBwout, somador_1_c4, S0);
  OverFlow overflow_1 (.A3(A3), .B3(xor_4_out), .S3(S3), .out_4(Overflow));

  // Notes on the sheet:
  //   0                       0 = Soma normal
  //   0                             1 subtracao
  //   1                              0 carryin(add1)
  //   1                           1 carryout(minus 1)
endmodule

module OverFlow (
  input  A3,
  input  B3,
  input  S3,
  output out_4
);

  wire and_1_out, and_2_out;

  and and_1 (and_1_out, A3, B3, ~S3);  // AND_Gate
  and and_2 (and_2_out, ~A3, ~B3, S3);  // AND_Gate
  or or_1 (out_4, and_1_out, and_2_out);
endmodule

module Mux4x1 (
  input  S0,
  input  S1,
  input  I0,
  input  I1,
  input  I2,
  input  I3,
  output out_7
);

  wire and_1_out, and_2_out, and_3_out, and_4_out;

  and and_1 (and_1_out, ~S0, I0, ~S1);  // AND_Gate
  and and_2 (and_2_out, S0, I1, ~S1);  // AND_Gate
  and and_3 (and_3_out, ~S0, I2, S1);  // AND_Gate
  and and_4 (and_4_out, S0, I3, S1);
  or or_1 (out_7, and_1_out, and_2_out, and_3_out, and_4_out);
endmodule

module Selecionador_de_Funcao (
  input  CyBwIn,
  input  S1,
  input  S0,
  output C0
);

  wire not_1_out;

  not not_1 (not_1_out, CyBwIn);
  Mux4x1 mux4x1_1 (.S0(S0), .S1(S1), .I0(1'b0), .I1(1'b1), .I2(CyBwIn), .I3(not_1_out), .out_7(C0));

  // Notes on the sheet:
  //   soma normal
  //   +1 para subtracao
endmodule
