// Logisim project ALU Grupo 8 44873 44587 44884.circ as structural Verilog: 15 circuits, main circuit main
module main (
  input  CyIn_BwOut,
  input  A0,
  input  A1,
  input  A2,
  input  B0,
  input  B1,
  input  B2,
  input  S0,
  input  S1,
  input  S2,
  output R1,
  output R2,
  output R3,
  output CyOut_BwOut,
  output Zero,
  output Overflow,
  output Greater_or_Equal
);

  ALU alu_1 (
    .A0(A0), .A1(A1), .A2(A2), .B0(B0), .B1(B1), .B2(B2), .CyBwIn(CyIn_BwOut), .Zero(Zero), .R0(R1), .R1(R2),
    .R2(R3), .CyOut_BwOut(CyOut_BwOut), .Overflow(Overflow), .S1(S1), .S0(S0), .S2(S2), .GE(Greater_or_Equal));
endmodule

module UNIDADE_ARITMETICA (
  input  CyIn_BwIn_Inc,
  input  S1,
  input  S0,
  input  A0,
  input  A1,
  input  A2,
  input  B0,
  input  B1,
  input  B2,
  output R0,
  output R1,
  output R2,
  output GreaterOrEqual_Inteiros_com_sinal,
  output CyOut_BwOut,
  output AboveOrEqual_Naturais,
  output Overflow
);

  wire bt_1_out_7, bt_1_out_8, bt_1_out_9, bt_1_s0_2, c0t_1_out_4, somador_1_cyout;

  BT bt_1 (
    .B0(B0), .B1(B1), .B2(B2), .out_7(bt_1_out_7), .out_8(bt_1_out_8), .out_9(bt_1_out_9), .S0_2(bt_1_s0_2),
    .S0(S0), .S1(S1));
  C0T c0t_1 (.Cy_Bw(CyIn_BwIn_Inc), .in_3(S1), .in_2(S0), .out_4(c0t_1_out_4));
  Somador somador_1 (
    .CyIn(c0t_1_out_4), .A0(A0), .B0(bt_1_out_7), .in_4(A1), .in_5(bt_1_out_8), .in_6(A2), .in_7(bt_1_out_9),
    .R0(R0), .out_9(R1), .out_10(R2), .CyOut(somador_1_cyout));
  Overflow overflow_1 (.A3(A2), .B3(bt_1_out_9), .OV(Overflow), .R3(R2));
  xor xor_1 (CyOut_BwOut, somador_1_cyout, bt_1_s0_2);
  not not_1 (AboveOrEqual_Naturais, CyOut_BwOut);
  xor xor_2 (GreaterOrEqual_Inteiros_com_sinal, Overflow, ~R2);  // XOR_Gate

  // Other names for the same wires on the sheet: O = Overflow

  // Notes on the sheet:
  //   0
  //   0  Sum
  //   0
  //   1 Subtra
  //   1
  //   A+Inc
  //   0
  //   1
  //   A-Dec
  //   1
  //   A+B
  //   Quando ha sub nao deve haver cyout
  //   0____7
  //   -3___+4
  //   001 1 +1 -2
  //   ^  logo positivo
  //   111 7  -1 = 8(2^3)-1
endmodule

module Soma (
  input  A,
  input  B,
  input  CyIn,
  output Soma,
  output CyOut
);

  wire and_1_out, and_2_out, and_3_out;

  and and_1 (and_1_out, A, B);
  and and_2 (and_2_out, A, CyIn);
  and and_3 (and_3_out, B, CyIn);
  xor xor_1 (Soma, A, B, CyIn);
  or or_1 (CyOut, and_1_out, and_2_out, and_3_out);
endmodule

module Somador (
  input  CyIn,
  input  A0,
  input  B0,
  input  in_4,
  input  in_5,
  input  in_6,
  input  in_7,
  output R0,
  output out_9,
  output out_10,
  output CyOut
);

  wire soma_1_cyout, soma_2_cyout;

  Soma soma_1 (.A(A0), .B(B0), .CyIn(CyIn), .Soma(R0), .CyOut(soma_1_cyout));
  Soma soma_2 (.A(in_4), .B(in_5), .CyIn(soma_1_cyout), .Soma(out_9), .CyOut(soma_2_cyout));
  Soma soma_3 (.A(in_6), .B(in_7), .CyIn(soma_2_cyout), .Soma(out_10), .CyOut(CyOut));
endmodule

module MUX_4X1 (
  input  in_1,
  input  in_2,
  input  in_3,
  input  in_4,
  input  S1,
  input  S0,
  output out_7,
  output out_8,
  output out_9
);

  wire and_1_out, and_2_out, and_3_out, and_4_out;

  and and_1 (and_1_out, in_1, ~S1, ~S0);  // AND_Gate
  and and_2 (and_2_out, in_2, ~S1, S0);  // AND_Gate
  and and_3 (and_3_out, in_3, S1, ~S0);  // AND_Gate
  and and_4 (and_4_out, in_4, S1, S0);
  or or_1 (out_9, and_1_out, and_2_out, and_3_out, and_4_out);

  assign out_7 = S1;
  assign out_8 = S0;

  // Notes on the sheet:
  //   Usado para 4x3, CondicaodeFuncao E mux 4x3
endmodule

module C0T (
  input  Cy_Bw,
  input  in_2,
  input  in_3,
  output out_4
);

  wire not_1_out;

  not not_1 (not_1_out, Cy_Bw);
  MUX_4X1 mux_4x1_1 (
    .in_1(Cy_Bw), .in_2(not_1_out), .in_3(1'b1), .in_4(1'b0), .out_9(out_4), .S1(in_3), .S0(in_2));  // open: out_7, out_8

  // Notes on the sheet:
  //   Condicao de funcao
endmodule

module BT (
  input  B0,
  input  B1,
  input  B2,
  input  S1,
  input  S0,
  output S0_2,
  output out_7,
  output out_8,
  output out_9
);

  wire and_1_out, and_2_out, and_3_out;

  and and_1 (and_1_out, B0, ~S1);  // AND_Gate
  and and_2 (and_2_out, B1, ~S1);  // AND_Gate
  and and_3 (and_3_out, B2, ~S1);  // AND_Gate
  xor xor_1 (out_7, and_1_out, S0);
  xor xor_2 (out_8, and_2_out, S0);
  xor xor_3 (out_9, and_3_out, S0);

  assign S0_2 = S0;

  // Notes on the sheet:
  //   B Transformation, B for subTraction
  //   A+1 e A-1 nao podem ser afetados pelo B
endmodule

module Overflow (
  input  A3,
  input  B3,
  input  R3,
  output OV
);

  wire and_1_out, and_2_out;

  and and_1 (and_1_out, A3, B3, ~R3);  // AND_Gate
  and and_2 (and_2_out, ~A3, ~B3, R3);  // AND_Gate
  or or_1 (OV, and_1_out, and_2_out);
endmodule

module UNIDADE_LOGICA (
  input  A0,
  input  A1,
  input  A2,
  input  B0,
  input  B1,
  input  B2,
  input  CyBwIn,
  input  S1,
  input  S0,
  output R0,
  output R1,
  output R2,
  output CyOut_BwOut_Logic,
  output Overflow_Logic,
  output S1_2,
  output S0_2
);

  wire and_1_out, and_2_out, and_3_out, aricshiftright_1_carry_bow, aricshiftright_1_r0, aricshiftright_1_r1,
       aricshiftright_1_r2, mux_2x1_1_s0_2, not_1_out, not_2_out, not_3_out, rotatecarryleft_1_cyout,
       rotatecarryleft_1_r0, rotatecarryleft_1_r1, rotatecarryleft_1_r2;

  AricShiftRight aricshiftright_1 (
    .Carry_Bow(aricshiftright_1_carry_bow), .A0(A0), .A1(A1), .R0(aricshiftright_1_r0), .A2(A2),
    .R1(aricshiftright_1_r1), .CyBw(CyBwIn), .R2(aricshiftright_1_r2), .B0(B1), .B1(B0));  // open: OV
  and and_1 (and_1_out, A0, B0);
  and and_2 (and_2_out, A1, B1);
  and and_3 (and_3_out, A2, B2);
  not not_1 (not_1_out, A0);
  not not_2 (not_2_out, A1);
  not not_3 (not_3_out, A2);
  RotateCarryLeft rotatecarryleft_1 (
    .CyIn(CyBwIn), .A0(A0), .A1(A1), .A2(A2), .R0(rotatecarryleft_1_r0), .R1(rotatecarryleft_1_r1),
    .R2(rotatecarryleft_1_r2), .CyOut(rotatecarryleft_1_cyout));
  MUX_4X3 mux_4x3_1 (
    .A0_B0(and_1_out), .nA(not_1_out), .ShiftLeft(rotatecarryleft_1_r0), .ShiftRight(aricshiftright_1_r0),
    .in_5(and_2_out), .in_6(not_2_out), .in_7(rotatecarryleft_1_r1), .in_8(aricshiftright_1_r1),
    .in_9(and_3_out), .in_10(not_3_out), .in_11(rotatecarryleft_1_r2), .in_12(aricshiftright_1_r2), .R(R0),
    .out_16(R1), .out_17(R2), .in_14(S1), .in_13(mux_2x1_1_s0_2));
  MUX_2X1 mux_2x1_1 (
    .A0(rotatecarryleft_1_cyout), .B0(aricshiftright_1_carry_bow), .R0(CyOut_BwOut_Logic),
    .S0_2(mux_2x1_1_s0_2), .S0(S0));

  assign S0_2 = S0;
  assign S1_2 = S1;

  // Notes on the sheet:
  //   A&B
  //   !A
  //   A<<1 
  //   A>>B0-1
endmodule

module MUX_4X3 (
  input  A0_B0,
  input  nA,
  input  ShiftLeft,
  input  ShiftRight,
  input  in_5,
  input  in_6,
  input  in_7,
  input  in_8,
  input  in_9,
  input  in_10,
  input  in_11,
  input  in_12,
  input  in_13,
  input  in_14,
  output R,
  output out_16,
  output out_17
);

  wire mux_4x1_2_out_7, mux_4x1_2_out_8, mux_4x1_3_out_7, mux_4x1_3_out_8;

  MUX_4X1 mux_4x1_1 (
    .in_1(A0_B0), .in_2(nA), .in_3(ShiftLeft), .in_4(ShiftRight), .out_9(R), .S1(mux_4x1_2_out_7),
    .S0(mux_4x1_2_out_8));  // open: out_7, out_8
  MUX_4X1 mux_4x1_2 (
    .in_1(in_5), .in_2(in_6), .in_3(in_7), .in_4(in_8), .out_9(out_16), .out_7(mux_4x1_2_out_7),
    .out_8(mux_4x1_2_out_8), .S1(mux_4x1_3_out_7), .S0(mux_4x1_3_out_8));
  MUX_4X1 mux_4x1_3 (
    .in_1(in_9), .in_2(in_10), .in_3(in_11), .in_4(in_12), .out_9(out_17), .out_7(mux_4x1_3_out_7),
    .out_8(mux_4x1_3_out_8), .S1(in_14), .S0(in_13));

  // Notes on the sheet:
  //   Para o logic/shift
endmodule

module RotateCarryLeft (
  input  CyIn,
  input  A0,
  input  A1,
  input  A2,
  output R0,
  output R1,
  output R2,
  output CyOut
);


  assign CyOut = A2;
  assign R0 = CyIn;
  assign R1 = A0;
  assign R2 = A1;
endmodule

module AricShiftRight (
  input  A0,
  input  A1,
  input  A2,
  input  CyBw,
  input  B0,
  input  B1,
  output Carry_Bow,
  output R0,
  output R1,
  output OV,
  output R2
);

  wire mux_4x1_2_out_7, mux_4x1_2_out_8, mux_4x1_3_out_7, mux_4x1_3_out_8, mux_4x1_4_out_7, mux_4x1_4_out_8;

  MUX_4X1 mux_4x1_1 (
    .in_1(1'b0), .in_2(A0), .in_3(A1), .in_4(A2), .out_9(Carry_Bow), .S1(mux_4x1_2_out_7),
    .S0(mux_4x1_2_out_8));  // open: out_7, out_8
  MUX_4X1 mux_4x1_2 (
    .in_1(A0), .in_2(A1), .in_3(A2), .in_4(CyBw), .out_9(R0), .out_7(mux_4x1_2_out_7),
    .out_8(mux_4x1_2_out_8), .S1(mux_4x1_3_out_7), .S0(mux_4x1_3_out_8));
  MUX_4X1 mux_4x1_3 (
    .in_1(A1), .in_2(A2), .in_3(CyBw), .in_4(CyBw), .out_9(R1), .out_7(mux_4x1_3_out_7),
    .out_8(mux_4x1_3_out_8), .S1(mux_4x1_4_out_7), .S0(mux_4x1_4_out_8));
  MUX_4X1 mux_4x1_4 (
    .in_1(A2), .in_2(CyBw), .in_3(CyBw), .in_4(CyBw), .out_9(R2), .out_7(mux_4x1_4_out_7),
    .out_8(mux_4x1_4_out_8), .S1(B1), .S0(B0));
  xor xor_1 (OV, A2, R2);
endmodule

module MUX_2X1 (
  input  A0,
  input  B0,
  input  S0,
  output S0_2,
  output R0
);

  wire and_1_out, and_2_out;

  and and_1 (and_1_out, ~A0, S0);  // AND_Gate
  and and_2 (and_2_out, B0, S0);
  or or_1 (R0, and_1_out, and_2_out);

  assign S0_2 = S0;

  // Notes on the sheet:
  //   Usado em 2x3, e alternancia de valores a apresentar em logic e alu
endmodule

module MUX_2X3 (
  input  R0_ARITME,
  input  R0_LOGIC,
  input  R1_A,
  input  R1_L,
  input  R2_A,
  input  R2_L,
  input  in_7,
  output out_8,
  output out_9,
  output out_10
);

  wire mux_2x1_2_s0_2, mux_2x1_3_s0_2;

  MUX_2X1 mux_2x1_1 (.A0(R0_ARITME), .B0(R0_LOGIC), .R0(out_8), .S0(mux_2x1_2_s0_2));  // open: S0_2
  MUX_2X1 mux_2x1_2 (.A0(R1_A), .B0(R1_L), .R0(out_9), .S0_2(mux_2x1_2_s0_2), .S0(mux_2x1_3_s0_2));
  MUX_2X1 mux_2x1_3 (.A0(R2_A), .B0(R2_L), .R0(out_10), .S0_2(mux_2x1_3_s0_2), .S0(in_7));

  // Notes on the sheet:
  //   Para ALU, separar logic de aritmetico
endmodule

module ALU (
  input  A0,
  input  A1,
  input  A2,
  input  B0,
  input  B1,
  input  B2,
  input  CyBwIn,
  input  S1,
  input  S0,
  input  S2,
  output Zero,
  output GE,
  output R0,
  output R1,
  output R2,
  output CyOut_BwOut,
  output Overflow
);

  wire mux_2x1_1_s0_2, mux_2x1_2_s0_2, unidade_aritmetica_1_aboveorequal_naturais,
       unidade_aritmetica_1_cyout_bwout, unidade_aritmetica_1_overflow, unidade_aritmetica_1_r0,
       unidade_aritmetica_1_r1, unidade_aritmetica_1_r2, unidade_logica_1_cyout_bwout_logic,
       unidade_logica_1_overflow_logic, unidade_logica_1_r0, unidade_logica_1_r1, unidade_logica_1_r2,
       unidade_logica_1_s0_2, unidade_logica_1_s1_2;

  UNIDADE_ARITMETICA unidade_aritmetica_1 (
    .S0(unidade_logica_1_s0_2), .A0(A0), .A1(A1), .A2(A2), .B0(B0), .B1(B1), .B2(B2),
    .R0(unidade_aritmetica_1_r0), .R1(unidade_aritmetica_1_r1), .R2(unidade_aritmetica_1_r2),
    .GreaterOrEqual_Inteiros_com_sinal(GE), .CyOut_BwOut(unidade_aritmetica_1_cyout_bwout),
    .AboveOrEqual_Naturais(unidade_aritmetica_1_aboveorequal_naturais),
    .Overflow(unidade_aritmetica_1_overflow), .CyIn_BwIn_Inc(CyBwIn), .S1(unidade_logica_1_s1_2));
  UNIDADE_LOGICA unidade_logica_1 (
    .A0(A0), .A1(A1), .A2(A2), .B0(B0), .B1(B1), .B2(B2), .CyBwIn(CyBwIn), .R0(unidade_logica_1_r0),
    .R1(unidade_logica_1_r1), .R2(unidade_logica_1_r2),
    .CyOut_BwOut_Logic(unidade_logica_1_cyout_bwout_logic), .Overflow_Logic(unidade_logica_1_overflow_logic),
    .S1(S1), .S0(S0), .S1_2(unidade_logica_1_s1_2), .S0_2(unidade_logica_1_s0_2));
  MUX_2X3 mux_2x3_1 (
    .R0_ARITME(unidade_aritmetica_1_r0), .R0_LOGIC(unidade_logica_1_r0), .R1_A(unidade_aritmetica_1_r1),
    .R1_L(unidade_logica_1_r1), .R2_A(unidade_aritmetica_1_r2), .R2_L(unidade_logica_1_r2), .out_8(R0),
    .out_9(R1), .out_10(R2), .in_7(mux_2x1_1_s0_2));
  MUX_2X1 mux_2x1_1 (
    .A0(unidade_aritmetica_1_cyout_bwout), .B0(unidade_logica_1_cyout_bwout_logic), .R0(CyOut_BwOut),
    .S0_2(mux_2x1_1_s0_2), .S0(mux_2x1_2_s0_2));
  MUX_2X1 mux_2x1_2 (
    .A0(unidade_aritmetica_1_overflow), .B0(unidade_logica_1_overflow_logic), .R0(Overflow),
    .S0_2(mux_2x1_2_s0_2), .S0(S2));
  and and_1 (Zero, ~R2, ~R1, ~R0);  // AND_Gate
endmodule
