// Logisim project ALU.circ as structural Verilog: 14 circuits, main circuit main
module main (
  input  A0,
  input  A1,
  input  A2,
  input  A3,
  input  B0,
  input  B1,
  input  B2,
  input  B3,
  input  CyBwIn,
  input  S1,
  input  S0,
  input  S2,
  output Zero,
  output R0,
  output R1,
  output R2,
  output R3,
  output CyBwOut,
  output OV
);

  wire mux2x1_1_s0_2, mux2x1_2_s0_2, unidade_aritmetica_1_cybwout, unidade_aritmetica_1_overflow,
       unidade_aritmetica_1_s0_2, unidade_aritmetica_1_s1_2, unidade_aritmetica_1_s2,
       unidade_aritmetica_1_s3, unidade_logica_1_cyout, unidade_logica_1_ov, unidade_logica_1_r0,
       unidade_logica_1_r1, unidade_logica_1_r2, unidade_logica_1_r3, unidade_logica_1_s0_2,
       unidade_logica_1_s1_2;

  Unidade_Aritmetica unidade_aritmetica_1 (
    .A0(A0), .A1(A1), .A2(A2), .A3(A3), .B0(B0), .B1(B1), .B2(B2), .B3(B3), .S0_2(unidade_aritmetica_1_s0_2),
    .S1_2(unidade_aritmetica_1_s1_2), .S2(unidade_aritmetica_1_s2), .S3(unidade_aritmetica_1_s3),
    .CyBwout(unidade_aritmetica_1_cybwout), .Overflow(unidade_aritmetica_1_overflow), .CyBwIn(CyBwIn),
    .S1(unidade_logica_1_s1_2), .S0(unidade_logica_1_s0_2));  // open: S1_3, S0_3
  Unidade_Logica unidade_logica_1 (
    .A0(A0), .A1(A1), .A2(A2), .A3(A3), .B0(B0), .B1(B1), .B2(B2), .B3(B3), .CyIn(CyBwIn),
    .R0(unidade_logica_1_r0), .R1(unidade_logica_1_r1), .R2(unidade_logica_1_r2), .R3(unidade_logica_1_r3),
    .CyOut(unidade_logica_1_cyout), .OV(unidade_logica_1_ov), .S1(S1), .S0(S0), .S1_2(unidade_logica_1_s1_2),
    .S0_2(unidade_logica_1_s0_2));
  Mux2x4 mux2x4_1 (
    .A0(unidade_aritmetica_1_s0_2), .B0(unidade_logica_1_r0), .A1(unidade_aritmetica_1_s1_2),
    .B1(unidade_logica_1_r1), .A2(unidade_aritmetica_1_s2), .B2(unidade_logica_1_r2),
    .A3(unidade_aritmetica_1_s3), .B3(unidade_logica_1_r3), .S0(mux2x1_1_s0_2), .R0(R0), .R1(R1), .R2(R2),
    .R3(R3));  // open: S0_2
  Mux2x1 mux2x1_1 (
    .S0(mux2x1_2_s0_2), .A0(unidade_aritmetica_1_cybwout), .B0(unidade_logica_1_cyout), .S0_2(mux2x1_1_s0_2),
    .R0(CyBwOut));
  Mux2x1 mux2x1_2 (
    .S0(S2), .A0(unidade_aritmetica_1_overflow), .B0(unidade_logica_1_ov), .S0_2(mux2x1_2_s0_2), .R0(OV));
  and and_1 (Zero, ~R3, ~R2, ~R1, ~R0);  // AND_Gate
endmodule

module Half_Adder (
  input  a,
  input  b,
  output Soma,
  output Carry
);

  xor xor_1 (Soma, a, b);
  and and_1 (Carry, b, a);
endmodule

module Full_Adder (
  input  a,
  input  b,
  input  Carry_in,
  output Soma,
  output Carry_Out
);

  wire half_adder_1_carry, half_adder_1_soma, half_adder_2_carry;

  Half_Adder half_adder_1 (.a(a), .b(b), .Soma(half_adder_1_soma), .Carry(half_adder_1_carry));
  Half_Adder half_adder_2 (.a(half_adder_1_soma), .b(Carry_in), .Soma(Soma), .Carry(half_adder_2_carry));
  or or_1 (Carry_Out, half_adder_2_carry, half_adder_1_carry);
endmodule

module Somador (
  input  C0,
  input  A0,
  input  B0,
  input  A1,
  input  B1,
  input  A2,
  input  B2,
  input  A3,
  input  B3,
  output S0,
  output S1,
  output S2,
  output S3,
  output C4
);

  wire full_adder_1_carry_out, full_adder_2_carry_out, full_adder_3_carry_out;

  Full_Adder full_adder_1 (.a(A0), .b(B0), .Carry_in(C0), .Soma(S0), .Carry_Out(full_adder_1_carry_out));
  Full_Adder full_adder_2 (
    .a(A1), .b(B1), .Carry_in(full_adder_1_carry_out), .Soma(S1), .Carry_Out(full_adder_2_carry_out));
  Full_Adder full_adder_3 (
    .a(A2), .b(B2), .Carry_in(full_adder_2_carry_out), .Soma(S2), .Carry_Out(full_adder_3_carry_out));
  Full_Adder full_adder_4 (.a(A3), .b(B3), .Carry_in(full_adder_3_carry_out), .Soma(S3), .Carry_Out(C4));
endmodule

module Unidade_Aritmetica (
  input  CyBwIn,
  input  A0,
  input  A1,
  input  A2,
  input  A3,
  input  B0,
  input  B1,
  input  B2,
  input  B3,
  input  S1,
  input  S0,
  output S0_2,
  output S1_2,
  output S2,
  output S3,
  output CyBwout,
  output S1_3,
  output S0_3,
  output Overflow
);

  wire selecionador_de_funcao_1_c0, somador_1_c4, xor_1_out, xor_2_out, xor_3_out, xor_4_out;

  Selecionador_de_Funcao selecionador_de_funcao_1 (.CyBwIn(CyBwIn), .C0(selecionador_de_funcao_1_c0), .S1(S1), .S0(S0));
  xor xor_1 (xor_1_out, B0, S0);
  xor xor_2 (xor_2_out, B1, S0);
  xor xor_3 (xor_3_out, B2, S0);
  xor xor_4 (xor_4_out, B3, S0);
  Somador somador_1 (
    .A0(A0), .B0(xor_1_out), .A1(A1), .B1(xor_2_out), .A2(A2), .B2(xor_3_out), .A3(A3), .B3(xor_4_out),
    .S0(S0_2), .S1(S1_2), .S2(S2), .S3(S3), .C0(selecionador_de_funcao_1_c0), .C4(somador_1_c4));
  xor xor_5 (CyBwout, somador_1_c4, S0);
  OverFlow overflow_1 (.A3(A3), .B3(xor_4_out), .S3(S3), .Ov(Overflow));

  assign S0_3 = S0;
  assign S1_3 = S1;
endmodule

module OverFlow (
  input  A3,
  input  B3,
  input  S3,
  output Ov
);

  wire and_1_out, and_2_out;

  and and_1 (and_1_out, A3, B3, ~S3);  // AND_Gate
  and and_2 (and_2_out, ~A3, ~B3, S3);  // AND_Gate
  or or_1 (Ov, and_1_out, and_2_out);
endmodule

module Mux4x1 (
  input  S0,
  input  S1,
  input  I0,
  input  I1,
  input  I2,
  input  I3,
  output S0_2,
  output S1_2,
  output Out
);

  wire and_1_out, and_2_out, and_3_out, and_4_out;

  and and_1 (and_1_out, ~S0, I0, ~S1);  // AND_Gate
  and and_2 (and_2_out, S0, I1, ~S1);  // AND_Gate
  and and_3 (and_3_out, ~S0, I2, S1);  // AND_Gate
  and and_4 (and_4_out, S0, I3, S1);
  or or_1 (Out, and_1_out, and_2_out, and_3_out, and_4_out);

  assign S0_2 = S0;
  assign S1_2 = S1;
endmodule

module Selecionador_de_Funcao (
  input  CyBwIn,
  input  S1,
  input  S0,
  output C0
);

  wire not_1_out;

  not not_1 (not_1_out, CyBwIn);
  Mux4x1 mux4x1_1 (.S0(S0), .S1(S1), .I0(1'b0), .I1(1'b1), .I2(CyBwIn), .I3(not_1_out), .Out(C0));  // open: S0_2, S1_2
endmodule

module Mux2x4 (
  input  A0,
  input  B0,
  input  A1,
  input  B1,
  input  A2,
  input  B2,
  input  A3,
  input  B3,
  input  S0,
  output S0_2,
  output R0,
  output R1,
  output R2,
  output R3
);

  wire mux2x1_2_s0_2, mux2x1_3_s0_2, mux2x1_4_s0_2;

  Mux2x1 mux2x1_1 (.S0(mux2x1_2_s0_2), .A0(A0), .B0(B0), .S0_2(S0_2), .R0(R0));
  Mux2x1 mux2x1_2 (.S0(mux2x1_3_s0_2), .A0(A1), .B0(B1), .S0_2(mux2x1_2_s0_2), .R0(R1));
  Mux2x1 mux2x1_3 (.S0(mux2x1_4_s0_2), .A0(A2), .B0(B2), .S0_2(mux2x1_3_s0_2), .R0(R2));
  Mux2x1 mux2x1_4 (.S0(S0), .A0(A3), .B0(B3), .S0_2(mux2x1_4_s0_2), .R0(R3));
endmodule

module Mux2x1 (
  input  S0,
  input  A0,
  input  B0,
  output S0_2,
  output R0
);

  wire and_1_out, and_2_out;

  and and_1 (and_1_out, ~S0, A0);  // AND_Gate
  and and_2 (and_2_out, S0, B0);
  or or_1 (R0, and_1_out, and_2_out);

  assign S0_2 = S0;
endmodule

module Unidade_Logica (
  input  A0,
  input  A1,
  input  A2,
  input  A3,
  input  B0,
  input  B1,
  input  B2,
  input  B3,
  input  CyIn,
  input  S1,
  input  S0,
  output S1_2,
  output S0_2,
  output R0,
  output R1,
  output R2,
  output R3,
  output CyOut,
  output OV
);

  wire and_1_out, and_2_out, and_3_out, and_4_out, mux2x1_1_s0_2, mux2x1_2_s0_2, not_1_out, not_2_out,
       not_3_out, not_4_out, rcl_1_cyout, rcl_1_ov, rcl_1_r0, rcl_1_r1, rcl_1_r2, rcl_1_r3,
       shift_right_1_cyout, shift_right_1_ov, shift_right_1_r0, shift_right_1_r1, shift_right_1_r2,
       shift_right_1_r3;

  and and_1 (and_1_out, A0, B0);
  and and_2 (and_2_out, A1, B1);
  and and_3 (and_3_out, A2, B2);
  and and_4 (and_4_out, A3, B3);
  not not_1 (not_1_out, A0);
  not not_2 (not_2_out, A1);
  not not_3 (not_3_out, A2);
  not not_4 (not_4_out, A3);
  Shift_Right shift_right_1 (
    .A0(A0), .A1(A1), .A2(A2), .A3(A3), .CyIn(CyIn), .CyOut(shift_right_1_cyout), .R0(shift_right_1_r0),
    .R1(shift_right_1_r1), .R2(shift_right_1_r2), .R3(shift_right_1_r3), .OV(shift_right_1_ov), .B1(B1),
    .B0(B0));
  RCL rcl_1 (
    .CyIn(CyIn), .A0(A0), .A1(A1), .A2(A2), .A3(A3), .R0(rcl_1_r0), .R1(rcl_1_r1), .R2(rcl_1_r2),
    .R3(rcl_1_r3), .CyOut(rcl_1_cyout), .OV(rcl_1_ov));
  Mux4x4 mux4x4_1 (
    .A0(and_1_out), .B0(not_1_out), .C0(shift_right_1_r0), .D0(rcl_1_r0), .A1(and_2_out), .B1(not_2_out),
    .C1(shift_right_1_r1), .D1(rcl_1_r1), .A2(and_3_out), .B2(not_3_out), .C2(shift_right_1_r2),
    .D2(rcl_1_r2), .A3(and_4_out), .B3(not_4_out), .C3(shift_right_1_r3), .D3(rcl_1_r3), .S0(mux2x1_1_s0_2),
    .S1(S1), .R0(R0), .R1(R1), .R2(R2), .R3(R3), .S1_2(S1_2), .S0_2(S0_2));
  Mux2x1 mux2x1_1 (.S0(mux2x1_2_s0_2), .A0(shift_right_1_cyout), .B0(rcl_1_cyout), .S0_2(mux2x1_1_s0_2), .R0(CyOut));
  Mux2x1 mux2x1_2 (.S0(S0), .A0(shift_right_1_ov), .B0(rcl_1_ov), .S0_2(mux2x1_2_s0_2), .R0(OV));
endmodule

module Mux4x4 (
  input  A0,
  input  B0,
  input  C0,
  input  D0,
  input  A1,
  input  B1,
  input  C1,
  input  D1,
  input  A2,
  input  B2,
  input  C2,
  input  D2,
  input  A3,
  input  B3,
  input  C3,
  input  D3,
  input  S0,
  input  S1,
  output S1_2,
  output S0_2,
  output R0,
  output R1,
  output R2,
  output R3
);

  wire mux4x1_2_s0_2, mux4x1_2_s1_2, mux4x1_3_s0_2, mux4x1_3_s1_2, mux4x1_4_s0_2, mux4x1_4_s1_2;

  Mux4x1 mux4x1_1 (
    .S0(mux4x1_2_s0_2), .S1(mux4x1_2_s1_2), .I0(A0), .I1(B0), .I2(C0), .I3(D0), .Out(R0), .S0_2(S0_2),
    .S1_2(S1_2));
  Mux4x1 mux4x1_2 (
    .S0(mux4x1_3_s0_2), .S1(mux4x1_3_s1_2), .I0(A1), .I1(B1), .I2(C1), .I3(D1), .Out(R1),
    .S0_2(mux4x1_2_s0_2), .S1_2(mux4x1_2_s1_2));
  Mux4x1 mux4x1_3 (
    .S0(mux4x1_4_s0_2), .S1(mux4x1_4_s1_2), .I0(A2), .I1(B2), .I2(C2), .I3(D2), .Out(R2),
    .S0_2(mux4x1_3_s0_2), .S1_2(mux4x1_3_s1_2));
  Mux4x1 mux4x1_4 (
    .S0(S0), .S1(S1), .I0(A3), .I1(B3), .I2(C3), .I3(D3), .Out(R3), .S0_2(mux4x1_4_s0_2), .S1_2(mux4x1_4_s1_2));
endmodule

module Shift_Right (
  input  A0,
  input  A1,
  input  A2,
  input  A3,
  input  CyIn,
  input  B1,
  input  B0,
  output CyOut,
  output R0,
  output R1,
  output R2,
  output R3,
  output OV
);

  wire mux4x1_2_s0_2, mux4x1_2_s1_2, mux4x1_3_s0_2, mux4x1_3_s1_2, mux4x1_4_s0_2, mux4x1_4_s1_2,
       mux4x1_5_s0_2, mux4x1_5_s1_2;

  Mux4x1 mux4x1_1 (
    .S0(mux4x1_2_s0_2), .S1(mux4x1_2_s1_2), .I0(1'b0), .I1(A0), .I2(A1), .I3(A2), .Out(CyOut));  // open: S0_2, S1_2
  Mux4x1 mux4x1_2 (
    .S0(mux4x1_3_s0_2), .S1(mux4x1_3_s1_2), .I0(A0), .I1(A1), .I2(A2), .I3(A3), .Out(R0),
    .S0_2(mux4x1_2_s0_2), .S1_2(mux4x1_2_s1_2));
  Mux4x1 mux4x1_3 (
    .S0(mux4x1_4_s0_2), .S1(mux4x1_4_s1_2), .I0(A1), .I1(A2), .I2(A3), .I3(CyIn), .Out(R1),
    .S0_2(mux4x1_3_s0_2), .S1_2(mux4x1_3_s1_2));
  Mux4x1 mux4x1_4 (
    .S0(mux4x1_5_s0_2), .S1(mux4x1_5_s1_2), .I0(A2), .I1(A3), .I2(CyIn), .I3(CyIn), .Out(R2),
    .S0_2(mux4x1_4_s0_2), .S1_2(mux4x1_4_s1_2));
  Mux4x1 mux4x1_5 (
    .S0(B0), .S1(B1), .I0(A3), .I1(CyIn), .I2(CyIn), .I3(CyIn), .Out(R3), .S0_2(mux4x1_5_s0_2),
    .S1_2(mux4x1_5_s1_2));
  xor xor_1 (OV, R3, A3);
endmodule

module RCL (
  input  CyIn,
  input  A0,
  input  A1,
  input  A2,
  input  A3,
  output R0,
  output R1,
  output R2,
  output R3,
  output CyOut,
  output OV
);

  xor xor_1 (OV, A2, A3);

  assign CyOut = A3;
  assign R0 = CyIn;
  assign R1 = A0;
  assign R2 = A1;
  assign R3 = A2;
endmodule
