// Logisim project Cofre.circ as structural Verilog: 5 circuits, main circuit main
module MAIN (
  input  P,
  input  C1,
  input  C0,
  input  K,
  input  A0,
  input  A1,
  input  Inversor,
  output AL,
  output UL
);

  main main_1 (.P(P), .K(K), .A0(A0), .A1(A1), .C0(C0), .C1(C1), .I(Inversor), .Alarme(AL), .UL__Lock(UL));
endmodule

module main (
  input  P,
  input  K,
  input  A0,
  input  A1,
  input  C0,
  input  C1,
  input  I,
  output Alarme,
  output UL__Lock
);

  wire comparador_1_v_codico_v_f, inverter_1_c0_2, inverter_1_c1_2;

  Inverter inverter_1 (.C0(C0), .C1(C1), .Inverter(I), .C1_2(inverter_1_c1_2), .C0_2(inverter_1_c0_2));
  Comparador comparador_1 (
    .C0(inverter_1_c0_2), .A0(A0), .C1(inverter_1_c1_2), .A1(A1), .V_codico_v_f(comparador_1_v_codico_v_f));
  Controlo controlo_1 (.V(comparador_1_v_codico_v_f), .P(P), .AL(Alarme), .INV(I), .K(K), .L_lock(UL__Lock));

  // Notes on the sheet:
  //   V
endmodule

module Controlo (
  input  V,
  input  P,
  input  INV,
  input  K,
  output AL,
  output L_lock
);

  wire and_1_out, and_2_out;

  and and_1 (and_1_out, ~V, K);  // AND_Gate
  and and_2 (and_2_out, ~P, ~INV, K);  // AND_Gate
  or or_1 (AL, and_1_out, and_2_out);
  or or_2 (L_lock, AL, ~K);  // OR_Gate

  // Notes on the sheet:
  //   Porta 0 = fechada
  //   Chave
  //   Verificaçao
  //   1º faz se a verificao, dps inverso se se quiser de dps mete se a chave do ponto de vista da pessoa que sabe tudo para abrir o cofre
  //   Bloqueio do cofre, 1 = trancado
endmodule

module Comparador (
  input  C0,
  input  A0,
  input  C1,
  input  A1,
  output V_codico_v_f
);

  wire not_1_out, not_2_out, xor_1_out, xor_2_out;

  xor xor_1 (xor_1_out, C0, A0);
  xor xor_2 (xor_2_out, C1, A1);
  not not_1 (not_1_out, xor_1_out);
  not not_2 (not_2_out, xor_2_out);
  and and_1 (V_codico_v_f, not_1_out, not_2_out);
endmodule

// Inversor
module Inverter (
  input  C0,
  input  C1,
  input  Inverter,
  output C0_2,
  output C1_2
);

  xor xor_1 (C0_2, C0, Inverter);
  xor xor_2 (C1_2, C1, Inverter);
endmodule
