// Logisim project ALU 44873 46046.circ as structural Verilog: 16 circuits, main circuit ARITMETICO
module MAIN (
  input  CyIn,
  input  A0,
  input  A1,
  input  A2,
  input  A3,
  input  B0,
  input  B1,
  input  B2,
  input  B3,
  input  in_10,
  input  in_11,
  input  in_12,
  output S0,
  output S1,
  output S2,
  output S3,
  output overflow,
  output CyOut,
  output Zero
);

  Somatorio_mais_Logico somatorio_mais_logico_1 (
    .CyIn(CyIn), .A0(A0), .A1(A1), .A2(A2), .A3(A3), .B0(B0), .B1(B1), .B2(B2), .B3(B3), .overflow(overflow),
    .S0_2(S0), .S1_2(S1), .S2_2(S2), .S3(S3), .CyOut(CyOut), .S1(in_12), .S0(in_11), .S2(in_10), .Zero(Zero));
endmodule

module Somatorio_mais_Logico (
  input  CyIn,
  input  A0,
  input  A1,
  input  A2,
  input  A3,
  input  B0,
  input  B1,
  input  B2,
  input  B3,
  input  S2,
  input  S1,
  input  S0,
  output Zero,
  output overflow,
  output S0_2,
  output S1_2,
  output S2_2,
  output S3,
  output CyOut
);

  wire aritmetico_1_cybwout_overflow_dos_naturais, aritmetico_1_overflow, aritmetico_1_s0_2,
       aritmetico_1_s1_2, aritmetico_1_s2, aritmetico_1_s3, logico_1_cyoutlogic, logico_1_overflow,
       logico_1_r0, logico_1_r1, logico_1_r2, logico_1_r3, logico_1_s0_2, logico_1_s1_2, mux2x1_2_out_4;

  ARITMETICO aritmetico_1 (
    .CyBwIn(CyIn), .A0(A0), .A1(A1), .A2(A2), .A3(A3), .B0(B0), .B1(B1), .B2(B2), .B3(B3),
    .S0(logico_1_s0_2), .S0_2(aritmetico_1_s0_2), .S1_2(aritmetico_1_s1_2), .S2(aritmetico_1_s2),
    .S3(aritmetico_1_s3), .CyBwOut_overflow_dos_naturais(aritmetico_1_cybwout_overflow_dos_naturais),
    .Overflow(aritmetico_1_overflow), .S1(logico_1_s1_2));
  LOGICO logico_1 (
    .CyIn(CyIn), .A0(A0), .A1(A1), .A2(A2), .A3(A3), .B0(B0), .B1(B1), .B2(B2), .B3(B3),
    .CyOutLogic(logico_1_cyoutlogic), .Overflow(logico_1_overflow), .R0(logico_1_r0), .R1(logico_1_r1),
    .R2(logico_1_r2), .R3(logico_1_r3), .S0(S0), .S1(S1), .S1_2(logico_1_s1_2), .S0_2(logico_1_s0_2));
  MUX2X1 mux2x1_1 (
    .In0(aritmetico_1_overflow), .In1(logico_1_overflow), .Out(overflow), .S0(mux2x1_2_out_4));  // open: out_4
  MUX2X1 mux2x1_2 (
    .In0(aritmetico_1_cybwout_overflow_dos_naturais), .In1(logico_1_cyoutlogic), .Out(CyOut), .S0(S2),
    .out_4(mux2x1_2_out_4));
  Mux_grande_para_somatorio_e_logico mux_grande_para_somatorio_e_logico_1 (
    .AND0(aritmetico_1_s0_2), .SHIFT0(logico_1_r0), .A1(aritmetico_1_s1_2), .S1(logico_1_r1),
    .A2(aritmetico_1_s2), .S2(logico_1_r2), .A3(aritmetico_1_s3), .S3(logico_1_r3), .RLogic0(S0_2),
    .RL1(S1_2), .RL2(S2_2), .RL3(S3), .S1_2(S2));
  and and_1 (Zero, ~S3, ~S2_2, ~S1_2, ~S0_2);  // AND_Gate
endmodule

module Mux_grande_para_somatorio_e_logico (
  input  AND0,
  input  SHIFT0,
  input  A1,
  input  S1,
  input  A2,
  input  S2,
  input  A3,
  input  S3,
  input  S1_2,
  output RLogic0,
  output RL1,
  output RL2,
  output RL3
);

  wire mux2x1_2_out_4, mux2x1_3_out_4, mux2x1_4_out_4;

  MUX2X1 mux2x1_1 (.In0(AND0), .In1(SHIFT0), .Out(RLogic0), .S0(mux2x1_2_out_4));  // open: out_4
  MUX2X1 mux2x1_2 (.In0(A1), .In1(S1), .Out(RL1), .S0(mux2x1_3_out_4), .out_4(mux2x1_2_out_4));
  MUX2X1 mux2x1_3 (.In0(A2), .In1(S2), .Out(RL2), .S0(mux2x1_4_out_4), .out_4(mux2x1_3_out_4));
  MUX2X1 mux2x1_4 (.In0(A3), .In1(S3), .Out(RL3), .S0(S1_2), .out_4(mux2x1_4_out_4));
endmodule

module ARITMETICO (
  input  CyBwIn,
  input  A0,
  input  A1,
  input  A2,
  input  A3,
  input  B0,
  input  B1,
  input  B2,
  input  B3,
  input  S1,
  input  S0,
  output S0_2,
  output S1_2,
  output S2,
  output S3,
  output CyBwOut_overflow_dos_naturais,
  output Overflow
);

  wire b_trs_1_b0_trs, b_trs_1_b1_trs, b_trs_1_b2_trs, b_trs_1_b3_trs, cybw_trs_1_cy_bw_in, somador_1_cyout;

  CyBw__TRS cybw_trs_1 (.CyIn(CyBwIn), .S0(S0), .Cy_Bw_In(cybw_trs_1_cy_bw_in), .S1(S1));
  B__TRS b_trs_1 (
    .B0(B0), .B1(B1), .B2(B2), .B3(B3), .B0_TRS(b_trs_1_b0_trs), .B1_TRS(b_trs_1_b1_trs),
    .B2_TRS(b_trs_1_b2_trs), .B3_TRS(b_trs_1_b3_trs), .in_5(S0));
  Somador somador_1 (
    .Cyn(cybw_trs_1_cy_bw_in), .A0(A0), .B0(b_trs_1_b0_trs), .A0_2(A1), .in_5(b_trs_1_b1_trs), .in_6(A2),
    .in_7(b_trs_1_b2_trs), .S0(S0_2), .S1(S1_2), .S2(S2), .CyOut(somador_1_cyout), .in_8(A3),
    .in_9(b_trs_1_b3_trs), .S3(S3));
  Overflow overflow_1 (.A3(A3), .B3(B3), .S3(S3), .Overflow(Overflow));
  xor xor_1 (CyBwOut_overflow_dos_naturais, somador_1_cyout, S0);

  // Notes on the sheet:
  //   Naturais: 0 a 15
  //   Com sinal: -8 a +7
endmodule

module Soma (
  input  A,
  input  B,
  input  CyIn,
  output Soma,
  output CyOut
);

  wire and_1_out, and_2_out, and_3_out;

  xor xor_1 (Soma, A, B, CyIn);
  and and_1 (and_1_out, A, B);
  or or_1 (CyOut, and_1_out, and_2_out, and_3_out);
  and and_2 (and_2_out, A, CyIn);
  and and_3 (and_3_out, B, CyIn);
endmodule

// +
module Somador (
  input  Cyn,
  input  A0,
  input  B0,
  input  A0_2,
  input  in_5,
  input  in_6,
  input  in_7,
  input  in_8,
  input  in_9,
  output S0,
  output S1,
  output S2,
  output S3,
  output CyOut
);

  wire soma_1_cyout, soma_2_cyout, soma_3_cyout;

  Soma soma_1 (.A(A0), .B(B0), .CyIn(Cyn), .Soma(S0), .CyOut(soma_1_cyout));
  Soma soma_2 (.A(A0_2), .B(in_5), .CyIn(soma_1_cyout), .Soma(S1), .CyOut(soma_2_cyout));
  Soma soma_3 (.A(in_6), .B(in_7), .CyIn(soma_2_cyout), .Soma(S2), .CyOut(soma_3_cyout));
  Soma soma_4 (.A(in_8), .B(in_9), .CyIn(soma_3_cyout), .Soma(S3), .CyOut(CyOut));
endmodule

module B__TRS (
  input  B0,
  input  B1,
  input  B2,
  input  B3,
  input  in_5,
  output B0_TRS,
  output B1_TRS,
  output B2_TRS,
  output B3_TRS
);

  xor xor_1 (B0_TRS, B0, in_5);
  xor xor_2 (B1_TRS, B1, in_5);
  xor xor_3 (B2_TRS, B2, in_5);
  xor xor_4 (B3_TRS, B3, in_5);
endmodule

module MUX2X1 (
  input  In0,
  input  In1,
  input  S0,
  output out_4,
  output Out
);

  wire and_1_out, and_2_out;

  and and_1 (and_1_out, In0, ~S0);  // AND_Gate
  and and_2 (and_2_out, In1, S0);
  or or_1 (Out, and_1_out, and_2_out);

  assign out_4 = S0;
endmodule

module CyBw__TRS (
  input  CyIn,
  input  S0,
  input  S1,
  output Cy_Bw_In
);

  wire and_1_out;

  and and_1 (and_1_out, ~CyIn, S0);  // AND_Gate
  MUX2X1 mux2x1_1 (.In0(and_1_out), .In1(CyIn), .Out(Cy_Bw_In), .S0(S1));  // open: out_4
endmodule

module Overflow (
  input  A3,
  input  B3,
  input  S3,
  output Overflow
);

  wire and_1_out, and_2_out;

  and and_1 (and_1_out, A3, B3, ~S3);  // AND_Gate
  and and_2 (and_2_out, ~B3, ~A3, S3);  // AND_Gate
  or or_1 (Overflow, and_1_out, and_2_out);
endmodule

module LOGICO (
  input  CyIn,
  input  A0,
  input  A1,
  input  A2,
  input  A3,
  input  B0,
  input  B1,
  input  B2,
  input  B3,
  input  S1,
  input  S0,
  output CyOutLogic,
  output Overflow,
  output R0,
  output R1,
  output R2,
  output R3,
  output S1_2,
  output S0_2
);

  wire and_1_out, and_2_out, and_3_out, and_4_out, shift_1_r0, shift_1_r1, shift_1_r2, shift_1_r3;

  Shift shift_1 (
    .CyIn(CyIn), .A0(A0), .A1(A1), .A2(A2), .A3(A3), .CyOut(CyOutLogic), .R0(shift_1_r0), .R1(shift_1_r1),
    .R2(shift_1_r2), .R3(shift_1_r3), .B1(B1), .B0(B0), .S0(S0), .OverflowL(Overflow));
  and and_1 (and_1_out, A0, B0);
  and and_2 (and_2_out, A1, B1);
  and and_3 (and_3_out, A2, B2);
  and and_4 (and_4_out, A3, B3);
  Muxdologic2X4 muxdologic2x4_1 (
    .AND0(and_1_out), .SHIFT0(shift_1_r0), .A1(and_2_out), .S1(shift_1_r1), .A2(and_3_out), .S2(shift_1_r2),
    .A3(and_4_out), .S3(shift_1_r3), .RLogic0(R0), .RL1(R1), .RL2(R2), .RL3(R3), .S1_2(S1));

  assign S0_2 = S0;
  assign S1_2 = S1;

  // Notes on the sheet:
  //   Para melhorar o gerenciamento de ligaçao e organizar a unidade logica, o mux recebe a operaçao AND em baixo e na posiçao 0(do mux), e alias é como esta no enunciado
endmodule

module Muxdologic2X4 (
  input  AND0,
  input  SHIFT0,
  input  A1,
  input  S1,
  input  A2,
  input  S2,
  input  A3,
  input  S3,
  input  S1_2,
  output RLogic0,
  output RL1,
  output RL2,
  output RL3
);

  wire mux2x1_2_out_4, mux2x1_3_out_4, mux2x1_4_out_4;

  MUX2X1 mux2x1_1 (.In0(AND0), .In1(SHIFT0), .Out(RLogic0), .S0(mux2x1_2_out_4));  // open: out_4
  MUX2X1 mux2x1_2 (.In0(A1), .In1(S1), .Out(RL1), .S0(mux2x1_3_out_4), .out_4(mux2x1_2_out_4));
  MUX2X1 mux2x1_3 (.In0(A2), .In1(S2), .Out(RL2), .S0(mux2x1_4_out_4), .out_4(mux2x1_3_out_4));
  MUX2X1 mux2x1_4 (.In0(A3), .In1(S3), .Out(RL3), .S0(S1_2), .out_4(mux2x1_4_out_4));
endmodule

module Mux4x1 (
  input  A0,
  input  A1,
  input  A2,
  input  A3,
  input  S1,
  input  S0,
  output S1_2,
  output S0_2,
  output Out
);

  wire and_1_out, and_2_out, and_3_out, and_4_out;

  and and_1 (and_1_out, A0, ~S1, ~S0);  // AND_Gate
  and and_2 (and_2_out, A1, ~S1, S0);  // AND_Gate
  and and_3 (and_3_out, A2, S1, ~S0);  // AND_Gate
  and and_4 (and_4_out, A3, S1, S0);
  or or_1 (Out, and_1_out, and_2_out, and_3_out, and_4_out);

  assign S0_2 = S0;
  assign S1_2 = S1;
endmodule

// AShiftRight
module Arithmetic_Shift_Right (
  input  A3,
  input  A2,
  input  A1,
  input  A0,
  input  B1,
  input  B0,
  output R3,
  output R1,
  output R0,
  output CyOut,
  output R2
);

  wire and_1_out, and_2_out, and_3_out, mux4x1_1_s0_2, mux4x1_1_s1_2, mux4x1_2_s0_2, mux4x1_2_s1_2;

  and and_1 (and_1_out, ~B0, ~B1);  // AND_Gate
  and and_2 (and_2_out, and_1_out, A2);
  and and_3 (and_3_out, A3, ~and_1_out);  // AND_Gate
  or or_1 (R2, and_3_out, and_2_out);
  Mux4x1 mux4x1_1 (
    .A0(A1), .A1(A2), .A2(A3), .A3(A3), .Out(R1), .S1(B1), .S0(B0), .S1_2(mux4x1_1_s1_2), .S0_2(mux4x1_1_s0_2));
  Mux4x1 mux4x1_2 (
    .A0(A0), .A1(A1), .A2(A2), .A3(A3), .Out(R0), .S1(mux4x1_1_s1_2), .S0(mux4x1_1_s0_2),
    .S1_2(mux4x1_2_s1_2), .S0_2(mux4x1_2_s0_2));
  Mux4x1 mux4x1_3 (
    .A0(1'b0), .A1(A0), .A2(A1), .A3(A2), .Out(CyOut), .S1(mux4x1_2_s1_2), .S0(mux4x1_2_s0_2));  // open: S1_2, S0_2

  assign R3 = A3;

  // Notes on the sheet:
  //   0 0
  //   0 1
  //   1 0
  //   11
endmodule

// Shift Left
module Rotate_Carry_Left (
  input  A3,
  input  A2,
  input  A1,
  input  A0,
  input  CyBwIn,
  output R3,
  output R2,
  output R1,
  output R0,
  output CyOut,
  output OV
);

  xor xor_1 (OV, A3, A2);

  assign CyOut = A3;
  assign R0 = CyBwIn;
  assign R1 = A0;
  assign R2 = A1;
  assign R3 = A2;
endmodule

module Shift (
  input  CyIn,
  input  A0,
  input  A1,
  input  A2,
  input  A3,
  input  B1,
  input  B0,
  input  S0,
  output OverflowL,
  output CyOut,
  output R0,
  output R1,
  output R2,
  output R3
);

  wire arithmetic_shift_right_1_r0, arithmetic_shift_right_1_r1, arithmetic_shift_right_1_r2,
       arithmetic_shift_right_1_r3, C, mux2x1_2_out_4, rotate_carry_left_1_cyout, rotate_carry_left_1_ov,
       rotate_carry_left_1_r0, rotate_carry_left_1_r1, rotate_carry_left_1_r2, rotate_carry_left_1_r3;

  Rotate_Carry_Left rotate_carry_left_1 (
    .A3(A3), .A2(A2), .A1(A1), .A0(A0), .CyBwIn(CyIn), .R3(rotate_carry_left_1_r3),
    .R2(rotate_carry_left_1_r2), .R1(rotate_carry_left_1_r1), .R0(rotate_carry_left_1_r0),
    .CyOut(rotate_carry_left_1_cyout), .OV(rotate_carry_left_1_ov));
  Arithmetic_Shift_Right arithmetic_shift_right_1 (
    .A3(A3), .A2(A2), .A1(A1), .A0(A0), .B1(B1), .B0(B0), .R3(arithmetic_shift_right_1_r3),
    .R2(arithmetic_shift_right_1_r2), .R1(arithmetic_shift_right_1_r1), .R0(arithmetic_shift_right_1_r0),
    .CyOut(C));
  Muxdologic2X4 muxdologic2x4_1 (
    .AND0(arithmetic_shift_right_1_r0), .SHIFT0(rotate_carry_left_1_r0), .A1(arithmetic_shift_right_1_r1),
    .S1(rotate_carry_left_1_r1), .A2(arithmetic_shift_right_1_r2), .S2(rotate_carry_left_1_r2),
    .A3(arithmetic_shift_right_1_r3), .S3(rotate_carry_left_1_r3), .RLogic0(R0), .RL1(R1), .RL2(R2),
    .RL3(R3), .S1_2(S0));
  MUX2X1 mux2x1_1 (.In0(1'b0), .In1(rotate_carry_left_1_ov), .Out(OverflowL), .S0(mux2x1_2_out_4));  // open: out_4
  MUX2X1 mux2x1_2 (.In0(C), .In1(rotate_carry_left_1_cyout), .Out(CyOut), .S0(S0), .out_4(mux2x1_2_out_4));
endmodule
