// Logisim project CofreTrab3.circ as structural Verilog: 15 circuits, main circuit main
module MAIN (
  input  P,
  input  [2:0] CA,
  input  [2:0] CB,
  input  K,
  input  Inversor,
  output AL
);

  wire button_1_out, main_1_luz;

  Button button_1 (.out(button_1_out));
  LED led_1 (.in(main_1_luz));
  main main_1 (.P(P), .K(K), .CA(CA), .CB(CB), .I(Inversor), .Alarme(AL), .Luz(main_1_luz));  // open: MCLK, _1hz, B
  Clock clock_1 ();  // open: out

  // Notes on the sheet:
  //   I = 0, implica CA
endmodule

module main (
  input  P,
  input  K,
  input  I,
  input  B,
  input  [2:0] CA,
  input  [2:0] CB,
  input  _1hz,
  input  MCLK,
  output Alarme,
  output Luz
);

  wire validador_1_v;

  Validador validador_1 (.K(K), .I(I), ._1Hz(_1hz), .CA(CA), .CB(CB), .MCLK(MCLK), .V(validador_1_v), .L(Luz), .B(B));
  Controlo controlo_1 (.V(validador_1_v), .P(P), .AL(Alarme), .INV(I), .K(K));

  // Notes on the sheet:
  //   I = 0, implica CA
  //   V
endmodule

module Controlo (
  input  V,
  input  P,
  input  INV,
  input  K,
  output AL
);

  wire and_1_out, and_2_out;

  and and_1 (and_1_out, ~V, K);  // AND_Gate
  and and_2 (and_2_out, ~P, ~INV, K);  // AND_Gate
  or or_1 (AL, and_1_out, and_2_out);

  // Notes on the sheet:
  //   Porta 0 = fechada
  //   Chave
  //   Verificaçao
endmodule

module Comparador__out_Error (
  input  Z0,
  input  Y0,
  input  Z1,
  input  Y1,
  input  Z2,
  input  Y2,
  output Y__Z
);

  wire xor_1_out, xor_2_out, xor_3_out;

  xor xor_1 (xor_1_out, Z0, Y0);
  xor xor_2 (xor_2_out, Z1, Y1);
  xor xor_3 (xor_3_out, Z2, Y2);
  or or_1 (Y__Z, xor_1_out, xor_2_out, xor_3_out);
endmodule

module MUX8X1 (
  input  I0,
  input  I1,
  input  I2,
  input  I3,
  input  I4,
  input  I5,
  input  I6,
  input  I7,
  input  S1,
  input  S0,
  input  S2,
  output S1_2,
  output S0_2,
  output S2_2,
  output out_15
);

  wire mux4x1_1_out, mux4x1_2_out, mux4x1_2_s0_2, mux4x1_2_s1_2;

  MUX4X1 mux4x1_1 (
    .I0(I0), .I1(I1), .I2(I2), .I3(I3), .Out(mux4x1_1_out), .S1_2(S1_2), .S0_2(S0_2), .S1(mux4x1_2_s1_2),
    .S0(mux4x1_2_s0_2));
  MUX4X1 mux4x1_2 (
    .I0(I4), .I1(I5), .I2(I6), .I3(I7), .Out(mux4x1_2_out), .S1_2(mux4x1_2_s1_2), .S0_2(mux4x1_2_s0_2),
    .S1(S1), .S0(S0));
  Mux2x1 mux2x1_1 (.I0(mux4x1_1_out), .I1(mux4x1_2_out), .Out(out_15), .S0(S2), .out_4(S2_2));
endmodule

module MUX4X1 (
  input  I0,
  input  I1,
  input  I2,
  input  I3,
  input  S1,
  input  S0,
  output S1_2,
  output S0_2,
  output Out
);

  wire and_1_out, and_2_out, and_3_out, and_4_out;

  and and_1 (and_1_out, I0, ~S1, ~S0);  // AND_Gate
  and and_2 (and_2_out, I1, ~S1, S0);  // AND_Gate
  and and_3 (and_3_out, I2, S1, ~S0);  // AND_Gate
  and and_4 (and_4_out, I3, S1, S0);
  or or_1 (Out, and_1_out, and_2_out, and_3_out, and_4_out);

  assign S0_2 = S0;
  assign S1_2 = S1;
endmodule

module Mux2x1 (
  input  I0,
  input  I1,
  input  S0,
  output out_4,
  output Out
);

  wire and_1_out, and_2_out;

  and and_1 (and_1_out, I0, ~S0);  // AND_Gate
  and and_2 (and_2_out, I1, S0);
  or or_1 (Out, and_1_out, and_2_out);

  assign out_4 = S0;
endmodule

module Mux2x3 (
  input  CA0,
  input  CB0,
  input  CA1,
  input  CB1,
  input  CA2,
  input  CB2,
  input  S0,
  output Y0,
  output Y1,
  output Y2
);

  wire mux2x1_2_out_4, mux2x1_3_out_4;

  Mux2x1 mux2x1_1 (.I0(CA0), .I1(CB0), .Out(Y0), .S0(mux2x1_2_out_4));  // open: out_4
  Mux2x1 mux2x1_2 (.I0(CA1), .I1(CB1), .Out(Y1), .S0(mux2x1_3_out_4), .out_4(mux2x1_2_out_4));
  Mux2x1 mux2x1_3 (.I0(CA2), .I1(CB2), .Out(Y2), .S0(S0), .out_4(mux2x1_3_out_4));
endmodule

module FlipFlopT (
  input  CLK,
  input  D,
  input  AR,
  output Q
);

  T_Flip_Flop t_ff_1 (.clk(CLK), .T(D), .Q(Q), .preset(1'b0), .reset(AR), .en(1'b1));  // open: Qn
endmodule

module CountUp_Botao (
  input  CLOCK,
  input  RESET,
  output Q0,
  output Q1,
  output Q2
);

  wire and_1_out, and_2_out;

  FlipFlopT flipflopt_1 (.CLK(CLOCK), .D(1'b1), .AR(RESET), .Q(Q0));
  FlipFlopT flipflopt_2 (.CLK(CLOCK), .D(and_1_out), .Q(Q1));  // open: AR
  and and_1 (and_1_out, Q0, 1'b1);
  and and_2 (and_2_out, Q1, and_1_out);
  FlipFlopT flipflopt_3 (.CLK(CLOCK), .D(and_2_out), .AR(RESET), .Q(Q2));
endmodule

module CountUp2__Timer (
  input  CLOCK,
  input  RESET,
  output T5,
  output T10
);

  wire and_1_out, and_2_out, and_3_out, flipflopt_1_q, flipflopt_2_q, flipflopt_3_q, flipflopt_4_q;

  FlipFlopT flipflopt_1 (.CLK(CLOCK), .D(1'b1), .AR(RESET), .Q(flipflopt_1_q));
  FlipFlopT flipflopt_2 (.CLK(CLOCK), .D(and_1_out), .AR(RESET), .Q(flipflopt_2_q));
  and and_1 (and_1_out, flipflopt_1_q, 1'b1);
  and and_2 (and_2_out, flipflopt_2_q, and_1_out);
  FlipFlopT flipflopt_3 (.CLK(CLOCK), .D(and_2_out), .AR(RESET), .Q(flipflopt_3_q));
  and and_3 (and_3_out, flipflopt_3_q, and_2_out);
  FlipFlopT flipflopt_4 (.CLK(CLOCK), .D(and_3_out), .AR(RESET), .Q(flipflopt_4_q));
  and and_4 (T5, ~flipflopt_4_q, flipflopt_3_q, ~flipflopt_2_q, flipflopt_1_q);  // AND_Gate
  and and_5 (T10, flipflopt_4_q, ~flipflopt_3_q, flipflopt_2_q, ~flipflopt_1_q);  // AND_Gate

  // Notes on the sheet:
  //   Q0
  //   Q1
  //   Q2
  //   Q3
endmodule

module CounterOpcional (
  input  Clock,
  input  Clear,
  output [3:0] out_3
);

  wire [3:0] adder_1_out;

  Adder #(.width(4)) adder_1 (.a(out_3), .b(4'b0001), .out(adder_1_out));  // open: cin, cout
  Register #(.width(4)) register_1 (.D(adder_1_out), .Q(out_3), .clk(Clock), .clr(Clear));  // open: en
endmodule

module CTRL (
  input  Error,
  input  TOpen,
  input  TCode,
  input  CLK,
  input  Start,
  input  Reset,
  input  K,
  output InitTime,
  output Clear_Code,
  output SelCode,
  output V,
  output Luz
);

  wire and_1_out, and_2_out, and_3_out, and_4_out, and_5_out, and_6_out, d_ff_1_q, d_ff_2_q, d_ff_3_q,
       mux8x1_1_out_15, mux8x1_2_out_15, mux8x1_2_s0_2, mux8x1_2_s1_2, mux8x1_2_s2_2, mux8x1_3_out_15,
       mux8x1_3_s0_2, mux8x1_3_s1_2, mux8x1_3_s2_2, not_1_out, not_2_out, or_1_out, or_2_out;

  or or_1 (or_1_out, ~Error, ~TOpen);  // OR_Gate
  not not_1 (not_1_out, TOpen);
  and and_1 (and_1_out, TOpen, Error);
  or or_2 (or_2_out, Error, ~TCode);  // OR_Gate
  not not_2 (not_2_out, TOpen);
  MUX8X1 mux8x1_1 (
    .I0(1'b0), .I1(1'b0), .I2(1'b1), .I3(1'b0), .I4(or_1_out), .I5(1'b1), .I6(1'b1), .I7(K),
    .out_15(mux8x1_1_out_15), .S1(mux8x1_2_s1_2), .S0(mux8x1_2_s0_2), .S2(mux8x1_2_s2_2));  // open: S1_2, S0_2, S2_2
  MUX8X1 mux8x1_2 (
    .I0(1'b0), .I1(TCode), .I2(1'b0), .I3(not_1_out), .I4(and_1_out), .I5(1'b1), .I6(1'b1), .I7(K),
    .out_15(mux8x1_2_out_15), .S1(mux8x1_3_s1_2), .S0(mux8x1_3_s0_2), .S2(mux8x1_3_s2_2),
    .S1_2(mux8x1_2_s1_2), .S0_2(mux8x1_2_s0_2), .S2_2(mux8x1_2_s2_2));
  MUX8X1 mux8x1_3 (
    .I0(Start), .I1(or_2_out), .I2(1'b0), .I3(not_2_out), .I4(TOpen), .I5(1'b0), .I6(TOpen), .I7(K),
    .out_15(mux8x1_3_out_15), .S1(d_ff_2_q), .S0(d_ff_3_q), .S2(d_ff_1_q), .S1_2(mux8x1_3_s1_2),
    .S0_2(mux8x1_3_s0_2), .S2_2(mux8x1_3_s2_2));
  D_Flip_Flop d_ff_1 (.clk(CLK), .D(mux8x1_1_out_15), .Q(d_ff_1_q), .reset(Reset));  // open: Qn, preset, en
  D_Flip_Flop d_ff_2 (.clk(CLK), .D(mux8x1_2_out_15), .Q(d_ff_2_q), .reset(Reset));  // open: Qn, preset, en
  D_Flip_Flop d_ff_3 (.clk(CLK), .D(mux8x1_3_out_15), .Q(d_ff_3_q), .reset(Reset));  // open: Qn, preset, en
  and and_2 (and_2_out, ~d_ff_3_q, ~d_ff_2_q, ~d_ff_1_q);  // AND_Gate
  and and_3 (and_3_out, d_ff_3_q, ~d_ff_2_q, ~d_ff_1_q);  // AND_Gate
  and and_4 (and_4_out, ~d_ff_3_q, d_ff_2_q, ~d_ff_1_q);  // AND_Gate
  and and_5 (and_5_out, d_ff_3_q, ~d_ff_2_q, d_ff_1_q);  // AND_Gate
  and and_6 (and_6_out, d_ff_3_q, d_ff_2_q);
  and and_7 (SelCode, ~d_ff_3_q, ~d_ff_2_q, d_ff_1_q);  // AND_Gate
  and and_8 (V, d_ff_2_q, d_ff_1_q);
  or or_3 (InitTime, and_2_out, and_5_out);
  or or_4 (Clear_Code, and_4_out, and_6_out);
  or or_5 (Luz, V, and_3_out);

  // Other names for the same wires on the sheet: C = TCode; E = Error; O = TOpen

  // Notes on the sheet:
  //   S2
  //   S1
  //   S0
endmodule

module CTRLFase1 (
  input  K,
  input  TCode,
  input  TOpen,
  input  Error,
  input  Start,
  input  MCLK,
  input  Reset,
  output InitTime,
  output SelCode,
  output V,
  output ClrCode
);

  wire ctrl_1_luz;

  CTRL ctrl_1 (
    .CLK(MCLK), .Start(Start), .TCode(TCode), .Error(Error), .TOpen(TOpen), .K(K), .Clear_Code(ClrCode),
    .InitTime(InitTime), .Luz(ctrl_1_luz), .V(V), .SelCode(SelCode), .Reset(Reset));
  LED led_1 (.in(ctrl_1_luz));
endmodule

module Validador (
  input  K,
  input  I,
  input  _1Hz,
  input  [2:0] CA,
  input  [2:0] CB,
  input  B,
  input  MCLK,
  output L,
  output V
);

  wire comparador_out_error_1_y__z, countup2_timer_1_t5, countup2_timer_1_t10, countup_botao_1_q0,
       countup_botao_1_q1, countup_botao_1_q2, ctrl_1_clear_code, ctrl_1_inittime, ctrl_1_selcode,
       mux2x3_1_y0, mux2x3_1_y1, mux2x3_1_y2, xor_1_out;

  xor xor_1 (xor_1_out, I, ctrl_1_selcode);
  Mux2x3 mux2x3_1 (
    .CA0(CA[0]), .CB0(CB[0]), .CA1(CA[1]), .CB1(CB[1]), .CA2(CA[2]), .CB2(CB[2]), .Y0(mux2x3_1_y0),
    .Y1(mux2x3_1_y1), .Y2(mux2x3_1_y2), .S0(xor_1_out));
  CountUp_Botao countup_botao_1 (
    .CLOCK(B), .RESET(ctrl_1_clear_code), .Q0(countup_botao_1_q0), .Q1(countup_botao_1_q1),
    .Q2(countup_botao_1_q2));
  Comparador__out_Error comparador_out_error_1 (
    .Z0(countup_botao_1_q0), .Y0(mux2x3_1_y0), .Z2(countup_botao_1_q2), .Y2(mux2x3_1_y2),
    .Y__Z(comparador_out_error_1_y__z), .Z1(countup_botao_1_q1), .Y1(mux2x3_1_y1));
  CountUp2__Timer countup2_timer_1 (
    .T5(countup2_timer_1_t5), .T10(countup2_timer_1_t10), .CLOCK(_1Hz), .RESET(ctrl_1_inittime));
  CTRL ctrl_1 (
    .CLK(MCLK), .Start(B), .TCode(countup2_timer_1_t5), .Error(comparador_out_error_1_y__z),
    .TOpen(countup2_timer_1_t10), .K(K), .Clear_Code(ctrl_1_clear_code), .InitTime(ctrl_1_inittime), .Luz(L),
    .V(V), .SelCode(ctrl_1_selcode));  // open: Reset
  Clock clock_1 ();  // open: out

  // Notes on the sheet:
  //   Comp
endmodule
