// Logisim project TP3-Fase1.circ as structural Verilog: 7 circuits, main circuit ASM-MAIN
module ASM_MAIN (
  input  B,
  input  E7,
  input  L,
  input  TO,
  input  MCLK,
  output ARR,
  output CE,
  output ALERTA,
  output CLEAR
);

  wire ges_1_es0, ges_1_es1, ges_1_es2, mem_1_x0, mem_1_x1, mem_1_x2;

  GES ges_1 (
    .B(B), .E7(E7), .TO(TO), .L(L), .ES0(ges_1_es0), .X1(mem_1_x1), .X0(mem_1_x0), .ES1(ges_1_es1),
    .ES2(ges_1_es2), .X2(mem_1_x2));
  MEM mem_1 (
    .CLK(MCLK), .ES0(ges_1_es0), .ES1(ges_1_es1), .X0(mem_1_x0), .X1(mem_1_x1), .X2(mem_1_x2), .ES2(ges_1_es2));
  GVS gvs_1 (.X0(mem_1_x0), .X1(mem_1_x1), .CL(CLEAR), .AL(ALERTA), .X2(mem_1_x2), .CE(CE), .ARR(ARR));
endmodule

module TIMER (
  input  CLK,
  input  TEMP,
  output TOut
);

  wire and_1_out, and_2_out, and_3_out, not_1_out, t_ff_1_q, t_ff_2_q, t_ff_3_q, t_ff_4_q;

  not not_1 (not_1_out, TOut);
  T_Flip_Flop t_ff_1 (.clk(CLK), .T(not_1_out), .Q(t_ff_1_q), .reset(TEMP));  // open: Qn, preset, en
  and and_1 (and_1_out, t_ff_1_q, not_1_out);
  T_Flip_Flop t_ff_2 (.clk(CLK), .T(and_1_out), .Q(t_ff_2_q), .reset(TEMP));  // open: Qn, preset, en
  and and_2 (and_2_out, t_ff_2_q, and_1_out);
  T_Flip_Flop t_ff_3 (.clk(CLK), .T(and_2_out), .Q(t_ff_3_q), .reset(TEMP));  // open: Qn, preset, en
  and and_3 (and_3_out, t_ff_3_q, and_2_out);
  T_Flip_Flop t_ff_4 (.clk(CLK), .T(and_3_out), .Q(t_ff_4_q), .reset(TEMP));  // open: Qn, preset, en
  and and_4 (TOut, t_ff_1_q, t_ff_2_q, t_ff_3_q, t_ff_4_q);
endmodule

module MEM (
  input  CLK,
  input  ES0,
  input  ES1,
  input  ES2,
  output X0,
  output X1,
  output X2
);

  wire not_1_out;

  D_Flip_Flop d_ff_1 (.clk(CLK), .D(ES0), .Q(X0), .reset(not_1_out));  // open: Qn, preset, en
  D_Flip_Flop d_ff_2 (.clk(CLK), .D(ES1), .Q(X1), .reset(not_1_out));  // open: Qn, preset, en
  D_Flip_Flop d_ff_3 (.clk(CLK), .D(ES2), .Q(X2), .reset(not_1_out));  // open: Qn, preset, en
  not not_1 (not_1_out, 1'b1);
endmodule

module GVS (
  input  X0,
  input  X1,
  input  X2,
  output ARR,
  output AL,
  output CE,
  output CL
);

  and and_1 (ARR, ~X0, ~X1, ~X2);  // AND_Gate
  and and_2 (AL, ~X0, ~X1, X2);  // AND_Gate
  and and_3 (CE, X0, ~X1, ~X2);  // AND_Gate
  and and_4 (CL, X1, X0);
endmodule

module GES (
  input  X2,
  input  X1,
  input  X0,
  input  B,
  input  L,
  input  E7,
  input  TO,
  output ES0,
  output ES1,
  output ES2
);

  wire and_1_out, and_2_out, and_3_out, mux_8_1_1_s0_2, mux_8_1_1_s1_2, mux_8_1_1_s2_2, mux_8_1_2_s0_2,
       mux_8_1_2_s1_2, mux_8_1_2_s2_2;

  and and_1 (and_1_out, TO, L);
  and and_2 (and_2_out, ~E7, B);  // AND_Gate
  MUX_8_1 mux_8_1_1 (
    ._0(L), ._1(and_2_out), ._2(and_1_out), .S1(X1), .S0(X0), .S1_2(mux_8_1_1_s1_2), .S0_2(mux_8_1_1_s0_2),
    ._3(1'b0), .S2_2(mux_8_1_1_s2_2), .S2(X2), .out_15(ES0), ._4(1'b0), ._5(1'b0), ._6(1'b0), ._7(1'b0));
  and and_3 (and_3_out, ~E7, ~B);  // AND_Gate
  MUX_8_1 mux_8_1_2 (
    ._0(1'b0), ._1(and_3_out), ._2(L), .S1(mux_8_1_1_s1_2), .S0(mux_8_1_1_s0_2), .S1_2(mux_8_1_2_s1_2),
    .S0_2(mux_8_1_2_s0_2), ._3(1'b0), .S2_2(mux_8_1_2_s2_2), .S2(mux_8_1_1_s2_2), .out_15(ES1), ._4(1'b0),
    ._5(1'b0), ._6(1'b0), ._7(1'b0));
  MUX_8_1 mux_8_1_3 (
    ._0(1'b0), ._1(E7), ._2(1'b0), .S1(mux_8_1_2_s1_2), .S0(mux_8_1_2_s0_2), ._3(1'b0), .S2(mux_8_1_2_s2_2),
    .out_15(ES2), ._4(L), ._5(1'b0), ._6(1'b0), ._7(1'b0));  // open: S1_2, S0_2, S2_2
endmodule

module MUX_8_1 (
  input  _0,
  input  _1,
  input  _2,
  input  _3,
  input  _4,
  input  _5,
  input  _6,
  input  _7,
  input  S2,
  input  S1,
  input  S0,
  output S2_2,
  output S1_2,
  output S0_2,
  output out_15
);

  wire and_1_out, and_2_out, and_3_out, and_4_out, and_5_out, and_6_out, and_7_out, and_8_out;

  and and_1 (and_1_out, _0, ~S0, ~S1, ~S2);  // AND_Gate
  and and_2 (and_2_out, _1, S0, ~S1, ~S2);  // AND_Gate
  and and_3 (and_3_out, _2, ~S0, S1, ~S2);  // AND_Gate
  and and_4 (and_4_out, _3, S0, S1, ~S2);  // AND_Gate
  and and_5 (and_5_out, _4, ~S0, ~S1, S2);  // AND_Gate
  and and_6 (and_6_out, _5, S0, ~S1, S2);  // AND_Gate
  and and_7 (and_7_out, _6, ~S0, S1, S2);  // AND_Gate
  and and_8 (and_8_out, _7, S0, S1, S2);
  or or_1 (out_15, and_1_out, and_2_out, and_3_out, and_4_out, and_5_out, and_6_out, and_7_out, and_8_out);

  assign S0_2 = S0;
  assign S1_2 = S1;
  assign S2_2 = S2;
endmodule

module MUX_4_1 (
  input  in_1,
  input  in_2,
  input  in_3,
  input  in_4,
  input  S1,
  input  S0,
  output out_7,
  output out_8,
  output out_9
);

  wire and_1_out, and_2_out, and_3_out, and_4_out;

  and and_1 (and_1_out, in_1, ~S0, ~S1);  // AND_Gate
  and and_2 (and_2_out, in_2, S0, ~S1);  // AND_Gate
  and and_3 (and_3_out, in_3, ~S0, S1);  // AND_Gate
  and and_4 (and_4_out, in_4, S0, S1);
  or or_1 (out_9, and_1_out, and_2_out, and_3_out, and_4_out);

  assign out_7 = S1;
  assign out_8 = S0;
endmodule
