// Logisim project TP3-Fase2.circ as structural Verilog: 13 circuits, main circuit MAIN
module MAIN (
);

  wire _1Hz_out, button_1_out, t_ff_1_q, temporizador_1_alerta, temporizador_1_clear_light;

  Button button_1 (.out(button_1_out));
  Clock #(.highDuration(32), .lowDuration(32)) _1Hz (.out(_1Hz_out));
  T_Flip_Flop t_ff_1 (
    .clk(button_1_out), .T(1'b1), .Q(t_ff_1_q), .reset(temporizador_1_clear_light));  // open: Qn, preset, en
  TEMPORIZADOR temporizador_1 (
    .B(button_1_out), .L(t_ff_1_q), ._1Hz(_1Hz_out), .ALERTA(temporizador_1_alerta),
    .CLEAR_LIGHT(temporizador_1_clear_light));
  LED \LÂMPADA  (.in(t_ff_1_q));
  LED ALERTA (.in(temporizador_1_alerta));
endmodule

module TEMPORIZADOR (
  input  L,
  input  B,
  input  _1Hz,
  output ALERTA,
  output CLEAR_LIGHT
);

  wire asm_main_1_arr, asm_main_1_ce, d_ff_1_qn, MCLK_out, n3_1_e7, timer_count_down_1_to;
  wire [1:0] counter_1_q1__0;
  wire [3:0] r_n_5_5_1_r3__0;

  D_Flip_Flop d_ff_1 (.clk(_1Hz), .D(1'b1), .Qn(d_ff_1_qn), .reset(B));  // open: Q, preset, en
  COUNTER counter_1 (._1Hz(_1Hz), .AR(asm_main_1_arr), .Q1__0(counter_1_q1__0), .CE(asm_main_1_ce));
  r___n___5___5 r_n_5_5_1 (.Q(counter_1_q1__0), .R3__0(r_n_5_5_1_r3__0));
  TIMER_COUNT_DOWN timer_count_down_1 (
    .D3__0(r_n_5_5_1_r3__0), .PARALLEL_LOAD(d_ff_1_qn), ._1Hz(_1Hz), .TO(timer_count_down_1_to));
  // Probe on r_n_5_5_1_r3__0
  // Probe on counter_1_q1__0
  _3 u_3_1 (.Q1__0(counter_1_q1__0), .E7(n3_1_e7));
  Clock MCLK (.out(MCLK_out));
  ASM_MAIN asm_main_1 (
    .B(B), .E7(n3_1_e7), .L(L), .TO(timer_count_down_1_to), .MCLK(MCLK_out), .CE(asm_main_1_ce),
    .ALERTA(ALERTA), .CLEAR(CLEAR_LIGHT), .ARR(asm_main_1_arr));
endmodule

module U_D_COUNTER (
  input  CE,
  input  nU_D,
  input  [3:0] D3__0,
  input  PARALLEL_LOAD,
  input  _1Hz,
  output [3:0] Q3__0,
  output TO
);

  wire [3:0] adder_4_1_r, mux6_3_1_r;
  wire [3:3] and_1_out;

  and and_1 (and_1_out[3], CE, nU_D);
  ADDER_4 adder_4_1 (.A(Q3__0), .B({{3{and_1_out[3]}}, CE}), .R(adder_4_1_r));
  Mux6_3 mux6_3_1 (.PARALLEL_LOAD(PARALLEL_LOAD), ._0(adder_4_1_r), ._1(D3__0), .R(mux6_3_1_r));
  Register_4 register_4_1 (._1Hz(_1Hz), .Ant(mux6_3_1_r), .Post(Q3__0));  // open: AR
  and and_2 (TO, ~Q3__0[3], ~Q3__0[2], ~Q3__0[1], Q3__0[0]);  // AND_Gate
endmodule

module TIMER_COUNT_DOWN (
  input  [3:0] D3__0,
  input  PARALLEL_LOAD,
  input  _1Hz,
  output TO
);

  wire [3:0] adder_4_1_r, mux6_3_1_r, register_4_1_post;

  ADDER_4 adder_4_1 (.A(register_4_1_post), .B(4'b1111), .R(adder_4_1_r));
  Mux6_3 mux6_3_1 (.PARALLEL_LOAD(PARALLEL_LOAD), ._0(adder_4_1_r), ._1(D3__0), .R(mux6_3_1_r));
  Register_4 register_4_1 (._1Hz(_1Hz), .Ant(mux6_3_1_r), .Post(register_4_1_post));  // open: AR
  and and_1 (TO, register_4_1_post[0], ~register_4_1_post[1], ~register_4_1_post[2], ~register_4_1_post[3]);  // AND_Gate
endmodule

module COUNTER (
  input  CE,
  input  _1Hz,
  input  AR,
  output [1:0] Q1__0
);

  wire [1:0] adder_2_1_r;

  ADDER_2 adder_2_1 (.A(Q1__0), .B({1'b0, CE}), .R(adder_2_1_r));
  Register_2 register_2_1 (.AR(AR), ._1Hz(_1Hz), .Ant(adder_2_1_r), .Post(Q1__0));
endmodule

module FULL_ADDER (
  input  CYi,
  input  A,
  input  B,
  output R,
  output CYo
);

  wire and_1_out, and_2_out, and_3_out, xor_1_out;

  xor xor_1 (xor_1_out, A, B);
  and and_1 (and_1_out, CYi, A);
  and and_2 (and_2_out, CYi, B);
  and and_3 (and_3_out, A, B);
  xor xor_2 (R, CYi, xor_1_out);
  or or_1 (CYo, and_1_out, and_2_out, and_3_out);
endmodule

module ADDER_4 (
  input  [3:0] A,
  input  [3:0] B,
  output [3:0] R
);

  wire full_adder_1_cyo, full_adder_2_cyo, full_adder_3_cyo;

  FULL_ADDER full_adder_1 (.CYi(1'b0), .A(A[0]), .B(B[0]), .R(R[0]), .CYo(full_adder_1_cyo));
  FULL_ADDER full_adder_2 (.CYi(full_adder_1_cyo), .A(A[1]), .B(B[1]), .R(R[1]), .CYo(full_adder_2_cyo));
  FULL_ADDER full_adder_3 (.CYi(full_adder_2_cyo), .A(A[2]), .B(B[2]), .R(R[2]), .CYo(full_adder_3_cyo));
  FULL_ADDER full_adder_4 (.CYi(full_adder_3_cyo), .A(A[3]), .B(B[3]), .R(R[3]));  // open: CYo
endmodule

module ADDER_2 (
  input  [1:0] A,
  input  [1:0] B,
  output [1:0] R
);

  wire full_adder_1_cyo;

  FULL_ADDER full_adder_1 (.CYi(1'b0), .A(A[0]), .B(B[0]), .R(R[0]), .CYo(full_adder_1_cyo));
  FULL_ADDER full_adder_2 (.CYi(full_adder_1_cyo), .A(A[1]), .B(B[1]), .R(R[1]));  // open: CYo
endmodule

module Mux6_3 (
  input  PARALLEL_LOAD,
  input  [3:0] _0,
  input  [3:0] _1,
  output [3:0] R
);

  wire and_1_out, and_2_out, and_3_out, and_4_out, and_5_out, and_6_out, and_7_out, and_8_out;

  and and_1 (and_1_out, _0[0], ~PARALLEL_LOAD);  // AND_Gate
  and and_2 (and_2_out, _0[1], ~PARALLEL_LOAD);  // AND_Gate
  and and_3 (and_3_out, _0[2], ~PARALLEL_LOAD);  // AND_Gate
  and and_4 (and_4_out, _0[3], ~PARALLEL_LOAD);  // AND_Gate
  and and_5 (and_5_out, _1[0], PARALLEL_LOAD);
  and and_6 (and_6_out, _1[1], PARALLEL_LOAD);
  and and_7 (and_7_out, _1[2], PARALLEL_LOAD);
  and and_8 (and_8_out, _1[3], PARALLEL_LOAD);
  or or_1 (R[0], and_1_out, and_5_out);
  or or_2 (R[1], and_2_out, and_6_out);
  or or_3 (R[2], and_3_out, and_7_out);
  or or_4 (R[3], and_4_out, and_8_out);
endmodule

module Register_4 (
  input  _1Hz,
  input  [3:0] Ant,
  input  AR,
  output [3:0] Post
);

  D_Flip_Flop d_ff_1 (.clk(_1Hz), .D(Ant[0]), .Q(Post[0]), .reset(AR));  // open: Qn, preset, en
  D_Flip_Flop d_ff_2 (.clk(_1Hz), .D(Ant[1]), .Q(Post[1]), .reset(AR));  // open: Qn, preset, en
  D_Flip_Flop d_ff_3 (.clk(_1Hz), .D(Ant[2]), .Q(Post[2]), .reset(AR));  // open: Qn, preset, en
  D_Flip_Flop d_ff_4 (.clk(_1Hz), .D(Ant[3]), .Q(Post[3]), .reset(AR));  // open: Qn, preset, en
endmodule

module Register_2 (
  input  AR,
  input  _1Hz,
  input  [1:0] Ant,
  output [1:0] Post
);

  D_Flip_Flop d_ff_1 (.clk(_1Hz), .D(Ant[0]), .Q(Post[0]), .reset(AR));  // open: Qn, preset, en
  D_Flip_Flop d_ff_2 (.clk(_1Hz), .D(Ant[1]), .Q(Post[1]), .reset(AR));  // open: Qn, preset, en
endmodule

module r___n___5___5 (
  input  [1:0] Q,
  output [3:0] R3__0
);

  not not_1 (R3__0[2], Q[0]);
  or or_1 (R3__0[3], Q[0], Q[1]);

  assign R3__0[1:0] = R3__0[3:2];
endmodule

module _3 (
  input  [1:0] Q1__0,
  output E7
);

  and and_1 (E7, Q1__0[0], Q1__0[1]);
endmodule
