// Logisim project timer8.circ as structural Verilog: 5 circuits, main circuit Timer
module main (
  input  [7:0] in_1,
  input  in_2,
  input  in_3,
  input  in_4,
  output out_5,
  output out_6
);

  wire clock_1_out;

  Clock clock_1 (.out(clock_1_out));
  Timer timer_1 (.D0_7(in_1), .nCS(in_4), .nWE(in_3), .nOE(in_2), .nRTC(out_6), .TCLK(clock_1_out));  // open: TC
endmodule

module Timer (
  input  [7:0] D0_7,
  input  TCLK,
  input  nCS,
  input  nWE,
  input  nOE,
  output TC,
  output nRTC
);

  wire and_1_out, and_2_out, and_3_out, ffd_1_q, ffd_2_q, or_1_out, or_2_out;
  wire [7:0] cont_dn_1_out_5, cont_dn_1_out_6, reg_1_out_4, reg_1_out_5;

  and and_1 (and_1_out, ~nCS, ~nWE);  // AND_Gate
  and and_2 (and_2_out, ~nCS, ~nOE);  // AND_Gate
  ffd ffd_1 (.CLK(TCLK), .D(1'b1), .AR(and_1_out), .Q(ffd_1_q));
  or or_1 (or_1_out, ~ffd_1_q, and_3_out);  // OR_Gate
  cont_dn cont_dn_1 (
    .out_5(cont_dn_1_out_5), .CLK(TCLK), .AR(and_1_out), .D0_7(reg_1_out_4), .PL(or_1_out),
    .out_6(cont_dn_1_out_6));
  // Probe on reg_1_out_5
  \reg  reg_1 (.D0_7(D0_7), .E(nCS), .CLK(nWE), .out_4(reg_1_out_4), .out_5(reg_1_out_5));
  // Probe on cont_dn_1_out_6
  and and_3 (and_3_out, cont_dn_1_out_5[0], ~cont_dn_1_out_5[1], ~cont_dn_1_out_5[2], ~cont_dn_1_out_5[3], ~cont_dn_1_out_5[4], ~cont_dn_1_out_5[5], ~cont_dn_1_out_5[6], ~cont_dn_1_out_5[7]);  // AND_Gate
  and and_4 (TC, and_3_out, ~TCLK);  // AND_Gate
  or or_2 (or_2_out, and_1_out, and_2_out);
  ffd ffd_2 (.CLK(TC), .D(1'b1), .AR(or_2_out), .Q(ffd_2_q));
  not not_1 (nRTC, ffd_2_q);

  // Notes on the sheet:
  //   WR
  //   RD
  //   COUNT DOWN
  //   REGISTER
endmodule

module ffd (
  input  CLK,
  input  D,
  input  AR,
  output Q
);

  D_Flip_Flop d_ff_1 (.clk(CLK), .D(D), .Q(Q), .preset(1'b0), .en(1'b1), .reset(AR));  // open: Qn
endmodule

module \reg  (
  input  [7:0] D0_7,
  input  E,
  input  CLK,
  output [7:0] out_4,
  output [7:0] out_5
);

  wire not_1_out;

  Register register_1 (.D(D0_7), .en(not_1_out), .Q(out_4), .clk(CLK), .clr(1'b0));
  not not_1 (not_1_out, E);

  assign out_5 = out_4;
endmodule

module cont_dn (
  input  [7:0] D0_7,
  input  PL,
  input  CLK,
  input  AR,
  output [7:0] out_5,
  output [7:0] out_6
);

  wire [7:0] adder_1_out, multiplexer_1_out;

  Adder adder_1 (.a(out_5), .b({8{1'b1}}), .out(adder_1_out));  // open: cin, cout
  Multiplexer #(.width(8), .enable("false")) multiplexer_1 (
    .in0(adder_1_out), .in1(D0_7), .out(multiplexer_1_out), .sel(PL));
  Register register_1 (.D(multiplexer_1_out), .en(1'b1), .Q(out_5), .clk(CLK), .clr(AR));

  assign out_6 = out_5;
endmodule
